// Logisim project CPU.circ as structural Verilog: 1 circuit, main circuit Core
module Core (
);

  wire pipeline_core_1_p1, pipeline_core_1_p2, pipeline_core_1_p3, pipeline_core_1_p4, pipeline_core_1_p5,
       pipeline_core_1_p6;

  // Pipeline_Core pipeline_core_1: pin names not known; wires that end beside it: pipeline_core_1_p1, pipeline_core_1_p2, pipeline_core_1_p3, pipeline_core_1_p4, pipeline_core_1_p5, pipeline_core_1_p6
  // Local_APIC local_apic_1: pin names not known; wires that end beside it: pipeline_core_1_p4, pipeline_core_1_p5, pipeline_core_1_p6, pipeline_core_1_p2, pipeline_core_1_p3, pipeline_core_1_p1
endmodule
