// Logisim project LAPIC-V1.circ as structural Verilog
module Local_APIC_V1 (
  output [6:0] IRQ_Cant,
  output [31:0] IO_A,
  output [31:0] IO_B,
  output IO,
  output [5:0] Vector,
  output [31:0] LVT_A,
  output [31:0] LVT_B,
  output LVT,
  output [31:0] IPI_A,
  output [31:0] IPI_B,
  output IPI
);

  wire ISR_free_isr, TSR_to_irr, undriven, undriven_2;
  wire [31:0] IRR_irr_out_a, IRR_irr_out_b, TSR_to_irr_a, TSR_to_irr_b, TSR_to_isr_a, TSR_to_isr_b;

  Interrupt_Request_Register_V1 IRR (
    .From_IO_APIC_A(IO_A), .TPR_In_A(TSR_to_irr_a), .From_LVT_A(LVT_A), .IPI_A(IPI_A), .From_IO_APIC_B(IO_B),
    .TPR_In_B(TSR_to_irr_b), .From_LVT_B(LVT_B), .IPI_B(IPI_B), .IO_APIC(IO), .TPR(TSR_to_irr), .LVT(LVT),
    .IPI(IPI), .Clk(undriven_2), .RST(undriven), .IRR_Out_A(IRR_irr_out_a), .Interrupt_Cant(IRQ_Cant),
    .IRR_Out_B(IRR_irr_out_b));
  Task_Priority_Register_V1 TSR (
    .IRR_In_A(IRR_irr_out_a), .En(ISR_free_isr), .IRR_In_B(IRR_irr_out_b), .To_IRR(TSR_to_irr),
    .To_ISR_A(TSR_to_isr_a), .To_IRR_A(TSR_to_irr_a), .To_IRR_B(TSR_to_irr_b), .To_ISR_B(TSR_to_isr_b));
  In_Service_Register_V1 ISR (
    .Clean_ISR(undriven), .Clk(undriven_2), .ISR_Write(ISR_free_isr), .ISR_A_In(TSR_to_isr_a),
    .ISR_B_In(TSR_to_isr_b), .Free_ISR(ISR_free_isr), .Vector_Out(Vector));
endmodule

module In_Service_Register_V1 (
  input  Clean_ISR,
  input  Clk,
  input  ISR_Write,
  input  [31:0] ISR_A_In,
  input  [31:0] ISR_B_In,
  output Free_ISR,
  output [5:0] Vector_Out
);

  wire [31:0] Line_A_q, Line_B_q;

  Register #(.width(32)) Line_A (.D(ISR_A_In), .en(ISR_Write), .clk(Clk), .Q(Line_A_q), .clr(Clean_ISR));
  Register #(.width(32)) Line_B (.D(ISR_B_In), .en(ISR_Write), .clk(Clk), .Q(Line_B_q), .clr(Clean_ISR));
  Comparator #(.mode("unsigned"), .width(64)) comparator_1 (
    .a({64{1'b0}}), .b({Line_B_q, Line_A_q}), .eq(Free_ISR));  // open: gt, lt
  Priority_Encoder #(.select(6)) priority_encoder_1 (
    .in0(Line_A_q[0]), .in1(Line_A_q[1]), .in2(Line_A_q[2]), .in3(Line_A_q[3]), .in4(Line_A_q[4]),
    .in5(Line_A_q[5]), .in6(Line_A_q[6]), .in7(Line_A_q[7]), .in8(Line_A_q[8]), .in9(Line_A_q[9]),
    .in10(Line_A_q[10]), .in11(Line_A_q[11]), .in12(Line_A_q[12]), .in13(Line_A_q[13]), .in14(Line_A_q[14]),
    .in15(Line_A_q[15]), .in16(Line_A_q[16]), .in17(Line_A_q[17]), .in18(Line_A_q[18]), .in19(Line_A_q[19]),
    .in20(Line_A_q[20]), .in21(Line_A_q[21]), .in22(Line_A_q[22]), .in23(Line_A_q[23]), .in24(Line_A_q[24]),
    .in25(Line_A_q[25]), .in26(Line_A_q[26]), .in27(Line_A_q[27]), .in28(Line_A_q[28]), .in29(Line_A_q[29]),
    .in30(Line_A_q[30]), .in31(Line_A_q[31]), .in32(Line_B_q[0]), .in33(Line_B_q[1]), .in34(Line_B_q[2]),
    .in35(Line_B_q[3]), .in36(Line_B_q[4]), .in37(Line_B_q[5]), .in38(Line_B_q[6]), .in39(Line_B_q[7]),
    .in40(Line_B_q[8]), .in41(Line_B_q[9]), .in42(Line_B_q[10]), .in43(Line_B_q[11]), .in44(Line_B_q[12]),
    .in45(Line_B_q[13]), .in46(Line_B_q[14]), .in47(Line_B_q[15]), .in48(Line_B_q[16]), .in49(Line_B_q[17]),
    .in50(Line_B_q[18]), .in51(Line_B_q[19]), .in52(Line_B_q[20]), .in53(Line_B_q[21]), .in54(Line_B_q[22]),
    .in55(Line_B_q[23]), .in56(Line_B_q[24]), .in57(Line_B_q[25]), .in58(Line_B_q[26]), .in59(Line_B_q[27]),
    .in60(Line_B_q[28]), .in61(Line_B_q[29]), .in62(Line_B_q[30]), .in63(Line_B_q[31]), .out(Vector_Out));  // open: gs, en_out, en_in
endmodule

module Task_Priority_Register_V1 (
  input  [31:0] IRR_In_A,
  input  En,
  input  [31:0] IRR_In_B,
  output [31:0] To_ISR_A,
  output [31:0] To_IRR_A,
  output To_IRR,
  output [31:0] To_IRR_B,
  output [31:0] To_ISR_B
);

  wire and_1_out, priority_encoder_2_en_out, priority_encoder_2_gs;
  wire [4:0] priority_encoder_1_out, priority_encoder_2_out;
  wire [31:0] decoder_1_out0, decoder_2_out0;

  Priority_Encoder #(.select(5)) priority_encoder_1 (
    .in0(IRR_In_A[0]), .in1(IRR_In_A[1]), .in2(IRR_In_A[2]), .in3(IRR_In_A[3]), .in4(IRR_In_A[4]),
    .in5(IRR_In_A[5]), .in6(IRR_In_A[6]), .in7(IRR_In_A[7]), .in8(IRR_In_A[8]), .in9(IRR_In_A[9]),
    .in10(IRR_In_A[10]), .in11(IRR_In_A[11]), .in12(IRR_In_A[12]), .in13(IRR_In_A[13]), .in14(IRR_In_A[14]),
    .in15(IRR_In_A[15]), .in16(IRR_In_A[16]), .in17(IRR_In_A[17]), .in18(IRR_In_A[18]), .in19(IRR_In_A[19]),
    .in20(IRR_In_A[20]), .in21(IRR_In_A[21]), .in22(IRR_In_A[22]), .in23(IRR_In_A[23]), .in24(IRR_In_A[24]),
    .in25(IRR_In_A[25]), .in26(IRR_In_A[26]), .in27(IRR_In_A[27]), .in28(IRR_In_A[28]), .in29(IRR_In_A[29]),
    .in30(IRR_In_A[30]), .in31(IRR_In_A[31]), .out(priority_encoder_1_out));  // open: gs, en_out, en_in
  and and_1 (and_1_out, priority_encoder_2_en_out, En);
  Priority_Encoder #(.select(5)) priority_encoder_2 (
    .in0(IRR_In_B[0]), .in1(IRR_In_B[1]), .in2(IRR_In_B[2]), .in3(IRR_In_B[3]), .in4(IRR_In_B[4]),
    .in5(IRR_In_B[5]), .in6(IRR_In_B[6]), .in7(IRR_In_B[7]), .in8(IRR_In_B[8]), .in9(IRR_In_B[9]),
    .in10(IRR_In_B[10]), .in11(IRR_In_B[11]), .in12(IRR_In_B[12]), .in13(IRR_In_B[13]), .in14(IRR_In_B[14]),
    .in15(IRR_In_B[15]), .in16(IRR_In_B[16]), .in17(IRR_In_B[17]), .in18(IRR_In_B[18]), .in19(IRR_In_B[19]),
    .in20(IRR_In_B[20]), .in21(IRR_In_B[21]), .in22(IRR_In_B[22]), .in23(IRR_In_B[23]), .in24(IRR_In_B[24]),
    .in25(IRR_In_B[25]), .in26(IRR_In_B[26]), .in27(IRR_In_B[27]), .in28(IRR_In_B[28]), .in29(IRR_In_B[29]),
    .in30(IRR_In_B[30]), .in31(IRR_In_B[31]), .out(priority_encoder_2_out), .gs(priority_encoder_2_gs),
    .en_out(priority_encoder_2_en_out));  // open: en_in
  Decoder #(.select(5)) decoder_1 (
    .out0(decoder_1_out0[0]), .out1(decoder_1_out0[1]), .out2(decoder_1_out0[2]), .out3(decoder_1_out0[3]),
    .out4(decoder_1_out0[4]), .out5(decoder_1_out0[5]), .out6(decoder_1_out0[6]), .out7(decoder_1_out0[7]),
    .out8(decoder_1_out0[8]), .out9(decoder_1_out0[9]), .out10(decoder_1_out0[10]),
    .out11(decoder_1_out0[11]), .out12(decoder_1_out0[12]), .out13(decoder_1_out0[13]),
    .out14(decoder_1_out0[14]), .out15(decoder_1_out0[15]), .out16(decoder_1_out0[16]),
    .out17(decoder_1_out0[17]), .out18(decoder_1_out0[18]), .out19(decoder_1_out0[19]),
    .out20(decoder_1_out0[20]), .out21(decoder_1_out0[21]), .out22(decoder_1_out0[22]),
    .out23(decoder_1_out0[23]), .out24(decoder_1_out0[24]), .out25(decoder_1_out0[25]),
    .out26(decoder_1_out0[26]), .out27(decoder_1_out0[27]), .out28(decoder_1_out0[28]),
    .out29(decoder_1_out0[29]), .out30(decoder_1_out0[30]), .out31(decoder_1_out0[31]),
    .sel(priority_encoder_1_out), .en(and_1_out));
  Decoder #(.select(5)) decoder_2 (
    .out0(decoder_2_out0[0]), .out1(decoder_2_out0[1]), .out2(decoder_2_out0[2]), .out3(decoder_2_out0[3]),
    .out4(decoder_2_out0[4]), .out5(decoder_2_out0[5]), .out6(decoder_2_out0[6]), .out7(decoder_2_out0[7]),
    .out8(decoder_2_out0[8]), .out9(decoder_2_out0[9]), .out10(decoder_2_out0[10]),
    .out11(decoder_2_out0[11]), .out12(decoder_2_out0[12]), .out13(decoder_2_out0[13]),
    .out14(decoder_2_out0[14]), .out15(decoder_2_out0[15]), .out16(decoder_2_out0[16]),
    .out17(decoder_2_out0[17]), .out18(decoder_2_out0[18]), .out19(decoder_2_out0[19]),
    .out20(decoder_2_out0[20]), .out21(decoder_2_out0[21]), .out22(decoder_2_out0[22]),
    .out23(decoder_2_out0[23]), .out24(decoder_2_out0[24]), .out25(decoder_2_out0[25]),
    .out26(decoder_2_out0[26]), .out27(decoder_2_out0[27]), .out28(decoder_2_out0[28]),
    .out29(decoder_2_out0[29]), .out30(decoder_2_out0[30]), .out31(decoder_2_out0[31]),
    .sel(priority_encoder_2_out), .en(En));
  assign To_ISR_A = {32{1'b0}} & decoder_1_out0;  // AND_Gate and_2, 32 bits wide
  assign To_ISR_B = decoder_2_out0 & {32{1'b0}};  // AND_Gate and_3, 32 bits wide
  assign To_IRR_A = To_ISR_A ^ IRR_In_A;  // XOR_Gate xor_1, 32 bits wide
  assign To_IRR_B = IRR_In_B ^ To_ISR_B;  // XOR_Gate xor_2, 32 bits wide

  assign To_IRR = En;
endmodule

module Interrupt_Request_Register_V1 (
  input  Clk,
  input  RST,
  input  [31:0] From_IO_APIC_A,
  input  [31:0] TPR_In_A,
  input  [31:0] From_LVT_A,
  input  [31:0] IPI_A,
  input  [31:0] From_IO_APIC_B,
  input  [31:0] TPR_In_B,
  input  [31:0] From_LVT_B,
  input  [31:0] IPI_B,
  input  IO_APIC,
  input  TPR,
  input  LVT,
  input  IPI,
  output [31:0] IRR_Out_A,
  output [6:0] Interrupt_Cant,
  output [31:0] IRR_Out_B
);

  wire or_1_out;
  wire [1:0] Controller_out;
  wire [31:0] multiplexer_1_out, multiplexer_2_out, or_2_out, or_3_out;

  or or_1 (or_1_out, IPI, LVT, TPR, IO_APIC);
  PLA #(.in_width(4), .\table ("0001 00 # I/O\nxx1x 01 # TPR\n01xx 10 # LVT\n1x0x 11 # IPI")) Controller (
    .in({IPI, LVT, TPR, IO_APIC}), .out(Controller_out));
  Multiplexer #(.enable("true"), .select(2), .width(32)) multiplexer_1 (
    .in0(From_IO_APIC_A), .in1(TPR_In_A), .in2(From_LVT_A), .in3(IPI_A), .out(multiplexer_1_out),
    .sel(Controller_out), .en(or_1_out));
  Multiplexer #(.enable("true"), .select(2), .width(32)) multiplexer_2 (
    .in0(From_IO_APIC_B), .in1(TPR_In_B), .in2(From_LVT_B), .in3(IPI_B), .out(multiplexer_2_out),
    .sel(Controller_out), .en(or_1_out));
  Register #(.width(32)) IRR_A (.D(or_2_out), .clk(Clk), .Q(IRR_Out_A), .clr(RST));  // open: en
  assign or_2_out = IRR_Out_A | multiplexer_1_out;  // OR_Gate or_2, 32 bits wide
  Register #(.width(32)) IRR_B (.D(or_3_out), .clk(Clk), .Q(IRR_Out_B), .clr(RST));  // open: en
  assign or_3_out = multiplexer_2_out | IRR_Out_B;  // OR_Gate or_3, 32 bits wide
  // PopCount64 Bit_Counter: pin names not known; wires that end beside it: IRR_Out_A, IRR_Out_B, Interrupt_Cant
endmodule

// VHDL entity PopCount64, as the project stores it:
library IEEE;
use IEEE.STD_LOGIC_1164.ALL;
use IEEE.NUMERIC_STD.ALL;

entity PopCount64 is
    Port (
        A      : in  STD_LOGIC_VECTOR(31 downto 0);
        B      : in  STD_LOGIC_VECTOR(31 downto 0);
        RESULT : out STD_LOGIC_VECTOR(6 downto 0)
    );
end PopCount64;

architecture Behavioral of PopCount64 is
begin

    process(A, B)
    	variable count : integer range 0 to 64;
    begin

    if A = X"00000000" and B = X"00000000" then
        RESULT <= "0000000";
    else
        count := 0;

        for i in 0 to 31 loop
            if A(i) = '1' then
                count := count + 1;
            end if;
        end loop;

        for i in 0 to 31 loop
            if B(i) = '1' then
                count := count + 1;
            end if;
        end loop;

        RESULT <= std_logic_vector(to_unsigned(count, 7));
    end if;

end process;

end Behavioral;
