// Logisim project Memory_System.circ as structural Verilog
module MMIO_Controller (
  input  [31:0] Addr
);

  Comparator #(.mode("unsigned"), .width(6)) comparator_1 (.a(Addr[31:26]), .b(6'b111000));  // open: gt, eq, lt

  // Notes on the sheet:
  //   ECAM=E00 a E3F
endmodule

module Address_Decoder (
  input  [31:0] Addr_In,
  input  LVC_SEL
);

  wire and_1_out, comparator_1_gt;

  and and_1 (and_1_out, comparator_1_gt, LVC_SEL);
  Comparator #(.mode("unsigned"), .width(12)) comparator_1 (.gt(comparator_1_gt));  // open: a, b, eq, lt
endmodule

module ECAM_Registers_Type_Zero (
  input  RoW,
  input  Is_ECAM,
  input  [31:0] Addr,
  input  RST,
  input  Clk,
  input  [31:0] Data_In,
  input  Status_REQ,
  input  [15:0] Status_In,
  input  [31:0] Memory_Needed,
  input  [31:0] Bus_Numbers_In,
  input  [31:0] Capabilities_Pointer_In,
  input  [31:0] Class_Code,
  output [31:0] ECAN_Out,
  output [31:0] BAR_Out,
  output [31:0] Limit_Out,
  output [31:0] Command_Out,
  output [63:0] MSI_Out1,
  output [63:0] MSI_Out2
);

  wire and_1_out, and_2_out, comparator_1_eq, decoder_1_out0, decoder_1_out2, decoder_1_out4, decoder_1_out5,
       decoder_1_out6, decoder_1_out7, or_1_out, Primary_ECAM;
  wire [1:0] Addr_t;
  wire [11:0] bit_extender_1_out;
  wire [31:0] Capabilities_Pointer_q, common_ecam_registers_1_reg_out, Expansion_ROM_Base_q,
       multiplexer_1_out, multiplexer_2_out;

  Bit_Extender #(.in_width(32), .out_width(12), .\type ("zero")) bit_extender_1 (
    .in(Addr), .out({bit_extender_1_out[11:4], Addr_t, bit_extender_1_out[1:0]}));
  Comparator comparator_1 (.a(bit_extender_1_out[11:4]), .b({8{1'b0}}), .eq(comparator_1_eq));  // open: gt, lt
  and and_1 (and_1_out, ~comparator_1_eq, Is_ECAM);  // AND_Gate
  Decoder #(.select(3)) decoder_1 (
    .out0(decoder_1_out0), .out2(decoder_1_out2), .out4(decoder_1_out4), .out5(decoder_1_out5),
    .out6(decoder_1_out6), .out7(decoder_1_out7), .sel({bit_extender_1_out[4], Addr_t}), .en(and_1_out));  // open: out1, out3
  Multiplexer #(.width(32)) multiplexer_1 (.in0(Data_In), .in1(Memory_Needed), .out(multiplexer_1_out), .sel(RST));
  or or_1 (or_1_out, decoder_1_out2, RST);
  and and_2 (and_2_out, ~RoW, Is_ECAM);  // AND_Gate
  and and_3 (Primary_ECAM, Is_ECAM, comparator_1_eq);
  Register #(.width(32)) BAR (.D(Data_In), .en(decoder_1_out0), .clk(Clk), .Q(BAR_Out), .clr(RST));
  Register #(.width(32)) Expansion_ROM_Base (.D(Bus_Numbers_In), .clk(Clk), .Q(Expansion_ROM_Base_q));  // open: en, clr
  Register #(.width(32)) Memory_Limit (.D(multiplexer_1_out), .en(or_1_out), .clk(Clk), .Q(Limit_Out));  // open: clr
  Register #(.width(32)) Capabilities_Pointer (
    .D(Capabilities_Pointer_In), .clk(Clk), .Q(Capabilities_Pointer_q), .clr(RST));  // open: en
  Register #(.width(32)) MSI_1 (.D(Data_In), .en(decoder_1_out4), .clk(Clk), .Q(MSI_Out1[31:0]), .clr(RST));
  Register #(.width(32)) MSI_2 (.D(Data_In), .en(decoder_1_out5), .clk(Clk), .Q(MSI_Out1[63:32]), .clr(RST));
  Register #(.width(32)) MSI_3 (.D(Data_In), .en(decoder_1_out6), .clk(Clk), .Q(MSI_Out2[31:0]), .clr(RST));
  Register #(.width(32)) MSI_4 (.D(Data_In), .en(decoder_1_out7), .clk(Clk), .Q(MSI_Out2[63:32]), .clr(RST));
  Common_ECAM_Registers common_ecam_registers_1 (
    .ECAM_Register(Addr_t), .Status_Bus_REQ(Status_REQ), .Status_In(Status_In), .Clk(Clk),
    .Class_Code_In(Class_Code), .Header_Type_In({32{1'b0}}), .RST(RST), .Primary_ECAM(Primary_ECAM),
    .Data_In(Data_In), .Command_Ont(Command_Out), .Reg_Out(common_ecam_registers_1_reg_out));
  Multiplexer #(.enable("true"), .select(3), .width(32)) multiplexer_2 (
    .in0(BAR_Out), .in1(Expansion_ROM_Base_q), .in2(Limit_Out), .in3(Capabilities_Pointer_q),
    .in4(MSI_Out1[31:0]), .in5(MSI_Out1[63:32]), .in6(MSI_Out2[31:0]), .in7(MSI_Out2[63:32]),
    .out(multiplexer_2_out), .sel({bit_extender_1_out[4], Addr_t}), .en(and_2_out));
  Multiplexer #(.enable("true"), .width(32)) multiplexer_3 (
    .in0(multiplexer_2_out), .in1(common_ecam_registers_1_reg_out), .out(ECAN_Out), .sel(comparator_1_eq),
    .en(and_2_out));
endmodule

module ECAM_Registers_Type_One (
  input  RoW,
  input  Is_ECAM,
  input  [31:0] Addr,
  input  RST,
  input  Clk,
  input  [31:0] Data_In,
  input  Status_REQ,
  input  [15:0] Status_In,
  input  [31:0] Memory_Needed,
  input  [31:0] Bus_Numbers_In,
  input  [31:0] Capabilities_Pointer_In,
  input  [31:0] Class_Code,
  output [31:0] ECAN_Out,
  output [31:0] BAR_Out,
  output [31:0] Limit_Out,
  output [31:0] Command_Out
);

  wire and_1_out, and_2_out, comparator_1_eq, decoder_1_out0, decoder_1_out2, or_1_out, Primary_ECAM;
  wire [1:0] Addr_t;
  wire [11:0] bit_extender_1_out;
  wire [31:0] Bus_Numbers_q, Capabilities_Pointer_q, common_ecam_registers_1_reg_out, multiplexer_1_out,
       multiplexer_2_out;

  Bit_Extender #(.in_width(32), .out_width(12), .\type ("zero")) bit_extender_1 (
    .in(Addr), .out({bit_extender_1_out[11:4], Addr_t, bit_extender_1_out[1:0]}));
  Comparator comparator_1 (.a(bit_extender_1_out[11:4]), .b({8{1'b0}}), .eq(comparator_1_eq));  // open: gt, lt
  and and_1 (and_1_out, ~comparator_1_eq, Is_ECAM);  // AND_Gate
  Decoder #(.select(2)) decoder_1 (
    .out0(decoder_1_out0), .out2(decoder_1_out2), .sel(Addr_t), .en(and_1_out));  // open: out1, out3
  Multiplexer #(.width(32)) multiplexer_1 (.in0(Data_In), .in1(Memory_Needed), .out(multiplexer_1_out), .sel(RST));
  or or_1 (or_1_out, decoder_1_out2, RST);
  and and_2 (and_2_out, ~RoW, Is_ECAM);  // AND_Gate
  and and_3 (Primary_ECAM, Is_ECAM, comparator_1_eq);
  Register #(.width(32)) BAR (.D(Data_In), .en(decoder_1_out0), .clk(Clk), .Q(BAR_Out), .clr(RST));
  Register #(.width(32)) Bus_Numbers (.D(Bus_Numbers_In), .clk(Clk), .Q(Bus_Numbers_q));  // open: en, clr
  Register #(.width(32)) Memory_Limit (.D(multiplexer_1_out), .en(or_1_out), .clk(Clk), .Q(Limit_Out));  // open: clr
  Register #(.width(32)) Capabilities_Pointer (
    .D(Capabilities_Pointer_In), .clk(Clk), .Q(Capabilities_Pointer_q), .clr(RST));  // open: en
  Common_ECAM_Registers common_ecam_registers_1 (
    .ECAM_Register(Addr_t), .Status_Bus_REQ(Status_REQ), .Status_In(Status_In), .Clk(Clk),
    .Class_Code_In(Class_Code), .Header_Type_In({32{1'b1}}), .RST(RST), .Primary_ECAM(Primary_ECAM),
    .Data_In(Data_In), .Command_Ont(Command_Out), .Reg_Out(common_ecam_registers_1_reg_out));
  Multiplexer #(.enable("true"), .select(2), .width(32)) multiplexer_2 (
    .in0(BAR_Out), .in1(Bus_Numbers_q), .in2(Limit_Out), .in3(Capabilities_Pointer_q),
    .out(multiplexer_2_out), .sel(Addr_t), .en(and_2_out));
  Multiplexer #(.enable("true"), .width(32)) multiplexer_3 (
    .in0(multiplexer_2_out), .in1(common_ecam_registers_1_reg_out), .out(ECAN_Out), .sel(comparator_1_eq),
    .en(and_2_out));
endmodule

module Common_ECAM_Registers (
  input  Clk,
  input  RST,
  input  Primary_ECAM,
  input  [1:0] ECAM_Register,
  input  [31:0] Data_In,
  input  Status_Bus_REQ,
  input  [15:0] Status_In,
  input  [31:0] Class_Code_In,
  input  [31:0] Header_Type_In,
  output [31:0] Command_Ont,
  output [31:0] Reg_Out
);

  wire decoder_1_out0, decoder_1_out1;
  wire [15:0] bit_extender_1_out, Command_q, multiplexer_1_out, Status_q;
  wire [31:0] bit_extender_3_out, Class_Code_q, Header_Type_q;

  Bit_Extender #(.in_width(32), .\type ("zero")) bit_extender_1 (.in(Data_In), .out(bit_extender_1_out));
  Decoder #(.select(2)) decoder_1 (
    .out0(decoder_1_out0), .out1(decoder_1_out1), .sel(ECAM_Register), .en(Primary_ECAM));  // open: out2, out3
  Multiplexer #(.width(16)) multiplexer_1 (
    .in0(bit_extender_1_out), .in1(Status_In), .out(multiplexer_1_out), .sel(Status_Bus_REQ));
  Register #(.width(16)) Command (.D(bit_extender_1_out), .en(decoder_1_out0), .clk(Clk), .Q(Command_q), .clr(RST));
  Register #(.width(16)) Status (.D(multiplexer_1_out), .en(decoder_1_out1), .clk(Clk), .Q(Status_q), .clr(RST));
  Register #(.width(32)) Class_Code (.D(Class_Code_In), .clk(Clk), .Q(Class_Code_q));  // open: en, clr
  Register #(.width(32)) Header_Type (.D(Header_Type_In), .clk(Clk), .Q(Header_Type_q));  // open: en, clr
  assign Command_Ont = {{16{1'b0}}, Command_q};  // Bit_Extender bit_extender_2
  assign bit_extender_3_out = {{16{1'b0}}, Status_q};  // Bit_Extender bit_extender_3
  Multiplexer #(.enable("true"), .select(2), .width(32)) multiplexer_2 (
    .in0(Command_Ont), .in1(bit_extender_3_out), .in2(Class_Code_q), .in3(Header_Type_q), .out(Reg_Out),
    .sel(ECAM_Register), .en(Primary_ECAM));
endmodule
