// Logisim project CPU.circ as structural Verilog: 3 circuits, main circuit Die
module Die (
  input  [63:0] Data_In,
  input  RAM_Ready,
  input  [31:0] Addr_From_Perif_1,
  input  [63:0] Data_From_Perif_1,
  input  [1:0] Ctrl_Up_1,
  input  [31:0] Addr_From_Perif_2,
  input  [63:0] Data_From_Perif_2,
  input  [1:0] Ctrl_Up_2,
  input  [31:0] Addr_From_Perif_3,
  input  [63:0] Data_From_Perif_3,
  input  [1:0] Ctrl_Up_3,
  input  [63:0] ROM_Data_In,
  input  Clk,
  input  RST,
  output [7:0] Write_Flags,
  output [31:0] Addr,
  output [63:0] Data_Out,
  output RST_Out,
  output Clk_Out,
  output Read_En,
  output Write_En,
  output [63:0] Data_To_Perif_1,
  output [31:0] Addr_To_Perif_1,
  output [6:0] Ctrl_Down_1,
  output [63:0] Data_To_Perif_2,
  output [31:0] Addr_To_Perif_2,
  output [6:0] Ctrl_Down_2,
  output [63:0] Data_To_Perif_3,
  output [31:0] Addr_To_Perif_3,
  output [6:0] Ctrl_Down_3,
  output [19:0] ROM_Addr,
  output HLT
);

  wire core_1_en_read, core_1_en_write, core_1_mem_req, DMA_ACK, mapper_1_is_rom,
       memory_controller_1_cpu_ack, memory_controller_1_stall, root_complex_1_bus_req, root_complex_1_is_ram,
       root_complex_1_ram_read, root_complex_1_ram_write, router_1_en_read_root, router_1_en_write_root,
       router_1_read_cpu_out, router_1_write_cpu_out;
  wire [2:0] core_1_tipo;
  wire [31:0] core_1_addr, core_1_data_out, root_complex_1_addr_to_cpu, router_1_addr_to_lapic,
       router_1_addr_to_ram, router_1_addr_to_rom_mapper, router_1_addr_to_root;
  wire [63:0] mapper_1_data_out, memory_controller_1_data_out, root_complex_1_data_out, router_1_data_to_cpu,
       router_1_data_to_ram, router_1_data_to_root;

  Router router_1 (
    .Is_ROM(mapper_1_is_rom), .Is_RAM(root_complex_1_is_ram), .Read_CPU(core_1_en_read),
    .Write_CPU(core_1_en_write), .DMA_ACK(DMA_ACK), .Read_REQ(root_complex_1_ram_read),
    .Write_REQ(root_complex_1_ram_write), .Data_From_RAM(memory_controller_1_data_out),
    .Data_From_ROM(mapper_1_data_out), .Data_From_Root(root_complex_1_data_out), .Addr_From_CPU(core_1_addr),
    .Addr_From_Root(root_complex_1_addr_to_cpu), .Data_From_CPU(core_1_data_out),
    .Read_CPU_Out(router_1_read_cpu_out), .Write_CPU_Out(router_1_write_cpu_out),
    .Data_To_CPU(router_1_data_to_cpu), .Addr_To_LAPIC(router_1_addr_to_lapic),
    .Addr_To_Root(router_1_addr_to_root), .Addr_To_ROM_Mapper(router_1_addr_to_rom_mapper),
    .Addr_To_RAM(router_1_addr_to_ram), .Data_To_RAM(router_1_data_to_ram),
    .Data_To_Root(router_1_data_to_root), .En_Read_Root(router_1_en_read_root),
    .En_Write_Root(router_1_en_write_root));
  Memory_Controller memory_controller_1 (
    .Write_REQ(router_1_write_cpu_out), .Read_REQ(router_1_read_cpu_out),
    .Read_REQ_Root(root_complex_1_ram_read), .Write_REQ_Root(root_complex_1_ram_write),
    .Root_REQ(root_complex_1_bus_req), .Addr(router_1_addr_to_ram), .Data_In(router_1_data_to_ram),
    .RAM_Ready(RAM_Ready), .Tipo(core_1_tipo), .CPU_REQ(core_1_mem_req), .Data_From_RAM(Data_In),
    .DMA_ACK(DMA_ACK), .Data_Out(memory_controller_1_data_out), .CPU_ACK(memory_controller_1_cpu_ack),
    .Stall(memory_controller_1_stall), .Addr_To_RAM(Addr), .Data_To_RAM(Data_Out), .Write_En(Write_En),
    .Read_En(Read_En), .Write_Flags(Write_Flags));
  Core core_1 (
    .Data_In(router_1_data_to_cpu), .RAM_Ready(memory_controller_1_cpu_ack),
    .Stall(memory_controller_1_stall), .DMA_ACK(DMA_ACK), .Clk(Clk), .RST(RST),
    .Addr_LAPIC(router_1_addr_to_lapic), .HLT(HLT), .Addr(core_1_addr), .Tipo(core_1_tipo),
    .En_Read(core_1_en_read), .En_Write(core_1_en_write), .MEM_REQ(core_1_mem_req), .Data_Out(core_1_data_out));
  Mapper mapper_1 (
    .Addr(router_1_addr_to_rom_mapper), .Data_in(ROM_Data_In), .Data_Out(mapper_1_data_out),
    .Is_ROM(mapper_1_is_rom), .ROM_Addr(ROM_Addr));
  Root_Complex root_complex_1 (
    .Data_In(router_1_data_to_root), .Read(router_1_en_read_root), .Write(router_1_en_write_root), .Clk(Clk),
    .RST(RST), .Addr(router_1_addr_to_root), .DMA_ACK(DMA_ACK), .Data_To_Up_1(Data_From_Perif_1),
    .Addr_To_Up_1(Addr_From_Perif_1), .Ctrl_Up_1(Ctrl_Up_1), .Data_To_Up_2(Data_From_Perif_2),
    .Addr_To_Up_2(Addr_From_Perif_2), .Ctrl_Up_2(Ctrl_Up_2), .Data_To_Up_3(Data_From_Perif_3),
    .Addr_To_Up_3(Addr_From_Perif_3), .Ctrl_Up_3(Ctrl_Up_3), .Is_RAM(root_complex_1_is_ram),
    .RAM_Write(root_complex_1_ram_write), .Addr_To_CPU(root_complex_1_addr_to_cpu),
    .RAM_Read(root_complex_1_ram_read), .Bus_REQ(root_complex_1_bus_req), .Data_Out(root_complex_1_data_out),
    .Addr_To_Down_1(Addr_To_Perif_1), .Data_To_Down_1(Data_To_Perif_1), .Ctrl_Down_1(Ctrl_Down_1),
    .Addr_To_Down_2(Addr_To_Perif_2), .Data_To_Down_2(Data_To_Perif_2), .Ctrl_Down_2(Ctrl_Down_2),
    .Addr_To_Down_3(Addr_To_Perif_3), .Data_To_Down_3(Data_To_Perif_3), .Ctrl_Down_3(Ctrl_Down_3));

  assign Clk_Out = Clk;
  assign RST_Out = RST;

  // Notes on the sheet:
  //   Addr_From_Perif_1: pull=down
  //   Data_From_Perif_1: pull=up
  //   Ctrl_Up_1: pull=down
  //   Addr_From_Perif_2: pull=down
  //   Data_From_Perif_2: pull=up
  //   Ctrl_Up_2: pull=down
  //   Addr_From_Perif_3: pull=down
  //   Data_From_Perif_3: pull=up
  //   Ctrl_Up_3: pull=down
endmodule

module Router (
  input  [63:0] Data_From_RAM,
  input  [63:0] Data_From_ROM,
  input  [63:0] Data_From_Root,
  input  [31:0] Addr_From_CPU,
  input  [31:0] Addr_From_Root,
  input  [31:0] Data_From_CPU,
  input  Is_ROM,
  input  Is_RAM,
  input  Read_CPU,
  input  Write_CPU,
  input  DMA_ACK,
  input  Read_REQ,
  input  Write_REQ,
  output [63:0] Data_To_CPU,
  output [31:0] Addr_To_LAPIC,
  output [31:0] Addr_To_Root,
  output [31:0] Addr_To_ROM_Mapper,
  output [31:0] Addr_To_RAM,
  output [63:0] Data_To_RAM,
  output [63:0] Data_To_Root,
  output En_Read_Root,
  output En_Write_Root,
  output Read_CPU_Out,
  output Write_CPU_Out
);

  wire Addr_Sel, Data_To_RAM_Sel, Data_To_Root_Sel, Enable;
  wire [1:0] Data_To_CPU_Sel;
  wire [63:0] bit_extender_1_out, bit_extender_2_out;

  PLA #(.in_width(7), .out_width(6), .\table ("1xxx0xx 101000 # ROM\n01100xx 100000 # RRAM\n01010xx 100000 # WRAM\n00100xx 110000 # RRoot\n00010xx 100000 # WRoot\nxxxx110 100101 # R->P\nxxxx101 110110 # P->R")) pla_1 (
    .in({Is_ROM, Is_RAM, Read_CPU, Write_CPU, DMA_ACK, Read_REQ, Write_REQ}),
    .out({Enable, Data_To_CPU_Sel, Addr_Sel, Data_To_RAM_Sel, Data_To_Root_Sel}));
  PLA #(.in_width(7), .\table ("00100xx 01 # RRoot\n00010xx 10 # WRoot")) pla_2 (
    .in({Is_ROM, Is_RAM, Read_CPU, Write_CPU, DMA_ACK, Read_REQ, Write_REQ}),
    .out({En_Write_Root, En_Read_Root}));
  and and_1 (Read_CPU_Out, Read_CPU, ~Is_ROM);  // AND_Gate
  and and_2 (Write_CPU_Out, Write_CPU, ~Is_ROM);  // AND_Gate
  Multiplexer #(.enable("true"), .select(2), .width(64)) multiplexer_1 (
    .in0(Data_From_RAM), .in1(Data_From_ROM), .in2(Data_From_Root), .out(Data_To_CPU), .sel(Data_To_CPU_Sel),
    .en(Enable));  // open: in3
  Multiplexer #(.enable("true"), .width(32)) multiplexer_2 (
    .in0(Addr_From_CPU), .in1(Addr_From_Root), .out(Addr_To_RAM), .sel(Addr_Sel), .en(Enable));
  assign bit_extender_1_out = {{32{1'b0}}, Data_From_CPU};  // Bit_Extender bit_extender_1
  Multiplexer #(.enable("true"), .width(64)) multiplexer_3 (
    .in0(bit_extender_1_out), .in1(Data_From_Root), .out(Data_To_RAM), .sel(Data_To_RAM_Sel), .en(Enable));
  assign bit_extender_2_out = {{32{1'b0}}, Data_From_CPU};  // Bit_Extender bit_extender_2
  Multiplexer #(.enable("true"), .width(64)) multiplexer_4 (
    .in0(bit_extender_2_out), .in1(Data_From_RAM), .out(Data_To_Root), .sel(Data_To_Root_Sel), .en(Enable));

  assign Addr_To_LAPIC = Addr_From_Root;
  assign Addr_To_ROM_Mapper = Addr_From_CPU;
  assign Addr_To_Root = Addr_From_CPU;
endmodule

module miniRouter (
  input  [63:0] in_1,
  input  [31:0] in_2,
  input  [31:0] Addr_From_Perif_1,
  input  [63:0] Data_From_Perif_1,
  input  [6:0] in_5,
  input  [1:0] Ctrl_Up_1,
  output [63:0] Data_To_Perif_1,
  output [31:0] Addr_To_Perif_1,
  output [31:0] out_9,
  output [63:0] out_10,
  output [6:0] Ctrl_Down_1,
  output [1:0] out_12
);


  assign Addr_To_Perif_1 = in_2;
  assign Ctrl_Down_1 = in_5;
  assign Data_To_Perif_1 = in_1;
  assign out_9 = Addr_From_Perif_1;
  assign out_10 = Data_From_Perif_1;
  assign out_12 = Ctrl_Up_1;

  // Notes on the sheet:
  //   out_9: pull=down
  //   out_10: pull=up
  //   out_12: pull=down
  //   Addr_From_Perif_1: pull=down
  //   Data_From_Perif_1: pull=up
  //   Ctrl_Up_1: pull=down
endmodule
