// Logisim project Control_FLush.circ as structural Verilog: 8 circuits, main circuit PC
module PC (
  input  [31:0] Addr,
  input  En_PC,
  input  Stall,
  input  Clk,
  input  RST,
  input  Flush,
  input  HLT,
  output [31:0] Sum,
  output [31:0] PC_Out
);

  wire and_1_out, and_2_out, or_1_out;
  wire [31:0] multiplexer_1_out;

  and and_1 (and_1_out, En_PC, ~Stall);  // AND_Gate
  and and_2 (and_2_out, Flush, ~HLT);  // AND_Gate
  Multiplexer #(.width(32)) multiplexer_1 (.in0(Addr), .in1(32'hfffffff0), .out(multiplexer_1_out), .sel(RST));
  Register #(.width(32)) register_1 (.D(multiplexer_1_out), .en(or_1_out), .clk(Clk), .Q(PC_Out));  // open: clr
  or or_1 (or_1_out, and_1_out, and_2_out, RST);
  Adder #(.width(32)) adder_1 (.a(32'h8), .b(PC_Out), .out(Sum));  // open: cin, cout
endmodule

module Bypass (
  input  No_Bypass,
  input  Is_RegE_A,
  input  [3:0] REG_A,
  input  Is_RegE_B,
  input  [3:0] REG_B,
  input  Res_From_MEM_Reg,
  input  Res_From_MEM_RegE,
  input  [3:0] W_From_MEM,
  input  Res_From_WB_Reg,
  input  Res_From_WB_RegE,
  input  [3:0] W_From_WB,
  input  [31:0] Data_From_MEM,
  input  [31:0] Data_From_WB,
  output A,
  output B,
  output [31:0] Data_For_A,
  output [31:0] Data_For_B
);

  wire and_3_out, and_4_out, and_5_out, and_6_out, comparator_1_eq, comparator_2_eq, comparator_3_eq,
       comparator_4_eq, or_1_out, or_2_out, or_3_out, or_4_out, or_5_out, or_6_out, pla_1_out, pla_2_out;
  wire [4:4] and_1_out, and_2_out;

  and and_1 (and_1_out[4], ~Res_From_MEM_Reg, Res_From_MEM_RegE);  // AND_Gate
  or or_1 (or_1_out, Res_From_MEM_Reg, Res_From_MEM_RegE);
  and and_2 (and_2_out[4], ~Res_From_WB_Reg, Res_From_WB_RegE);  // AND_Gate
  or or_2 (or_2_out, Res_From_WB_Reg, Res_From_WB_Reg);
  PLA #(.in_width(5), .out_width(1), .\table ("00000 1 # Is0")) pla_1 (.in({Is_RegE_A, REG_A}), .out(pla_1_out));
  PLA #(.in_width(5), .out_width(1), .\table ("00000 1 # Is0")) pla_2 (.in({Is_RegE_B, REG_B}), .out(pla_2_out));
  Comparator #(.mode("unsigned"), .width(5)) comparator_1 (
    .a({Is_RegE_A, REG_A}), .b({and_1_out[4], W_From_MEM}), .eq(comparator_1_eq));  // open: gt, lt
  Comparator #(.mode("unsigned"), .width(5)) comparator_2 (
    .a({Is_RegE_B, REG_B}), .b({and_1_out[4], W_From_MEM}), .eq(comparator_2_eq));  // open: gt, lt
  Comparator #(.mode("unsigned"), .width(5)) comparator_3 (
    .a({Is_RegE_A, REG_A}), .b({and_2_out[4], W_From_WB}), .eq(comparator_3_eq));  // open: gt, lt
  Comparator #(.mode("unsigned"), .width(5)) comparator_4 (
    .a({Is_RegE_B, REG_B}), .b({and_2_out[4], W_From_WB}), .eq(comparator_4_eq));  // open: gt, lt
  and and_3 (and_3_out, comparator_1_eq, or_1_out, ~pla_1_out);  // AND_Gate
  and and_4 (and_4_out, comparator_2_eq, or_1_out, ~pla_2_out);  // AND_Gate
  and and_5 (and_5_out, comparator_3_eq, or_2_out, ~pla_1_out);  // AND_Gate
  and and_6 (and_6_out, comparator_4_eq, or_2_out, ~pla_2_out);  // AND_Gate
  or or_3 (or_3_out, ~and_5_out, and_3_out);  // OR_Gate
  or or_4 (or_4_out, ~and_6_out, and_4_out);  // OR_Gate
  Multiplexer #(.width(32)) multiplexer_1 (.in0(Data_From_WB), .in1(Data_From_MEM), .out(Data_For_A), .sel(or_3_out));
  or or_5 (or_5_out, and_3_out, and_5_out);
  or or_6 (or_6_out, and_4_out, and_6_out);
  Multiplexer #(.width(32)) multiplexer_2 (.in0(Data_From_WB), .in1(Data_From_MEM), .out(Data_For_B), .sel(or_4_out));
  and and_7 (A, or_5_out, ~No_Bypass);  // AND_Gate
  and and_8 (B, or_6_out, ~No_Bypass);  // AND_Gate
endmodule

module Flush (
  input  Branch,
  input  Clk,
  input  RST,
  input  HLT,
  output Flush_Out
);

  wire and_1_out, and_2_out, d_ff_1_q, or_1_out;

  D_Flip_Flop #(.trigger("falling")) d_ff_1 (
    .D(and_1_out), .clk(Clk), .Q(d_ff_1_q), .preset(and_2_out));  // open: Qn, reset
  and and_1 (and_1_out, Branch, ~Flush_Out);  // AND_Gate
  and and_2 (and_2_out, Branch, ~Flush_Out);  // AND_Gate
  or or_1 (or_1_out, RST, HLT);
  or or_2 (Flush_Out, d_ff_1_q, or_1_out);
endmodule

module Dec (
  input  Kernel,
  input  [31:0] Instr,
  output [3:0] A,
  output [3:0] B,
  output [3:0] E,
  output [31:0] Error_Code,
  output [2:0] Tipo,
  output [15:0] Ctrl_Word,
  output [15:0] Inmd,
  output [3:0] W,
  output [31:0] Instr_Out
);

  wire or_1_out, or_2_out, pla_2_out, pla_3_out, pla_4_out;
  wire [1:0] not_1_out, pla_1_out;
  wire [15:0] pla_5_out;
  wire [31:0] pull_resistor_1_node;

  Multiplexer #(.width(4)) multiplexer_1 (.in0(Instr[19:16]), .in1(4'b0000), .out(B), .sel(pla_2_out));
  Multiplexer #(.width(4)) multiplexer_2 (.in0(Instr[23:20]), .in1(4'b0010), .out(E), .sel(or_1_out));
  PLA #(.in_width(5), .\table ("01011 10 # GOF\n01100 10 # LDI\n01101 10 # ADI\n10010 01 # LOD\n10100 01 # CYE\n10101 01 # CYR")) pla_1 (
    .in(Instr[28:24]), .out(pla_1_out));
  PLA #(.in_width(5), .out_width(1), .\table ("10100 1 # CYE\n10101 1 # CYR")) pla_2 (
    .in(Instr[28:24]), .out(pla_2_out));
  PLA #(.in_width(5), .out_width(1), .\table ("00000 1 # NOP\n00001 1 # HLT\n00010 1 # ADD\n00011 1 # SUB\n00100 1 # MUL\n00101 1 # DIV\n00110 1 # NOR\n00111 1 # AND\n01000 1 # XOR\n01001 1 # RSH\n01010 1 # LSH\n01011 1 # GOF\n01100 1 # LDI\n01101 1 # ADI\n01110 1 # JMP\n01111 1 # BRH\n10000 1 # CAL\n10001 1 # RET\n10010 1 # LOD\n10011 1 # STR\n10100 1 # CYE\n10101 1 # CYR\n10110 1 # SCL\n10111 1 # SRT")) pla_3 (
    .in(Instr[28:24]), .out(pla_3_out));
  PLA #(.in_width(5), .out_width(1), .\table ("00001 1 # HLT\n10100 1 # CYE\n10101 1 # CYR\n10111 1 # SRT")) pla_4 (
    .in(Instr[28:24]), .out(pla_4_out));
  or or_1 (or_1_out, pla_5_out[3], pla_5_out[9]);
  PLA #(.in_width(5), .out_width(16), .\table ("00000 0000000000000000 # NOP\n00001 0000010000000000 # HLT\n00010 0000100000000100 # ADD\n00011 0000100000000100 # SUB\n00100 0000100000000100 # MUL\n00101 0000100000000100 # DIV\n00110 0000100000000100 # NOR\n00111 0000100000000100 # AND\n01000 0000100000000100 # XOR\n01001 0000100000000100 # RSH\n01010 0000100000000100 # LSH\n01011 0000100000000001 # GOF\n01100 0000100000000010 # LDI\n01101 0000100000000110 # ADI\n01110 0000000000010000 # JMP\n01111 0000000000100000 # BRH\n10000 0100100110001000 # CAL\n10001 0100101100001000 # RET\n10010 0010100100000010 # LOD\n10011 0000000110000010 # STR\n10100 1000100000000000 # CYE\n10101 0001000000000000 # CYR\n10110 0000000001010000 # SCL\n10111 0000000001000000 # SRT")) pla_5 (
    .in(Instr[28:24]), .out(pla_5_out));
  not not_1 (not_1_out[0], pla_3_out);
  and and_1 (not_1_out[1], ~Kernel, pla_4_out);  // AND_Gate
  or or_2 (or_2_out, not_1_out[1], not_1_out[0]);
  Multiplexer #(.select(2), .width(4)) multiplexer_3 (
    .in0(Instr[15:12]), .in1(Instr[19:16]), .in2(Instr[23:20]), .out(W), .sel(pla_1_out));  // open: in3
  Multiplexer #(.width(16)) multiplexer_4 (.in0(pla_5_out), .in1(16'h50), .out(Ctrl_Word), .sel(or_2_out));
  Pull_Resistor pull_resistor_1 (.node(pull_resistor_1_node));
  Multiplexer #(.select(2), .width(32)) multiplexer_5 (
    .in0(pull_resistor_1_node), .in1(32'h4), .in2(32'h3), .in3(pull_resistor_1_node), .out(Error_Code),
    .sel(not_1_out));

  assign A = Instr[23:20];
  assign Inmd = Instr[15:0];
  assign Instr_Out = Instr;
  assign Tipo = Instr[31:29];
endmodule

module Instr_Fecher (
  input  [31:0] PC,
  input  En_Write,
  input  Flush,
  input  Clk,
  input  [63:0] Data_In,
  output [31:0] PC_Required,
  output En_PC,
  output Need_Instr,
  output [31:0] Instr_Out
);

  wire and_1_out, and_2_out, and_3_out, and_4_out, and_5_out, counter_1_carry, counter_2_carry, not_1_out,
       or_2_out, or_3_out, s_r_ff_1_q, Valid_q;
  wire [1:0] counter_1_q;
  wire [3:0] counter_2_q;
  wire [31:0] bit_extender_1_out, shifter_1_out;
  wire [63:0] multiplexer_1_out, Queue_p5, Queue_p6, Queue_p7, Queue_p8, Queue_p9, Queue_p10, Queue_p11,
       Queue_p12;

  S_R_Flip_Flop #(.trigger("falling")) Valid (
    .S(En_Write), .clk(Clk), .R(Flush), .Q(Valid_q), .reset(or_2_out));  // open: Qn, preset
  or or_1 (En_PC, Valid_q, En_Write);
  and and_1 (and_1_out, s_r_ff_1_q, En_Write);
  and and_2 (and_2_out, Need_Instr, En_PC, En_Write);
  and and_3 (and_3_out, ~counter_2_q[0], ~counter_2_q[1], ~counter_2_q[2], ~counter_2_q[3], counter_2_carry);  // AND_Gate
  or or_2 (or_2_out, and_3_out, Flush);
  and and_4 (and_4_out, En_PC, En_Write);
  // Probe on counter_1_q
  Counter #(.max('h3), .width(2)) counter_1 (
    .count(and_1_out), .Q(counter_1_q), .carry(counter_1_carry), .clk(Clk), .clr(or_3_out));  // open: load, D, up
  or or_3 (or_3_out, Need_Instr, Flush);
  and and_5 (and_5_out, and_4_out, Need_Instr);
  Counter #(.max('hf), .width(4)) counter_2 (
    .count(En_PC), .Q(counter_2_q), .carry(counter_2_carry), .up(and_5_out), .clk(Clk), .clr(Flush));  // open: load, D
  // Shift_Register #(.width(64)) Queue: pin names not known; wires that end beside it: Flush, and_2_out, Clk, Data_In, Queue_p5, Queue_p6, Queue_p7, Queue_p8, Queue_p9, Queue_p10, Queue_p11, Queue_p12
  assign bit_extender_1_out = {{28{1'b0}}, counter_2_q};  // Bit_Extender bit_extender_1
  S_R_Flip_Flop #(.trigger("falling")) s_r_ff_1 (
    .S(counter_2_carry), .clk(Clk), .R(counter_1_carry), .Q(s_r_ff_1_q), .Qn(Need_Instr), .reset(or_2_out));  // open: preset
  Shifter #(.width(32)) shifter_1 (.in(bit_extender_1_out), .\dist (5'b00010), .out(shifter_1_out));
  // Probe on counter_2_q
  Adder #(.width(32)) adder_1 (.a(PC), .b(shifter_1_out), .out(PC_Required));  // open: cin, cout
  Multiplexer #(.select(3), .width(64)) multiplexer_1 (
    .in0(Queue_p5), .in1(Queue_p6), .in2(Queue_p7), .in3(Queue_p8), .in4(Queue_p9), .in5(Queue_p10),
    .in6(Queue_p11), .in7(Queue_p12), .out(multiplexer_1_out), .sel(counter_2_q[3:1]));
  not not_1 (not_1_out, counter_2_q[0]);
  Multiplexer #(.width(32)) multiplexer_2 (
    .in0(multiplexer_1_out[31:0]), .in1(multiplexer_1_out[63:32]), .out(Instr_Out), .sel(not_1_out));
endmodule

module Instr_Fecher_V2 (
  input  [31:0] PC,
  input  En_Write,
  input  Flush,
  input  Clk,
  input  Stall,
  input  [63:0] Data_In,
  output [31:0] Addr,
  output En_IF_To_DEC,
  output En_PC,
  output Need_Instr,
  output [31:0] Instr_Out,
  output [31:0] PC_Out
);

  wire and_2_out, and_3_out, and_4_out, and_5_out, and_6_out, and_7_out, and_8_out, comparator_1_eq,
       comparator_2_eq, counter_1_carry, nand_1_out, not_1_out, or_1_out, or_2_out, or_3_out, or_4_out,
       s_r_ff_2_q, s_r_ff_2_qn, Valid;
  wire [3:0] counter_2_q;
  wire [31:0] adder_1_out, multiplexer_3_out, multiplexer_4_out;
  wire [63:0] multiplexer_1_out, multiplexer_2_out, shift_register_1_p5, shift_register_1_p6,
       shift_register_1_p7, shift_register_1_p8, shift_register_2_p5, shift_register_2_p6,
       shift_register_2_p7, shift_register_2_p8, shift_register_2_p9, shift_register_2_p10,
       shift_register_2_p11, shift_register_2_p12, shift_register_2_p13, shift_register_2_p14,
       shift_register_2_p15, shift_register_2_p16;

  and and_1 (En_PC, ~and_8_out, En_Write);  // AND_Gate
  S_R_Flip_Flop s_r_ff_1 (.S(En_Write), .clk(Clk), .R(and_2_out), .Q(Valid), .reset(Flush));  // open: Qn, preset
  and and_2 (and_2_out, Valid, comparator_1_eq);
  or or_1 (or_1_out, Flush, counter_1_carry);
  Adder #(.width(32)) adder_1 (.a(PC), .b(32'h4), .out(adder_1_out));  // open: cin, cout
  Counter #(.max('h3), .width(2)) counter_1 (
    .count(and_8_out), .carry(counter_1_carry), .clk(Clk), .clr(or_1_out));  // open: load, D, Q, up
  and and_3 (and_3_out, Valid, ~comparator_1_eq);  // AND_Gate
  and and_4 (and_4_out, En_Write, Valid);
  and and_5 (and_5_out, En_Write, ~Stall);  // AND_Gate
  or or_2 (or_2_out, and_3_out, and_4_out);
  and and_6 (and_6_out, or_2_out, ~Stall);  // AND_Gate
  // Shift_Register #(.width(64)) shift_register_1: pin names not known; wires that end beside it: Flush, and_5_out, Clk, Data_In, shift_register_1_p5, shift_register_1_p6, shift_register_1_p7, shift_register_1_p8
  // Shift_Register #(.width(64)) shift_register_2: pin names not known; wires that end beside it: Flush, and_5_out, Clk, {adder_1_out, PC}, shift_register_2_p5, shift_register_2_p6, shift_register_2_p7, shift_register_2_p8, shift_register_2_p9, shift_register_2_p10, shift_register_2_p11, shift_register_2_p12, shift_register_2_p13, shift_register_2_p14, shift_register_2_p15, shift_register_2_p16
  and and_7 (and_7_out, En_Write, ~and_8_out);  // AND_Gate
  Counter #(.max('hf), .width(4)) counter_2 (
    .count(and_6_out), .Q(counter_2_q), .up(and_7_out), .clk(Clk), .clr(Flush));  // open: load, D, carry
  Comparator #(.mode("unsigned"), .width(4)) comparator_1 (
    .a(4'b0000), .b(counter_2_q), .eq(comparator_1_eq));  // open: gt, lt
  S_R_Flip_Flop s_r_ff_2 (
    .Q(s_r_ff_2_q), .Qn(s_r_ff_2_qn), .preset(comparator_2_eq), .reset(or_3_out));  // open: S, clk, R
  Comparator #(.mode("unsigned"), .width(4)) comparator_2 (
    .a(counter_2_q), .b(4'b1111), .eq(comparator_2_eq));  // open: gt, lt
  or or_3 (or_3_out, Flush, counter_1_carry);
  and and_8 (and_8_out, s_r_ff_2_q, ~Stall);  // AND_Gate
  Multiplexer #(.select(3), .width(64)) multiplexer_1 (
    .in0(shift_register_1_p5), .in1(shift_register_1_p6), .in2(shift_register_1_p7),
    .in3(shift_register_1_p8), .in4(shift_register_2_p5), .in5(shift_register_2_p6),
    .in6(shift_register_2_p7), .in7(shift_register_2_p8), .out(multiplexer_1_out), .sel(counter_2_q[3:1]));
  Multiplexer #(.select(3), .width(64)) multiplexer_2 (
    .in0(shift_register_2_p9), .in1(shift_register_2_p10), .in2(shift_register_2_p11),
    .in3(shift_register_2_p12), .in4(shift_register_2_p13), .in5(shift_register_2_p14),
    .in6(shift_register_2_p15), .in7(shift_register_2_p16), .out(multiplexer_2_out), .sel(counter_2_q[3:1]));
  or or_4 (or_4_out, En_Write, Valid);
  not not_1 (not_1_out, counter_2_q[0]);
  and and_9 (En_IF_To_DEC, or_4_out, ~Stall);  // AND_Gate
  and and_10 (Need_Instr, s_r_ff_2_qn, ~Flush);  // AND_Gate
  Multiplexer #(.width(32)) multiplexer_3 (
    .in0(multiplexer_1_out[31:0]), .in1(multiplexer_1_out[63:32]), .out(multiplexer_3_out), .sel(not_1_out));
  Multiplexer #(.width(32)) multiplexer_4 (
    .in0(multiplexer_2_out[31:0]), .in1(multiplexer_2_out[63:32]), .out(multiplexer_4_out), .sel(not_1_out));
  nand nand_1 (nand_1_out, En_Write, ~Valid);  // NAND_Gate
  Multiplexer #(.width(32)) multiplexer_5 (
    .in0(Data_In[31:0]), .in1(multiplexer_3_out), .out(Instr_Out), .sel(nand_1_out));
  Multiplexer #(.width(32)) multiplexer_6 (.in0(PC), .in1(multiplexer_4_out), .out(PC_Out), .sel(nand_1_out));

  assign Addr = PC;

  // Other names for the same wires on the sheet: First_Instr[31:0] = Data_In[31:0]
endmodule

module Exception_Generator (
  input  JMP,
  input  [31:0] PC_In,
  input  [31:0] JMP_Addr,
  input  SCL,
  input  En_INTs,
  input  [31:0] Cause_INT,
  input  IRQ,
  input  Clk,
  input  [31:0] New_Cause,
  input  RST,
  input  SRT,
  output [31:0] EPC_In,
  output [31:0] Cause_Out,
  output Exception,
  output W_Cause
);

  wire and_1_out, and_2_out, and_3_out, and_4_out, and_5_out, d_ff_1_qn, INT, IRQ_t, ISF_q, j_k_ff_1_q,
       or_1_out, or_4_out;
  wire [31:0] adder_1_out, multiplexer_1_out, multiplexer_2_out, multiplexer_3_out, multiplexer_4_out,
       multiplexer_5_out, multiplexer_6_out;

  J_K_Flip_Flop j_k_ff_1 (.J(IRQ), .K(IRQ_t), .clk(Clk), .Q(j_k_ff_1_q));  // open: Qn, preset, reset
  Comparator #(.mode("unsigned"), .width(32)) comparator_1 (
    .a(New_Cause), .b({32{1'b0}}), .gt(Exception));  // open: eq, lt
  T_Flip_Flop ISF (.T(INT), .clk(Clk), .Q(ISF_q), .reset(or_1_out));  // open: Qn, preset
  or or_1 (or_1_out, RST, SRT);
  Adder #(.width(32)) adder_1 (.a(PC_In), .b(32'h4), .out(adder_1_out));  // open: cin, cout
  Multiplexer #(.enable("true"), .width(32)) multiplexer_1 (
    .in0({32{1'b0}}), .in1(Cause_INT), .out(multiplexer_1_out), .sel(j_k_ff_1_q), .en(En_INTs));
  Multiplexer #(.width(32)) multiplexer_2 (.in0({32{1'b0}}), .in1(New_Cause), .out(multiplexer_2_out), .sel(Exception));
  and and_1 (and_1_out, ~SCL, JMP);  // AND_Gate
  Multiplexer #(.width(32)) multiplexer_3 (.in0(adder_1_out), .in1(JMP_Addr), .out(multiplexer_3_out), .sel(and_1_out));
  and and_2 (and_2_out, ~Exception, IRQ_t);  // AND_Gate
  or or_2 (IRQ_t, SCL, and_3_out);
  and and_3 (and_3_out, j_k_ff_1_q, En_INTs);
  or or_3 (INT, and_3_out, SCL, Exception);
  Multiplexer #(.width(32)) multiplexer_4 (
    .in0(multiplexer_1_out), .in1(multiplexer_2_out), .out(multiplexer_4_out), .sel(Exception));
  and and_4 (and_4_out, INT, ~IRQ_t, ISF_q);  // AND_Gate
  D_Flip_Flop d_ff_1 (.D(and_5_out), .clk(Clk), .Q(W_Cause), .Qn(d_ff_1_qn));  // open: preset, reset
  and and_5 (and_5_out, INT, d_ff_1_qn);
  Multiplexer #(.width(32)) multiplexer_5 (
    .in0(PC_In), .in1(multiplexer_3_out), .out(multiplexer_5_out), .sel(and_2_out));
  Register #(.width(32)) register_1 (.D(multiplexer_5_out), .en(or_4_out), .clk(Clk), .Q(EPC_In), .clr(or_1_out));
  or or_4 (or_4_out, INT, SCL);
  Multiplexer #(.width(32)) multiplexer_6 (
    .in0(multiplexer_4_out), .in1(32'h5), .out(multiplexer_6_out), .sel(and_4_out));
  Register #(.width(32)) register_2 (.D(multiplexer_6_out), .en(INT), .clk(Clk), .Q(Cause_Out), .clr(or_1_out));

  // Notes on the sheet:
  //   Doble Fault Code
endmodule

module Pruebas (
  input  in_1,
  input  in_2,
  input  in_3
);

  wire flush_1_flush_out, instr_fecher_v2_1_en_pc, instr_fecher_v2_1_need_instr;
  wire [19:0] bit_extender_1_out;
  wire [31:0] instr_fecher_v2_1_addr, instr_fecher_v2_1_instr_out, instr_fecher_v2_1_pc_out, pc_1_pc_out,
       pc_1_sum, register_1_q, register_2_q;
  wire [63:0] undriven;

  // Probe on instr_fecher_v2_1_addr
  Instr_Fecher_V2 instr_fecher_v2_1 (
    .En_Write(instr_fecher_v2_1_need_instr), .Flush(flush_1_flush_out), .Clk(in_1), .Data_In(undriven),
    .PC(pc_1_pc_out), .Need_Instr(instr_fecher_v2_1_need_instr), .PC_Out(instr_fecher_v2_1_pc_out),
    .Instr_Out(instr_fecher_v2_1_instr_out), .En_PC(instr_fecher_v2_1_en_pc), .Addr(instr_fecher_v2_1_addr));  // open: Stall, En_IF_To_DEC
  PC pc_1 (
    .Addr(pc_1_sum), .En_PC(instr_fecher_v2_1_en_pc), .Clk(in_1), .RST(in_3), .Flush(flush_1_flush_out),
    .Sum(pc_1_sum), .PC_Out(pc_1_pc_out));  // open: Stall, HLT
  Flush flush_1 (.RST(in_3), .Clk(in_1), .Branch(in_2), .Flush_Out(flush_1_flush_out));  // open: HLT
  Bit_Extender #(.in_width(32), .out_width(20), .\type ("zero")) bit_extender_1 (
    .in(instr_fecher_v2_1_addr), .out(bit_extender_1_out));
  // Probe on undriven
  // ROM #(.addrWidth(20), .line("octo"), .misaligned("true")) rom_1: pin names not known; wires that end beside it: bit_extender_1_out
  Register #(.width(32)) register_1 (
    .D({instr_fecher_v2_1_instr_out[7:0], instr_fecher_v2_1_instr_out[15:8], instr_fecher_v2_1_instr_out[23:16], instr_fecher_v2_1_instr_out[31:24]}),
    .clk(in_1), .Q(register_1_q));  // open: en, clr
  Register #(.width(32)) register_2 (.D(instr_fecher_v2_1_pc_out), .clk(in_1), .Q(register_2_q));  // open: en, clr
  // Probe on register_1_q
  // Probe on register_2_q

  // Notes on the sheet:
  //   contents of rom_1 (hex, n*v repeats v):
  //   c 10 0 0 c 20 0 1 c 30 0 a 2 12 40 0 2 2 10 0 2 4 20 0 d 30 ff ff c f0 ff f0 c e0 0 10 8a fe f0 0 c
  //   e0 0 c 82 fe f0 0 f 1f 0 0 1 1048491*0 c f0 ff f0 c e0 0 10 a fe f0 0 c e0 0 0 2 fe f0 0 e f
endmodule
