// Logisim project LAPIC.circ as structural Verilog
module Local_APIC (
  input  DMA_ACK,
  input  [31:0] Addr_From_Perif,
  input  [31:0] Data_In,
  input  [31:0] Addr_From_CPU,
  input  [1:0] RoW,
  input  CLk,
  input  RST,
  output [63:0] Data_Out,
  output MMIO_LAPIC,
  output [31:0] Cause,
  output IRQ
);

  wire and_1_out, bit_extender_2_out, in_service_register_1_irq, interrupt_request_register_1_valid,
       mmio_1_eoi_out, task_priority_register_1_isr_write, task_priority_register_1_valid_out;
  wire [6:0] in_service_register_1_actual_isr, interrupt_request_register_1_irr_out,
       task_priority_register_1_new_isr;
  wire [31:0] mmio_1_apic_config_out, mmio_1_data_out, mmio_1_timmer_id, mmio_1_timmer_start, mmio_1_tpr_out;
  wire [63:0] interrupt_request_register_1_irr_a_out, interrupt_request_register_1_irr_b_out,
       local_timmer_1_lvt_1, local_timmer_1_lvt_2, mmio_1_irr_mmio_1, mmio_1_irr_mmio_2;

  Local_Timmer local_timmer_1 (
    .RST(RST), .Clk(CLk), .Timmer_Max(mmio_1_timmer_start), .Timmer_Config(mmio_1_timmer_id),
    .LVT_1(local_timmer_1_lvt_1), .LVT_2(local_timmer_1_lvt_2));
  assign Data_Out = {{32{1'b0}}, mmio_1_data_out};  // Bit_Extender bit_extender_1
  Interrupt_Request_Register interrupt_request_register_1 (
    .Clk(CLk), .LVT_1(local_timmer_1_lvt_1), .LVT_2(local_timmer_1_lvt_2), .MMIO_1(mmio_1_irr_mmio_1),
    .MMIO_2(mmio_1_irr_mmio_2), .IRQ_ACK(and_1_out), .RST(RST),
    .IRR_Out(interrupt_request_register_1_irr_out), .Valid(interrupt_request_register_1_valid),
    .IRR_A_Out(interrupt_request_register_1_irr_a_out), .IRR_B_Out(interrupt_request_register_1_irr_b_out));
  and and_1 (and_1_out, task_priority_register_1_valid_out, task_priority_register_1_isr_write);
  MMIO mmio_1 (
    .DMA_ACK(DMA_ACK), .Addr_CPU(Addr_From_CPU), .Addr_Perif(Addr_From_Perif), .RST(RST), .Clk(CLk),
    .Data_In(Data_In), .RoW(RoW), .IRR_MMIO_In_1(interrupt_request_register_1_irr_a_out),
    .IRR_MMIO_In_2(interrupt_request_register_1_irr_b_out), .MMIO_LAPIC(MMIO_LAPIC),
    .Data_Out(mmio_1_data_out), .Timmer_Start(mmio_1_timmer_start), .TPR_Out(mmio_1_tpr_out),
    .EOI_Out(mmio_1_eoi_out), .Timmer_ID(mmio_1_timmer_id), .APIC_Config_Out(mmio_1_apic_config_out),
    .IRR_MMIO_1(mmio_1_irr_mmio_1), .IRR_MMIO_2(mmio_1_irr_mmio_2));
  Bit_Extender #(.in_width(32), .out_width(1), .\type ("zero")) bit_extender_2 (
    .in(mmio_1_apic_config_out), .out(bit_extender_2_out));
  Task_Priority_Register task_priority_register_1 (
    .ISR(in_service_register_1_actual_isr), .MMIO_TPR_In(mmio_1_tpr_out),
    .Valid(interrupt_request_register_1_valid), .IRR_In(interrupt_request_register_1_irr_out),
    .ISR_Write(task_priority_register_1_isr_write), .Valid_Out(task_priority_register_1_valid_out),
    .New_ISR(task_priority_register_1_new_isr));
  In_Service_Register in_service_register_1 (
    .ISR_Write(task_priority_register_1_isr_write), .RST(RST), .Clk(CLk),
    .New_ISR(task_priority_register_1_new_isr), .Valid(task_priority_register_1_valid_out),
    .EOI(mmio_1_eoi_out), .IRQ(in_service_register_1_irq), .Actual_ISR(in_service_register_1_actual_isr),
    .Cause(Cause));
  and and_2 (IRQ, in_service_register_1_irq, bit_extender_2_out);
endmodule

module In_Service_Register (
  input  EOI,
  input  ISR_Write,
  input  RST,
  input  Clk,
  input  [6:0] New_ISR,
  input  Valid,
  output [6:0] Actual_ISR,
  output [31:0] Cause,
  output IRQ
);

  wire or_1_out, pri_encoder_1_valid;
  wire [63:0] Actual_ISR_A, Actual_ISR_B, ISR_A_q, ISR_B_q, multiplexer_1_out, multiplexer_2_out, or_2_out,
       or_3_out, pri_decoder_1_a, pri_decoder_1_b, xor_1_out, xor_2_out;

  Pri_Decoder pri_decoder_1 (.INDEX(New_ISR), .VALID(Valid), .A(pri_decoder_1_a), .B(pri_decoder_1_b));
  or or_1 (or_1_out, ISR_Write, EOI);
  assign or_2_out = ISR_A_q | pri_decoder_1_a;  // OR_Gate or_2, 64 bits wide
  assign or_3_out = ISR_B_q | pri_decoder_1_b;  // OR_Gate or_3, 64 bits wide
  assign xor_1_out = Actual_ISR_A ^ ISR_A_q;  // XOR_Gate xor_1, 64 bits wide
  Multiplexer #(.width(64)) multiplexer_1 (.in0(or_2_out), .in1(xor_1_out), .out(multiplexer_1_out), .sel(EOI));
  Multiplexer #(.width(64)) multiplexer_2 (.in0(or_3_out), .in1(xor_2_out), .out(multiplexer_2_out), .sel(EOI));
  assign xor_2_out = Actual_ISR_B ^ ISR_B_q;  // XOR_Gate xor_2, 64 bits wide
  Register #(.width(64)) ISR_A (.D(multiplexer_1_out), .en(or_1_out), .clk(Clk), .Q(ISR_A_q), .clr(RST));
  Register #(.width(64)) ISR_B (.D(multiplexer_2_out), .en(or_1_out), .clk(Clk), .Q(ISR_B_q), .clr(RST));
  Pri_Encoder pri_encoder_1 (.A(ISR_A_q), .B(ISR_B_q), .INDEX(Actual_ISR), .VALID(pri_encoder_1_valid));
  D_Flip_Flop d_ff_1 (.D(ISR_Write), .clk(Clk), .Q(IRQ));  // open: Qn, preset, reset
  assign Cause = {{25{1'b0}}, Actual_ISR};  // Bit_Extender bit_extender_1
  Pri_Decoder pri_decoder_2 (.INDEX(Actual_ISR), .VALID(pri_encoder_1_valid), .A(Actual_ISR_A), .B(Actual_ISR_B));

  // Other names for the same wires on the sheet: IRQ_t = ISR_Write
endmodule

module Task_Priority_Register (
  input  [6:0] ISR,
  input  [31:0] MMIO_TPR_In,
  input  Valid,
  input  [6:0] IRR_In,
  output ISR_Write,
  output Valid_Out,
  output [6:0] New_ISR
);

  wire comparator_1_gt, not_1_out;
  wire [6:0] bit_extender_1_out, multiplexer_1_out;

  Bit_Extender #(.in_width(32), .out_width(7), .\type ("zero")) bit_extender_1 (
    .in(MMIO_TPR_In), .out(bit_extender_1_out));
  Comparator #(.mode("unsigned"), .width(7)) comparator_1 (
    .a(ISR), .b(bit_extender_1_out), .gt(comparator_1_gt));  // open: eq, lt
  Multiplexer #(.width(7)) multiplexer_1 (
    .in0(bit_extender_1_out), .in1(ISR), .out(multiplexer_1_out), .sel(comparator_1_gt));
  Comparator #(.mode("unsigned"), .width(7)) comparator_2 (
    .a(multiplexer_1_out), .b(IRR_In), .lt(ISR_Write));  // open: gt, eq
  not not_1 (not_1_out, ISR_Write);
  and and_1 (Valid_Out, ISR_Write, Valid);
  Multiplexer #(.enable("true"), .width(7)) multiplexer_2 (
    .in0(IRR_In), .in1({7{1'b0}}), .out(New_ISR), .sel(not_1_out), .en(Valid));
endmodule

module Interrupt_Request_Register (
  input  IRQ_ACK,
  input  RST,
  input  Clk,
  input  [63:0] LVT_1,
  input  [63:0] LVT_2,
  input  [63:0] MMIO_1,
  input  [63:0] MMIO_2,
  output [63:0] IRR_A_Out,
  output [6:0] IRR_Out,
  output Valid,
  output [63:0] IRR_B_Out
);

  wire [63:0] IRQ_ACK_1, IRQ_ACK_2, or_1_out, or_2_out, xor_1_out, xor_2_out;

  assign or_1_out = IRR_A_Out | LVT_1 | MMIO_1 | {64{1'b0}};  // OR_Gate or_1, 64 bits wide
  assign or_2_out = {64{1'b0}} | MMIO_2 | LVT_2 | IRR_B_Out;  // OR_Gate or_2, 64 bits wide
  Register #(.width(64)) IRR_A (.D(xor_1_out), .clk(Clk), .Q(IRR_A_Out), .clr(RST));  // open: en
  assign xor_1_out = or_1_out ^ IRQ_ACK_1;  // XOR_Gate xor_1, 64 bits wide
  Register #(.width(64)) IRR_B (.D(xor_2_out), .clk(Clk), .Q(IRR_B_Out), .clr(RST));  // open: en
  assign xor_2_out = or_2_out ^ IRQ_ACK_2;  // XOR_Gate xor_2, 64 bits wide
  Pri_Encoder pri_encoder_1 (.A(IRR_A_Out), .B(IRR_B_Out), .INDEX(IRR_Out), .VALID(Valid));
  Pri_Decoder pri_decoder_1 (.INDEX(IRR_Out), .VALID(IRQ_ACK), .A(IRQ_ACK_1), .B(IRQ_ACK_2));

  // Notes on the sheet:
  //   IPIs
endmodule

module MMIO (
  input  [31:0] Addr_CPU,
  input  [31:0] Addr_Perif,
  input  DMA_ACK,
  input  RST,
  input  Clk,
  input  [31:0] Data_In,
  input  [1:0] RoW,
  input  [63:0] IRR_MMIO_In_1,
  input  [63:0] IRR_MMIO_In_2,
  output MMIO_LAPIC,
  output [31:0] APIC_Config_Out,
  output [31:0] TPR_Out,
  output EOI_Out,
  output [31:0] Timmer_ID,
  output [31:0] Timmer_Start,
  output [63:0] IRR_MMIO_1,
  output [63:0] IRR_MMIO_2,
  output [31:0] Data_Out
);

  wire and_2_out, and_3_out, and_5_out, and_6_out, and_7_out, bit_extender_2_out, comparator_1_eq,
       decoder_1_out0, decoder_1_out1, decoder_1_out2, decoder_1_out3, decoder_1_out4, decoder_1_out5,
       decoder_1_out6, decoder_1_out7, decoder_1_out8, decoder_1_out9, decoder_1_out10, decoder_1_out11,
       DMA_ACK_t, or_1_out, pla_1_out, t_ff_1_q;
  wire [3:0] Addr, bit_extender_5_out, demultiplexer_1_out0, demultiplexer_1_out1;
  wire [6:0] bit_extender_1_out;
  wire [11:0] shifter_1_out;
  wire [31:0] Base_Addr_q, bit_extender_3_out, bit_extender_4_out, LAPIC_ID_q, multiplexer_1_out,
       multiplexer_2_out, multiplexer_3_out, multiplexer_4_out, multiplexer_5_out, multiplexer_6_out;
  wire [63:0] pri_decoder_1_a, pri_decoder_1_b;

  Multiplexer #(.width(32)) multiplexer_1 (.in0(Addr_CPU), .in1(Addr_Perif), .out(multiplexer_1_out), .sel(DMA_ACK_t));
  and and_1 (DMA_ACK_t, DMA_ACK, APIC_Config_Out[1]);
  or or_1 (or_1_out, RoW[0], DMA_ACK_t);
  and and_2 (and_2_out, MMIO_LAPIC, or_1_out);
  Decoder #(.select(4)) decoder_1 (
    .out0(decoder_1_out0), .out1(decoder_1_out1), .out2(decoder_1_out2), .out3(decoder_1_out3),
    .out4(decoder_1_out4), .out5(decoder_1_out5), .out6(decoder_1_out6), .out7(decoder_1_out7),
    .out8(decoder_1_out8), .out9(decoder_1_out9), .out10(decoder_1_out10), .out11(decoder_1_out11),
    .sel(Addr), .en(and_2_out));  // open: out12, out13, out14, out15
  Bit_Extender #(.in_width(32), .out_width(7), .\type ("zero")) bit_extender_1 (.in(Data_In), .out(bit_extender_1_out));
  and and_3 (and_3_out, ~t_ff_1_q, decoder_1_out0);  // AND_Gate
  Register #(.width(32)) LAPIC_ID (.D(Data_In), .en(decoder_1_out1), .clk(Clk), .Q(LAPIC_ID_q), .clr(RST));
  Register #(.width(32)) APIC_Config (.D(Data_In), .en(decoder_1_out2), .clk(Clk), .Q(APIC_Config_Out), .clr(RST));
  Register #(.width(32)) TPR (.D(Data_In), .en(decoder_1_out3), .clk(Clk), .Q(TPR_Out), .clr(RST));
  Register #(.width(32)) Timmer (.D(Data_In), .en(decoder_1_out5), .clk(Clk), .Q(Timmer_ID), .clr(RST));
  Register #(.width(32)) Start_Timmer (.D(Data_In), .en(decoder_1_out6), .clk(Clk), .Q(Timmer_Start), .clr(RST));
  T_Flip_Flop t_ff_1 (.clk(Clk), .T(and_3_out), .Q(t_ff_1_q), .reset(RST));  // open: Qn, preset
  Multiplexer #(.width(32)) multiplexer_2 (
    .in0(32'hfee00000), .in1(Base_Addr_q), .out(multiplexer_2_out), .sel(t_ff_1_q));
  Register #(.width(32)) Base_Addr (.D(Data_In), .en(decoder_1_out0), .Q(Base_Addr_q), .clk(Clk), .clr(RST));
  Bit_Extender #(.in_width(32), .out_width(1)) bit_extender_2 (.in(Data_In), .out(bit_extender_2_out));
  and and_4 (EOI_Out, bit_extender_2_out, decoder_1_out4);
  Multiplexer #(.width(32)) multiplexer_3 (
    .in0({32{1'b0}}), .in1(Data_In), .out(multiplexer_3_out), .sel(decoder_1_out7));
  Multiplexer #(.width(32)) multiplexer_4 (
    .in0({32{1'b0}}), .in1(Data_In), .out(multiplexer_4_out), .sel(decoder_1_out8));
  Multiplexer #(.width(32)) multiplexer_5 (
    .in0({32{1'b0}}), .in1(Data_In), .out(multiplexer_5_out), .sel(decoder_1_out9));
  Multiplexer #(.width(32)) multiplexer_6 (
    .in0({32{1'b0}}), .in1(Data_In), .out(multiplexer_6_out), .sel(decoder_1_out10));
  Pri_Decoder pri_decoder_1 (
    .INDEX(bit_extender_1_out), .VALID(decoder_1_out11), .A(pri_decoder_1_a), .B(pri_decoder_1_b));
  and and_5 (and_5_out, MMIO_LAPIC, ~DMA_ACK_t, ~RoW[0]);  // AND_Gate
  assign bit_extender_3_out = {{12{1'b0}}, multiplexer_1_out[31:12]};  // Bit_Extender bit_extender_3
  assign bit_extender_4_out = {{12{1'b0}}, multiplexer_2_out[31:12]};  // Bit_Extender bit_extender_4
  Multiplexer #(.enable("true"), .select(4), .width(32)) multiplexer_7 (
    .in0(multiplexer_2_out), .in1(LAPIC_ID_q), .in2(APIC_Config_Out), .in3(TPR_Out), .in5(Timmer_ID),
    .in6(Timmer_Start), .in7(IRR_MMIO_In_1[31:0]), .in8(IRR_MMIO_In_1[63:32]), .in9(IRR_MMIO_In_2[31:0]),
    .in10(IRR_MMIO_In_2[63:32]), .out(Data_Out), .sel(Addr), .en(and_5_out));  // open: in4, in11, in12, in13, in14, in15
  Bit_Extender #(.in_width(12), .out_width(4), .\type ("zero")) bit_extender_5 (
    .in(shifter_1_out), .out(bit_extender_5_out));
  Shifter #(.shift("lr"), .width(12)) shifter_1 (.in(multiplexer_1_out[11:0]), .\dist (4'b0010), .out(shifter_1_out));
  Demultiplexer #(.width(4)) demultiplexer_1 (
    .out0(demultiplexer_1_out0), .out1(demultiplexer_1_out1), .in(bit_extender_5_out), .sel(DMA_ACK_t));
  Comparator #(.mode("unsigned"), .width(32)) comparator_1 (
    .a(bit_extender_3_out), .b(bit_extender_4_out), .eq(comparator_1_eq));  // open: gt, lt
  Multiplexer #(.width(64)) multiplexer_8 (
    .in0({multiplexer_4_out, multiplexer_3_out}), .in1(pri_decoder_1_a), .out(IRR_MMIO_1),
    .sel(decoder_1_out11));
  Multiplexer #(.width(64)) multiplexer_9 (
    .in0({multiplexer_6_out, multiplexer_5_out}), .in1(pri_decoder_1_b), .out(IRR_MMIO_2),
    .sel(decoder_1_out11));
  PLA #(.in_width(4), .out_width(1), .\table ("1011 1 # 11")) pla_1 (.in(demultiplexer_1_out1), .out(pla_1_out));
  and and_6 (and_6_out, comparator_1_eq, RoW[1]);
  Multiplexer #(.width(4)) multiplexer_10 (
    .in0(demultiplexer_1_out0), .in1(demultiplexer_1_out1), .out(Addr), .sel(DMA_ACK_t));
  and and_7 (and_7_out, DMA_ACK_t, comparator_1_eq);
  Multiplexer multiplexer_11 (.in0(and_6_out), .in1(pla_1_out), .out(MMIO_LAPIC), .sel(and_7_out));

  // Other names for the same wires on the sheet: En_Perif_IRQs = APIC_Config_Out[1]; Enable = MMIO_LAPIC;
  //   RAM = RoW[1]

  // Notes on the sheet:
  //   Atributes
  //   LVTs
  //   Timer
  //   Config
  //   MSI_MMIO
endmodule

module Local_Timmer (
  input  [31:0] Timmer_Config,
  input  RST,
  input  Clk,
  input  [31:0] Timmer_Max,
  output [63:0] LVT_1,
  output [63:0] LVT_2
);

  wire and_1_out, bit_extender_1_out, counter_1_carry;

  Bit_Extender #(.in_width(25), .out_width(1), .\type ("zero")) bit_extender_1 (
    .in(Timmer_Config[31:7]), .out(bit_extender_1_out));
  Counter #(.max('hffffffff), .width(32)) counter_1 (
    .clr(RST), .load(counter_1_carry), .up(1'b0), .count(bit_extender_1_out), .clk(Clk), .D(Timmer_Max),
    .carry(counter_1_carry));  // open: Q
  and and_1 (and_1_out, bit_extender_1_out, counter_1_carry);
  Pri_Decoder pri_decoder_1 (.INDEX(Timmer_Config[6:0]), .VALID(and_1_out), .A(LVT_1), .B(LVT_2));
endmodule

// VHDL entity Pri_Encoder, as the project stores it:
-- =============================================================================
-- Priority Encoder - Codificador de Prioridad
-- =============================================================================
-- Descripcion:
--   Recibe dos operandos de 64 bits (A y B). Los concatena en un vector de
--   128 bits donde B ocupa los bits [127:64] y A los bits [63:0].
--   Devuelve de forma ASINCRONA (combinacional puro) un codigo de 7 bits que
--   representa la posicion del bit '1' mas significativo (MSB activo).
--
--   Si ningun bit esta activo, la salida es "0000000" y la senal VALID = '0'.
--
-- Entradas:
--   A       : std_logic_vector(63 downto 0)  -- Operando bajo  [63:0]
--   B       : std_logic_vector(63 downto 0)  -- Operando alto [127:64]
--
-- Salidas:
--   INDEX   : std_logic_vector(6 downto 0)   -- Posicion del bit mas alto activo
--   VALID   : std_logic                      -- '1' si al menos un bit esta activo
-- =============================================================================

library IEEE;
use IEEE.STD_LOGIC_1164.ALL;
use IEEE.NUMERIC_STD.ALL;

-- -----------------------------------------------------------------------------
-- Entity
-- -----------------------------------------------------------------------------
entity Pri_Encoder is
    port (
        -- Operandos de entrada (64 bits cada uno)
        A     : in  std_logic_vector(63 downto 0);   -- bits [63:0]
        B     : in  std_logic_vector(63 downto 0);   -- bits [127:64]

        -- Resultado combinacional
        INDEX : out std_logic_vector(6 downto 0);    -- posicion del MSB activo
        VALID : out std_logic                         -- indica al menos un bit activo
    );
end entity Pri_Encoder;

-- -----------------------------------------------------------------------------
-- Architecture - Combinacional / Asincrona
-- -----------------------------------------------------------------------------
architecture rtl of Pri_Encoder is

    -- Vector interno de 128 bits: B en la mitad alta, A en la baja
    signal combined : std_logic_vector(127 downto 0);

begin

    -- -------------------------------------------------------------------------
    -- Concatenacion: B es mas significativo que A
    -- combined[127:64] = B
    -- combined[ 63: 0] = A
    -- -------------------------------------------------------------------------
    combined <= B & A;

    -- -------------------------------------------------------------------------
    -- Proceso combinacional - Priority Encoder
    -- Recorre el vector desde el bit mas alto (127) hacia el mas bajo (0).
    -- En cuanto encuentra el primer '1', codifica su posicion en INDEX y
    -- activa VALID. Si no hay ningun '1', INDEX = 0 y VALID = '0'.
    -- -------------------------------------------------------------------------
    PRIORITY_ENC : process(combined)
        variable found : boolean;
    begin
        INDEX <= (others => '0');
        VALID <= '0';
        found := false;

        for i in 127 downto 0 loop
            if (combined(i) = '1') and (not found) then
                INDEX <= std_logic_vector(to_unsigned(i, 7));
                VALID <= '1';
                found := true;
            end if;
        end loop;

    end process PRIORITY_ENC;

end architecture rtl;

// VHDL entity Pri_Decoder, as the project stores it:
-- =============================================================================
-- Priority Decoder - Decodificador de Prioridad
-- =============================================================================
-- Descripcion:
--   Es el inverso del Pri_Encoder. Recibe un codigo de 7 bits (INDEX) que
--   representa una posicion de bit entre 0 y 127, y genera un vector de 128
--   bits "one-hot" (un solo bit activo) particionado en dos salidas de 64 bits.
--
--   La salida sigue el mismo convenio que Pri_Encoder:
--     A   cubre los bits  [63:  0]  (posiciones  0 ..  63)
--     B   cubre los bits [127: 64]  (posiciones 64 .. 127)
--
--   Si VALID = '0' ambas salidas son todo ceros, independientemente de INDEX.
--
-- Entradas:
--   INDEX  : std_logic_vector(6 downto 0)  -- Posicion del bit a activar (0-127)
--   VALID  : std_logic                     -- '1' habilita la decodificacion
--
-- Salidas:
--   A      : std_logic_vector(63 downto 0) -- bits [63:0]   del resultado
--   B      : std_logic_vector(63 downto 0) -- bits [127:64] del resultado
-- =============================================================================

library IEEE;
use IEEE.STD_LOGIC_1164.ALL;
use IEEE.NUMERIC_STD.ALL;

-- -----------------------------------------------------------------------------
-- Entity
-- -----------------------------------------------------------------------------
entity Pri_Decoder is
    port (
        -- Entrada codificada
        INDEX  : in  std_logic_vector(6 downto 0);   -- posicion del bit activo
        VALID  : in  std_logic;                       -- habilita la decodificacion

        -- Salidas one-hot (64 bits cada una)
        A      : out std_logic_vector(63 downto 0);   -- bits [63:0]
        B      : out std_logic_vector(63 downto 0)    -- bits [127:64]
    );
end entity Pri_Decoder;

-- -----------------------------------------------------------------------------
-- Architecture - Combinacional / Asincrona
-- -----------------------------------------------------------------------------
architecture rtl of Pri_Decoder is

    -- Vector interno de 128 bits (one-hot)
    signal combined : std_logic_vector(127 downto 0);

begin

    -- -------------------------------------------------------------------------
    -- Proceso combinacional - Priority Decoder
    -- Activa solo el bit cuya posicion coincide con INDEX.
    -- Si VALID = '0', el resultado es todo ceros.
    -- -------------------------------------------------------------------------
    PRIORITY_DEC : process(INDEX, VALID)
        variable pos : integer range 0 to 127;
    begin
        combined <= (others => '0');          -- default: todo apagado

        if VALID = '1' then
            pos := to_integer(unsigned(INDEX));
            combined(pos) <= '1';             -- activa el bit indicado
        end if;

    end process PRIORITY_DEC;

    -- -------------------------------------------------------------------------
    -- Separacion del vector en dos salidas de 64 bits
    -- B <-- combined[127:64]   (posiciones 64 .. 127)
    -- A <-- combined[ 63: 0]   (posiciones  0 ..  63)
    -- -------------------------------------------------------------------------
    A <= combined(63  downto  0);
    B <= combined(127 downto 64);

end architecture rtl;
