// Logisim project MEM.circ as structural Verilog
module MMU (
  input  [3:0] E_Read,
  input  En_RegE,
  input  [3:0] W_Addr,
  input  [31:0] Data_From_CPU,
  input  Kernel,
  input  [31:0] Data_In,
  input  Stall_RAM,
  input  RAM_Ready,
  input  RST_for_INT,
  input  RST,
  input  Clk,
  input  IF_REQ,
  input  [31:0] IF_Addr,
  input  [1:0] MEM_REQ,
  input  [31:0] MEM_Addr,
  output [31:0] Data_To_CPU,
  output MEM_Write,
  output STALL,
  output [31:0] Addr,
  output IF_Write,
  output Exc,
  output [31:0] Code,
  output [1:0] RoW,
  output En_Write,
  output En_Read,
  output RAM_REQ
);

  wire Aling_Fault, and_1_out, and_2_out, and_3_out, and_4_out, and_7_out, and_8_out, Final_Addr,
       mmu_registers_1_en_mmu, mmu_registers_1_en_tlb, mmu_registers_1_flush_tlbs, not_1_out, or_3_out,
       page_walker_1_if_write, page_walker_1_write_d_tlb, page_walker_1_write_i_tlb, tlb_lru_1_hit,
       tlb_lru_2_hit;
  wire [1:0] bit_extender_1_out;
  wire [15:0] page_walker_1_code;
  wire [31:0] mmu_registers_1_cr3_out, mmu_registers_1_pcid_out, page_walker_1_cr2, page_walker_1_tlb_write,
       tlb_lru_1_phys_frame, tlb_lru_2_phys_frame;

  not not_1 (not_1_out, MEM_REQ[1]);
  or or_1 (RAM_REQ, MEM_REQ[1], IF_REQ);
  and and_1 (and_1_out, mmu_registers_1_en_tlb, IF_REQ);
  and and_2 (and_2_out, mmu_registers_1_en_tlb, page_walker_1_write_i_tlb);
  MMU_Registers mmu_registers_1 (
    .Clk(Clk), .RST(RST), .W(W_Addr), .En_RegE(En_RegE), .E(E_Read), .Data_In(Data_From_CPU),
    .CR2_In(page_walker_1_cr2), .Exc(Exc), .Code(page_walker_1_code), .PCID_Out(mmu_registers_1_pcid_out),
    .CR3_Out(mmu_registers_1_cr3_out), .Flush_TLBs(mmu_registers_1_flush_tlbs),
    .En_MMU(mmu_registers_1_en_mmu), .En_TLB(mmu_registers_1_en_tlb), .Data_Out(Data_To_CPU));
  Page_Walker page_walker_1 (
    .Hit_d(tlb_lru_2_hit), .Hit_i(tlb_lru_1_hit), .En_MMU(mmu_registers_1_en_mmu), .IF_REQ(not_1_out),
    .REQ(RAM_REQ), .Clk(Clk), .RST(RST), .RST_for_INT(RST_for_INT), .Aling_Fault(Aling_Fault),
    .Stall_RAM(Stall_RAM), .MEM_REQ(MEM_REQ[1]), .CR3(mmu_registers_1_cr3_out), .MEM_Addr(MEM_Addr),
    .IF_Addr(IF_Addr), .Data_In(Data_In), .d_TLB(tlb_lru_2_phys_frame), .i_TLB(tlb_lru_1_phys_frame),
    .Write(MEM_REQ[0]), .Kernel(Kernel), .RAM_Ready(RAM_Ready), .TLB_Write(page_walker_1_tlb_write),
    .Write_d_TLB(page_walker_1_write_d_tlb), .Write_i_TLB(page_walker_1_write_i_tlb),
    .IF_Write(page_walker_1_if_write), .Addr(Addr), .Exc(Exc), .Code(page_walker_1_code),
    .CR2(page_walker_1_cr2), .STALL(STALL), .Final_Addr(Final_Addr));
  Bit_Extender #(.in_width(32), .out_width(2), .\type ("zero")) bit_extender_1 (.in(IF_Addr), .out(bit_extender_1_out));
  or or_2 (Aling_Fault, bit_extender_1_out[0], bit_extender_1_out[1]);
  TLB_LRU tlb_lru_1 (
    .clk(Clk), .reset(or_3_out), .lookup_en(and_1_out), .pcid(mmu_registers_1_pcid_out), .virt_addr(IF_Addr),
    .write_en(and_2_out), .write_phys(page_walker_1_tlb_write), .hit(tlb_lru_1_hit),
    .phys_frame(tlb_lru_1_phys_frame));
  or or_3 (or_3_out, mmu_registers_1_flush_tlbs, RST);
  and and_3 (and_3_out, mmu_registers_1_en_tlb, MEM_REQ[1]);
  and and_4 (and_4_out, mmu_registers_1_en_tlb, page_walker_1_write_d_tlb);
  TLB_LRU tlb_lru_2 (
    .clk(Clk), .reset(or_3_out), .lookup_en(and_3_out), .pcid(mmu_registers_1_pcid_out),
    .virt_addr(MEM_Addr), .write_en(and_4_out), .write_phys(page_walker_1_tlb_write), .hit(tlb_lru_2_hit),
    .phys_frame(tlb_lru_2_phys_frame));
  and and_5 (MEM_Write, Final_Addr, ~page_walker_1_if_write);  // AND_Gate
  and and_6 (IF_Write, Final_Addr, page_walker_1_if_write);
  Multiplexer #(.enable("true"), .width(32)) multiplexer_1 (
    .in0(32'h1), .in1(32'h2), .out(Code), .sel(Aling_Fault), .en(Exc));
  Multiplexer #(.width(2)) multiplexer_2 (.in0(2'b00), .in1(MEM_REQ), .out(RoW), .sel(Final_Addr));
  and and_7 (and_7_out, Final_Addr, RAM_REQ, MEM_REQ[0]);
  and and_8 (and_8_out, ~and_7_out, RAM_REQ);  // AND_Gate
  and and_9 (En_Write, ~Exc, and_7_out);  // AND_Gate
  and and_10 (En_Read, ~Exc, and_8_out);  // AND_Gate

  // Other names for the same wires on the sheet: MEM_REQ_En = MEM_REQ[1]; MEM_REQ_t = RAM_REQ
endmodule

module Page_Walker (
  input  [31:0] CR3,
  input  En_MMU,
  input  IF_REQ,
  input  REQ,
  input  [31:0] MEM_Addr,
  input  [31:0] IF_Addr,
  input  [31:0] Data_In,
  input  [31:0] d_TLB,
  input  [31:0] i_TLB,
  input  Write,
  input  Kernel,
  input  RAM_Ready,
  input  Clk,
  input  RST_for_INT,
  input  Hit_d,
  input  Aling_Fault,
  input  Hit_i,
  input  RST,
  input  Stall_RAM,
  input  MEM_REQ,
  output [31:0] TLB_Write,
  output [31:0] Addr,
  output [31:0] CR2,
  output Exc,
  output [15:0] Code,
  output Write_d_TLB,
  output Write_i_TLB,
  output IF_Write,
  output STALL,
  output Final_Addr
);

  wire and_1_out, and_2_out, and_3_out, and_4_out, and_6_out, and_7_out, and_8_out, and_9_out, and_11_out,
       and_12_out, and_13_out, and_15_out, Busy, Busy_RST, En_MMU_REQ, FG_exc, Hit, IF_REQ_t, not_1_out,
       or_1_out, or_3_out, or_4_out, or_5_out, or_7_out, or_9_out, Page_Controller_carry, REQ_t, RST_t,
       t_ff_1_q, t_ff_2_q;
  wire [1:0] Controller_out, multiplexer_8_out, Mux, Page_Controller_q;
  wire [19:0] FG_addr_out;
  wire [31:0] Memory_Data_Register_q, multiplexer_4_out, multiplexer_5_out, V_Addr;

  and and_1 (and_1_out, IF_REQ, ~Busy);  // AND_Gate
  and and_2 (and_2_out, t_ff_2_q, Busy_RST);
  and and_3 (and_3_out, REQ, ~Busy);  // AND_Gate
  T_Flip_Flop t_ff_1 (.T(and_4_out), .clk(Clk), .Q(t_ff_1_q), .reset(or_1_out), .preset(and_3_out));  // open: Qn
  and and_4 (and_4_out, Busy_RST, t_ff_1_q);
  T_Flip_Flop t_ff_2 (.T(and_2_out), .clk(Clk), .Q(t_ff_2_q), .reset(or_1_out), .preset(and_1_out));  // open: Qn
  or or_1 (or_1_out, not_1_out, RST_t);
  not not_1 (not_1_out, En_MMU);
  Multiplexer multiplexer_1 (.in0(IF_REQ), .in1(t_ff_2_q), .out(IF_REQ_t), .sel(En_MMU));
  Multiplexer multiplexer_2 (.in0(REQ), .in1(t_ff_1_q), .out(REQ_t), .sel(En_MMU));
  or or_2 (RST_t, RST_for_INT, RST);
  and and_5 (En_MMU_REQ, REQ_t, En_MMU);
  Multiplexer #(.enable("true"), .width(32)) multiplexer_3 (
    .in0(MEM_Addr), .in1(IF_Addr), .out(V_Addr), .sel(IF_REQ_t), .en(REQ_t));
  Register #(.width(32)) Memory_Data_Register (
    .D(Data_In), .Q(Memory_Data_Register_q), .clk(Clk), .clr(RST_t));  // open: en
  and and_6 (and_6_out, ~RAM_Ready, REQ_t);  // AND_Gate
  and and_7 (and_7_out, En_MMU, ~Hit, ~IF_REQ_t);  // AND_Gate
  and and_8 (and_8_out, RAM_Ready, En_MMU_REQ);
  and and_9 (and_9_out, and_8_out, ~Busy);  // AND_Gate
  Multiplexer #(.width(32)) multiplexer_4 (
    .in0(Memory_Data_Register_q), .in1(multiplexer_5_out), .out(multiplexer_4_out), .sel(Hit));
  Multiplexer #(.width(32)) multiplexer_5 (.in0(d_TLB), .in1(i_TLB), .out(multiplexer_5_out), .sel(IF_REQ_t));
  Counter #(.max('h2), .width(2)) Page_Controller (
    .count(and_8_out), .Q(Page_Controller_q), .carry(Page_Controller_carry), .clk(Clk), .clr(or_3_out));  // open: load, D, up
  or or_3 (or_3_out, RST_t, Hit);
  or or_4 (or_4_out, Page_Controller_carry, Hit);
  and and_10 (Busy_RST, or_4_out, Busy);
  PLA #(.\table ("01 01 # PTE\n10 10 # Addr\n11 10 # NOP")) Controller (.in(Mux), .out(Controller_out));
  Fault_Generator FG (
    .Write(Write), .Kernel(Kernel), .Instr(IF_REQ_t), .Clk(Clk), .RST(RST), .Sel(Mux),
    .Data_In(multiplexer_4_out), .Code(Code), .Addr_Out(FG_addr_out), .Exc(FG_exc));
  T_Flip_Flop u_Busy (.T(or_5_out), .clk(Clk), .Q(Busy), .reset(RST_t));  // open: Qn, preset
  or or_5 (or_5_out, Busy_RST, and_9_out);
  and and_11 (and_11_out, En_MMU, ~Controller_out[1], MEM_REQ);  // AND_Gate
  and and_12 (and_12_out, MEM_REQ, Busy, IF_REQ_t);
  or or_6 (Exc, FG_exc, Aling_Fault);
  Demultiplexer demultiplexer_1 (.out0(Write_d_TLB), .out1(Write_i_TLB), .in(Controller_out[0]), .sel(IF_REQ_t));
  and and_13 (and_13_out, ~Controller_out[1], and_7_out);  // AND_Gate
  Multiplexer #(.select(2), .width(32)) multiplexer_6 (
    .in0({CR3[31:12], V_Addr[31:22], 2'b00}), .in1({FG_addr_out, V_Addr[21:12], 2'b00}),
    .in2({FG_addr_out, V_Addr[11:0]}), .in3(V_Addr), .out(Addr), .sel(Mux));
  Multiplexer #(.width(2)) multiplexer_7 (.in0(2'b11), .in1(multiplexer_8_out), .out(Mux), .sel(En_MMU));
  Multiplexer #(.width(2)) multiplexer_8 (.in0(Page_Controller_q), .in1(2'b10), .out(multiplexer_8_out), .sel(Hit));
  Multiplexer #(.width(32)) multiplexer_9 (.in0({32{1'b0}}), .in1(V_Addr), .out(CR2), .sel(Exc));
  and and_14 (IF_Write, IF_REQ_t, Controller_out[1]);
  or or_7 (or_7_out, and_13_out, and_6_out, Stall_RAM);
  and and_15 (and_15_out, ~IF_Write, or_7_out);  // AND_Gate
  Multiplexer multiplexer_10 (.in0(Hit_d), .in1(Hit_i), .out(Hit), .sel(IF_REQ_t));
  or or_8 (STALL, Exc, or_9_out);
  or or_9 (or_9_out, and_15_out, and_11_out, and_12_out);
  and and_16 (Final_Addr, Controller_out[1], REQ_t, ~STALL, RAM_Ready);  // AND_Gate

  assign TLB_Write = Data_In;

  // Notes on the sheet:
  //   Busy System
  //   MAIN CONTROLLER
  //   Page Walker
  //   Busy Controller
endmodule

module Fault_Generator (
  input  [1:0] Sel,
  input  [31:0] Data_In,
  input  Write,
  input  Kernel,
  input  Instr,
  input  Clk,
  input  RST,
  output [19:0] Addr_Out,
  output Exc,
  output [15:0] Code
);

  wire Decoder_out, or_1_out;
  wire [1:0] Generator_out;
  wire [3:1] and_1_out;
  wire [14:0] bit_extender_1_out;

  PLA #(.out_width(1), .\table ("00 0 # None\n01 1 # PDE\n10 1 # PTE\n11 0 # None")) Decoder (
    .in(Sel), .out(Decoder_out));
  and and_1 (and_1_out[1], Data_In[1], Write);
  and and_2 (and_1_out[2], Data_In[2], ~Kernel);  // AND_Gate
  and and_3 (and_1_out[3], ~Data_In[4], Instr);  // AND_Gate
  PLA #(.in_width(4), .\table ("xxx0 00 # NP\nx1x1 01 # PV\nx011 10 # RO\n1xx1 11 # Exe")) Generator (
    .in({and_1_out, Data_In[0]}), .out(Generator_out));
  and and_4 (Exc, Decoder_out, or_1_out);
  or or_1 (or_1_out, ~Data_In[0], and_1_out[1], and_1_out[2], and_1_out[3]);  // OR_Gate
  assign bit_extender_1_out = {{13{1'b0}}, Generator_out};  // Bit_Extender bit_extender_1
  Register #(.width(16)) register_1 (.D({bit_extender_1_out, Instr}), .en(Exc), .Q(Code), .clk(Clk), .clr(RST));

  assign Addr_Out = Data_In[31:12];
endmodule

module MMU_Registers (
  input  [3:0] E,
  input  [31:0] Data_In,
  input  Clk,
  input  RST,
  input  [3:0] W,
  input  En_RegE,
  input  [31:0] CR2_In,
  input  Exc,
  input  [15:0] Code,
  output [31:0] Data_Out,
  output [31:0] PCID_Out,
  output [31:0] CR3_Out,
  output Flush_TLBs,
  output En_MMU,
  output En_TLB
);

  wire decoder_1_out3, decoder_1_out4, decoder_1_out6;
  wire [15:0] bit_extender_1_out;
  wire [15:2] CR0_q;
  wire [31:0] CR2_q, multiplexer_1_out, pull_resistor_1_node;

  Decoder #(.select(3)) decoder_1 (
    .out3(decoder_1_out3), .out4(decoder_1_out4), .out6(decoder_1_out6), .sel(W[2:0]), .en(En_RegE));  // open: out0, out1, out2, out5, out7
  Register #(.width(32)) PCID (.D(Data_In), .en(decoder_1_out3), .clk(Clk), .Q(PCID_Out), .clr(RST));
  Register #(.width(32)) CR3 (.D(Data_In), .en(decoder_1_out4), .clk(Clk), .Q(CR3_Out), .clr(RST));
  Register #(.width(32)) CR2 (.D(CR2_In), .en(Exc), .clk(Clk), .Q(CR2_q), .clr(RST));
  Multiplexer #(.width(32)) multiplexer_1 (
    .in0({32{1'b0}}), .in1(Data_In), .out(multiplexer_1_out), .sel(decoder_1_out6));
  Bit_Extender #(.in_width(32), .\type ("zero")) bit_extender_1 (
    .in(multiplexer_1_out), .out({bit_extender_1_out[15:3], Flush_TLBs, bit_extender_1_out[1:0]}));
  Register #(.width(16)) CR0 (
    .D({bit_extender_1_out[15:3], 1'b0, bit_extender_1_out[1:0]}), .en(decoder_1_out6), .clk(Clk),
    .Q({CR0_q, En_TLB, En_MMU}), .clr(RST));
  Pull_Resistor pull_resistor_1 (.node(pull_resistor_1_node));
  Multiplexer #(.select(3), .width(32)) multiplexer_2 (
    .in0(pull_resistor_1_node), .in1(pull_resistor_1_node), .in2(pull_resistor_1_node), .in3(PCID_Out),
    .in4(CR3_Out), .in5(CR2_q), .in6({Code, CR0_q, En_TLB, En_MMU}), .in7(pull_resistor_1_node),
    .out(Data_Out), .sel(E[2:0]));

  // Other names for the same wires on the sheet: Sel[2:0] = W[2:0]
endmodule

// VHDL entity TLB_LRU, as the project stores it:
-- =============================================================================
--  TLB_LRU.vhd
--  Translation Lookaside Buffer de 32 bits con reemplazo LRU
--  Optimizado para simulación en Logisim / GHDL
-- =============================================================================
--  ARQUITECTURA:
--    · Lookup COMBINACIONAL (asíncrono): responde sin esperar el clock,
--      ideal para simulación en Logisim.
--    · Escritura y actualización de edad LRU SÍNCRONA (flanco de subida).
--    · 64 entradas. Cada entrada guarda:
--        valid  (1 bit)
--        vpn    (20 bits, virt_addr[31:12])
--        pcid_k (8 bits,  pcid[7:0])
--        frame  (32 bits)
--        age    (6 bits, 0 = LRU, 63 = MRU)
--
--  POLÍTICA LRU (orden relativo siempre preservado):
--    · En HIT  → sea A = age[hit_idx] ANTES de promover.
--                age[hit_idx] = MAX
--                age[i]-- SOLO si age[i] > A   ← clave: no tocar entradas
--                                                  ya más viejas que hit
--    · En WRITE → sea A = age[víctima] ANTES de reemplazar.
--                 se inserta con age = MAX
--                 age[i]-- SOLO si valid[i] AND age[i] > A
--    · Prioridad: write_en > lookup hit (si ambas llegan al mismo ciclo)
--
--  ¿Por qué? Si decrementaras TODAS las entradas en cada hit, después de
--  suficientes hits en la misma entrada todas las demás llegarían a 0 y
--  perderías el orden relativo entre ellas (empate masivo en LRU).
-- =============================================================================

library IEEE;
use IEEE.STD_LOGIC_1164.ALL;
use IEEE.NUMERIC_STD.ALL;

entity TLB_LRU is
    Generic (
        -- Parámetros: 64 entradas (puedes ajustar)
        NUM_ENTRIES   : integer := 64;  -- 64 entradas en la TLB

        -- Reducimos la comparación a VPN y PCID pequeño (más realista)
        VPN_HIGH      : integer := 31;
        VPN_LOW       : integer := 12;  -- página de 4 KB → 20 bits de VPN
        PCID_LOW_BITS : integer := 7    -- usamos 8 bits de PCID (bits 7..0)
    );
    Port (
        clk           : in  STD_LOGIC;
        reset         : in  STD_LOGIC;

        -- Búsqueda (ASÍNCRONA combinacional para simulación / Logisim)
        lookup_en     : in  STD_LOGIC;                      -- Habilitar búsqueda
        pcid          : in  STD_LOGIC_VECTOR(31 downto 0);  -- Process-Context ID
        virt_addr     : in  STD_LOGIC_VECTOR(31 downto 0);  -- Dirección virtual (32 bits)
        hit           : out STD_LOGIC;                      -- '1' si encontró
        phys_frame    : out STD_LOGIC_VECTOR(31 downto 0);  -- Marco físico (32 bits)

        -- Escritura (SÍNCRONA con reemplazo LRU automático)
        write_en      : in  STD_LOGIC;                      -- Habilitar escritura
        write_phys    : in  STD_LOGIC_VECTOR(31 downto 0)   -- Marco físico a insertar
    );
end TLB_LRU;

architecture Behavioral of TLB_LRU is

    -- -------------------------------------------------------------------------
    -- Constantes derivadas
    -- -------------------------------------------------------------------------
    constant VPN_BITS  : integer := VPN_HIGH - VPN_LOW + 1;  -- 20
    constant PCID_BITS : integer := PCID_LOW_BITS + 1;        -- 8  (bits 7..0)
    constant AGE_BITS  : integer := 4;                        -- log2(64) = 6
    constant MAX_AGE   : integer := NUM_ENTRIES - 1;          -- 63

    -- -------------------------------------------------------------------------
    -- Tipos de arrays para la tabla TLB
    -- -------------------------------------------------------------------------
    type t_vpn   is array(0 to NUM_ENTRIES-1) of std_logic_vector(VPN_BITS-1  downto 0);
    type t_pcid  is array(0 to NUM_ENTRIES-1) of std_logic_vector(PCID_BITS-1 downto 0);
    type t_frame is array(0 to NUM_ENTRIES-1) of std_logic_vector(31 downto 0);
    type t_age   is array(0 to NUM_ENTRIES-1) of unsigned(AGE_BITS-1 downto 0);
    type t_valid is array(0 to NUM_ENTRIES-1) of std_logic;

    -- -------------------------------------------------------------------------
    -- Registros de la TLB
    -- -------------------------------------------------------------------------
    signal tlb_valid : t_valid;
    signal tlb_vpn   : t_vpn;
    signal tlb_pcid  : t_pcid;
    signal tlb_frame : t_frame;
    signal tlb_age   : t_age;

    -- -------------------------------------------------------------------------
    -- Señales de resultado del bloque combinacional
    -- (leídas por el bloque síncrono para actualizar la edad en HIT)
    -- -------------------------------------------------------------------------
    signal s_hit_found : std_logic;
    signal s_hit_idx   : integer range 0 to NUM_ENTRIES-1;

begin

    -- =========================================================================
    -- BLOQUE 1: Lookup combinacional (asíncrono)
    -- =========================================================================
    -- Responde en el mismo ciclo de simulación sin esperar un flanco de clock.
    -- Recorre todas las entradas en paralelo (síntesis) o en delta-cycles
    -- (simulación) y devuelve hit + phys_frame.
    -- También actualiza las señales internas s_hit_found / s_hit_idx que
    -- serán leídas por el bloque síncrono para el aging LRU en hit.
    -- =========================================================================
    comb_lookup : process(lookup_en, virt_addr, pcid,
                          tlb_valid, tlb_vpn, tlb_pcid, tlb_frame)
        variable v_vpn   : std_logic_vector(VPN_BITS-1  downto 0);
        variable v_pcid  : std_logic_vector(PCID_BITS-1 downto 0);
        variable v_found : std_logic;
        variable v_frame : std_logic_vector(31 downto 0);
        variable v_idx   : integer range 0 to NUM_ENTRIES-1;
    begin
        -- Extraer campos de comparación
        v_vpn  := virt_addr(VPN_HIGH downto VPN_LOW);
        v_pcid := pcid(PCID_LOW_BITS downto 0);

        -- Valores por defecto (miss)
        v_found := '0';
        v_frame := (others => '0');
        v_idx   := 0;

        -- Recorrido de las 64 entradas (en síntesis: lógica paralela)
        if lookup_en = '1' then
            for i in 0 to NUM_ENTRIES-1 loop
                if tlb_valid(i) = '1'
                   and tlb_vpn(i)  = v_vpn
                   and (tlb_pcid(i) = v_pcid or tlb_frame(i)(3) = '1')
                then
                    v_found := '1';
                    v_frame := tlb_frame(i);
                    v_idx   := i;
                    -- No hay break en VHDL; si hubiera dos hits (no debería)
                    -- el último índice gana. En una TLB correcta no hay duplicados.
                end if;
            end loop;
        end if;

        -- Salidas principales
        hit        <= v_found;
        phys_frame <= v_frame;

        -- Señales internas para el bloque síncrono
        s_hit_found <= v_found;
        s_hit_idx   <= v_idx;
    end process comb_lookup;


    -- =========================================================================
    -- BLOQUE 2: Actualización síncrona de la TLB y política LRU
    -- =========================================================================
    -- En cada flanco de subida de clk:
    --   · reset  → invalida todo
    --   · write_en = '1' → inserta nueva entrada con LRU replacement
    --   · write_en = '0' y hit = '1' → promueve la entrada a MRU
    -- Prioridad: write_en > hit (si llegan juntos, se procesa la escritura).
    -- =========================================================================
    sync_tlb : process(clk)
        variable v_vpn        : std_logic_vector(VPN_BITS-1  downto 0);
        variable v_pcid_w     : std_logic_vector(PCID_BITS-1 downto 0);
        variable v_target     : integer range 0 to NUM_ENTRIES-1;
        variable v_lru_idx    : integer range 0 to NUM_ENTRIES-1;
        variable v_min_age    : unsigned(AGE_BITS-1 downto 0);
        variable v_free_found : boolean;
        variable v_free_idx   : integer range 0 to NUM_ENTRIES-1;
        -- Captura la edad de la víctima/hit ANTES de sobreescribirla,
        -- necesaria para el decremento selectivo correcto.
        variable v_victim_age : unsigned(AGE_BITS-1 downto 0);
    begin
        if rising_edge(clk) then

            -- -----------------------------------------------------------------
            -- Reset: invalida toda la tabla y pone las edades a 0
            -- -----------------------------------------------------------------
            if reset = '1' then
                for i in 0 to NUM_ENTRIES-1 loop
                    tlb_valid(i) <= '0';
                    tlb_age(i)   <= (others => '0');
                end loop;

            -- -----------------------------------------------------------------
            -- Escritura con reemplazo LRU
            -- -----------------------------------------------------------------
            elsif write_en = '1' then
                v_vpn    := virt_addr(VPN_HIGH downto VPN_LOW);
                v_pcid_w := pcid(PCID_LOW_BITS downto 0);

                -- Paso 1: Buscar entrada libre (inválida) o la de menor edad
                v_free_found := false;
                v_free_idx   := 0;
                v_min_age    := (others => '1');  -- inicializar al máximo
                v_lru_idx    := 0;

                for i in 0 to NUM_ENTRIES-1 loop
                    -- Primera entrada inválida encontrada = candidata gratis
                    if tlb_valid(i) = '0' and not v_free_found then
                        v_free_found := true;
                        v_free_idx   := i;
                    end if;
                    -- Mínima edad (LRU real)
                    if tlb_age(i) < v_min_age then
                        v_min_age := tlb_age(i);
                        v_lru_idx := i;
                    end if;
                end loop;

                -- Paso 2: Elegir víctima y capturar su edad actual
                if v_free_found then
                    v_target     := v_free_idx;
                    v_victim_age := tlb_age(v_free_idx); -- 0 si era inválida
                else
                    v_target     := v_lru_idx;
                    v_victim_age := v_min_age;            -- edad LRU real
                end if;

                -- Paso 3: Insertar la nueva entrada como MRU
                tlb_vpn(v_target)   <= v_vpn;
                tlb_pcid(v_target)  <= v_pcid_w;
                tlb_frame(v_target) <= write_phys;
                tlb_valid(v_target) <= '1';
                tlb_age(v_target)   <= to_unsigned(MAX_AGE, AGE_BITS);

                -- Paso 4: Decrementar SOLO las entradas más recientes que la víctima.
                --   Invariante: si age[i] <= v_victim_age, esas entradas ya eran
                --   más viejas que la víctima y no deben cambiar su posición relativa.
                for i in 0 to NUM_ENTRIES-1 loop
                    if i /= v_target then
                        if tlb_valid(i) = '1' and tlb_age(i) > v_victim_age then
                            tlb_age(i) <= tlb_age(i) - 1;
                        end if;
                    end if;
                end loop;

            -- -----------------------------------------------------------------
            -- Hit: promover la entrada encontrada a MRU.
            -- CORRECCIÓN LRU: solo decrementan las entradas cuya edad sea
            -- MAYOR que la edad actual de la entrada en hit.  Las entradas
            -- que ya eran más viejas que hit conservan su posición relativa.
            -- -----------------------------------------------------------------
            elsif lookup_en = '1' and s_hit_found = '1' then
                -- Capturar la edad actual del hit (antes de promoverla)
                v_victim_age := tlb_age(s_hit_idx);

                for i in 0 to NUM_ENTRIES-1 loop
                    if i = s_hit_idx then
                        -- Entrada accedida → MRU
                        tlb_age(i) <= to_unsigned(MAX_AGE, AGE_BITS);
                    elsif tlb_valid(i) = '1' and tlb_age(i) > v_victim_age then
                        -- Solo las entradas más recientes que hit pierden un puesto
                        tlb_age(i) <= tlb_age(i) - 1;
                        -- Las entradas con age <= v_victim_age ya eran más viejas
                        -- que hit: su orden relativo entre sí no debe cambiar.
                    end if;
                end loop;
            end if;

        end if;
    end process sync_tlb;

end Behavioral;

-- =============================================================================
-- NOTAS DE USO
-- =============================================================================
--
--  1. LOOKUP (asíncrono):
--       · Pon lookup_en = '1', virt_addr y pcid en los pines.
--       · hit y phys_frame responden sin esperar el clock.
--       · La actualización LRU del hit se efectúa en el siguiente flanco.
--
--  2. ESCRITURA (síncrona):
--       · Pon write_en = '1', virt_addr, pcid y write_phys en los pines.
--       · La inserción y el reemplazo LRU ocurren en el flanco de subida.
--       · write_en tiene prioridad sobre lookup_en si llegan juntos.
--
--  3. RESET:
--       · reset = '1' (síncrono) invalida todas las entradas en el
--         siguiente flanco de subida.
--
--  4. AJUSTE DE TAMAÑO:
--       · Para una TLB más pequeña (y más rápida en Logisim) baja
--         NUM_ENTRIES a 16 o 32.
--       · Ajusta AGE_BITS = ceil(log2(NUM_ENTRIES)):
--           16 entradas → AGE_BITS = 4
--           32 entradas → AGE_BITS = 5
--           64 entradas → AGE_BITS = 6  (valor actual)
--
--  5. LOGISIM:
--       · Compila con GHDL y exporta el netlist.
--       · El loop de 64 entradas genera lógica paralela; si el simulador
--         va lento, reduce NUM_ENTRIES a 16 y ajusta AGE_BITS.
-- =============================================================================
