// Logisim project MEM_V1.circ as structural Verilog
module MMU (
  input  RST,
  input  Clk,
  input  From_PC,
  input  [31:0] Virtual_Addr_PC,
  input  [31:0] Data_In,
  input  [1:0] From_Ex,
  input  [31:0] Virtual_Addr_ALU,
  input  RAM_Ready,
  input  [31:0] RegE_In,
  input  [3:0] W,
  input  Stall_RAM,
  input  En_RegE,
  input  Kernel,
  input  [3:0] E,
  output [31:0] Addr_Out,
  output [1:0] RoW,
  output MEM_REQ,
  output W_En,
  output Read_En,
  output IF_Ready,
  output Stall,
  output Final_Addr,
  output Exception,
  output [31:0] Excep_Code,
  output [31:0] RegE_Out
);

  wire Alignment_Fault, and_1_out, and_4_out, dTLB_hit, iTLB_hit, mmu_controller_1_en_dtlb,
       mmu_controller_1_en_excep, mmu_controller_1_en_itlb, mmu_controller_1_en_mmu, mmu_controller_1_mux,
       mmu_controller_1_mux_pw, mmu_controller_1_stall, or_2_out, or_3_out;
  wire [1:0] bit_extender_1_out, mmu_controller_1_en_mmu_mux, mmu_controller_1_pw_controler;
  wire [2:0] plarom_1_p3;
  wire [31:0] adder_1_out, adder_2_out, adder_3_out, bit_extender_2_out, bit_extender_3_out,
       bit_extender_4_out, CR0, CR2_Reg_q, CR3, dTLB_phys_frame, exception_generator_mmu_1_adress_out,
       From_TLBs, iTLB_phys_frame, Memory_Address_Register_q, multiplexer_1_out, multiplexer_4_out,
       multiplexer_5_out, multiplier_1_out, multiplier_2_out, PCID, pull_resistor_2_node;

  // PlaRom #(.Contents("1 1 2 2 1 2 1*3 2 2 1 0 0 1 0 1 0 1 0 0"), .Select("high"), .\and (3), .outputs(3)) plarom_1: pin names not known; wires that end beside it: W, En_RegE, plarom_1_p3
  Pull_Resistor pull_resistor_1 (.node(plarom_1_p3));
  Register #(.width(32)) Memory_Address_Register (
    .D(Data_In), .en(From_Ex[1]), .Q(Memory_Address_Register_q), .clk(Clk), .clr(RST));
  Register #(.width(32)) PCID_Reg (.D(RegE_In), .en(plarom_1_p3[0]), .Q(PCID), .clk(Clk), .clr(RST));
  Register #(.width(32)) CR3_Reg (.D(RegE_In), .en(plarom_1_p3[1]), .Q(CR3), .clk(Clk), .clr(RST));
  Register #(.width(32)) u_CR0 (.D(RegE_In), .en(plarom_1_p3[2]), .Q(CR0), .clk(Clk), .clr(RST));
  Bit_Extender #(.in_width(32), .out_width(2), .\type ("zero")) bit_extender_1 (
    .in(Virtual_Addr_PC), .out(bit_extender_1_out));
  Multiplexer #(.width(32)) multiplexer_1 (
    .in0(Virtual_Addr_ALU), .in1(Virtual_Addr_PC), .out(multiplexer_1_out), .sel(mmu_controller_1_mux_pw));
  Pull_Resistor pull_resistor_2 (.node(pull_resistor_2_node));
  or or_1 (Alignment_Fault, bit_extender_1_out[0], bit_extender_1_out[1]);
  assign bit_extender_2_out = {{22{1'b0}}, multiplexer_1_out[31:22]};  // Bit_Extender bit_extender_2
  assign bit_extender_3_out = {{22{1'b0}}, multiplexer_1_out[21:12]};  // Bit_Extender bit_extender_3
  assign bit_extender_4_out = {{20{1'b0}}, multiplexer_1_out[11:0]};  // Bit_Extender bit_extender_4
  Register #(.width(32)) CR2_Reg (.D(multiplexer_1_out), .Q(CR2_Reg_q), .clk(Clk), .clr(RST));  // open: en
  TLB_LRU iTLB (
    .clk(Clk), .reset(RST), .lookup_en(From_PC), .pcid(PCID), .virt_addr(Virtual_Addr_PC),
    .write_en(mmu_controller_1_en_itlb), .write_phys(Memory_Address_Register_q), .hit(iTLB_hit),
    .phys_frame(iTLB_phys_frame));
  Adder #(.width(32)) adder_1 (.a(CR3), .b(multiplier_1_out), .out(adder_1_out));  // open: cin, cout
  Multiplier #(.width(32)) multiplier_1 (.a(bit_extender_2_out), .b(32'h4), .out(multiplier_1_out));  // open: cin, cout
  Multiplier #(.width(32)) multiplier_2 (.a(bit_extender_3_out), .b(32'h4), .out(multiplier_2_out));  // open: cin, cout
  Multiplexer #(.select(4), .width(32)) multiplexer_2 (
    .in0(pull_resistor_2_node), .in1(pull_resistor_2_node), .in2(pull_resistor_2_node), .in3(PCID),
    .in4(CR3), .in5(CR2_Reg_q), .in6(CR0), .in7(pull_resistor_2_node), .in8(pull_resistor_2_node),
    .in9(pull_resistor_2_node), .in10(pull_resistor_2_node), .in11(pull_resistor_2_node),
    .in12(pull_resistor_2_node), .in13(pull_resistor_2_node), .in14(pull_resistor_2_node),
    .in15(pull_resistor_2_node), .out(RegE_Out), .sel(E));
  or or_2 (or_2_out, From_PC, From_Ex[1]);
  and and_1 (and_1_out, From_Ex[0], Final_Addr);
  and and_2 (W_En, or_2_out, and_1_out);
  and and_3 (Read_En, or_2_out, ~and_1_out);  // AND_Gate
  TLB_LRU dTLB (
    .clk(Clk), .reset(RST), .lookup_en(From_Ex[1]), .pcid(PCID), .virt_addr(Virtual_Addr_ALU),
    .write_en(mmu_controller_1_en_dtlb), .write_phys(Memory_Address_Register_q), .hit(dTLB_hit),
    .phys_frame(dTLB_phys_frame));
  Multiplexer #(.enable("true"), .width(32)) multiplexer_3 (
    .in0(dTLB_phys_frame), .in1(iTLB_phys_frame), .out(From_TLBs), .sel(mmu_controller_1_mux), .en(or_3_out));
  or or_3 (or_3_out, dTLB_hit, iTLB_hit);
  Pull_Resistor pull_resistor_3 (.node(iTLB_hit));
  Pull_Resistor pull_resistor_4 (.node(dTLB_hit));
  Pull_Resistor pull_resistor_5 (.node(Read_En));
  Pull_Resistor pull_resistor_6 (.node(W_En));
  MMU_Controller mmu_controller_1 (
    .Hit_iTLB(iTLB_hit), .From_PC(From_PC), .From_Ex(From_Ex[1]), .Hit_dTLB(dTLB_hit), .RAM_Ready(RAM_Ready),
    .Clk(Clk), .RST(RST), .CR0(CR0), .Fault(Exception), .IF_Ready(IF_Ready), .Stall(mmu_controller_1_stall),
    .Addr_On(Final_Addr), .PW_Controler(mmu_controller_1_pw_controler), .En_Excep(mmu_controller_1_en_excep),
    .En_MMU_Mux(mmu_controller_1_en_mmu_mux), .En_MMU(mmu_controller_1_en_mmu), .Mux(mmu_controller_1_mux),
    .Mux_PW(mmu_controller_1_mux_pw), .En_iTLB(mmu_controller_1_en_itlb), .En_dTLB(mmu_controller_1_en_dtlb));
  Multiplexer #(.width(32)) multiplexer_4 (
    .in0(Memory_Address_Register_q), .in1(From_TLBs), .out(multiplexer_4_out), .sel(mmu_controller_1_mux));
  Exception_Generator_MMU exception_generator_mmu_1 (
    .RoW(From_Ex), .Kernel(Kernel), .En_MMU(mmu_controller_1_en_mmu), .En_Excep(mmu_controller_1_en_excep),
    .Final_Addr(Final_Addr), .Alignment_Fault(Alignment_Fault), .Adress_In(multiplexer_4_out),
    .Adress_Out(exception_generator_mmu_1_adress_out), .Excep_Code(Excep_Code), .Exception(Exception));
  Adder #(.width(32)) adder_2 (
    .a(Memory_Address_Register_q), .b(multiplier_2_out), .out(adder_2_out));  // open: cin, cout
  Adder #(.width(32)) adder_3 (
    .a(bit_extender_4_out), .b(exception_generator_mmu_1_adress_out), .out(adder_3_out));  // open: cin, cout
  Multiplexer #(.select(2), .width(32)) multiplexer_5 (
    .in0(adder_3_out), .in1(adder_1_out), .in2(adder_2_out), .in3(adder_3_out), .out(multiplexer_5_out),
    .sel(mmu_controller_1_pw_controler));
  Multiplexer #(.select(2), .width(32)) multiplexer_6 (
    .in0(multiplexer_5_out), .in1(Virtual_Addr_ALU), .in2(Virtual_Addr_PC), .out(Addr_Out),
    .sel(mmu_controller_1_en_mmu_mux));  // open: in3
  or or_4 (MEM_REQ, Read_En, W_En);
  and and_4 (and_4_out, Stall_RAM, MEM_REQ);
  or or_5 (Stall, mmu_controller_1_stall, and_4_out);

  assign RoW = From_Ex;
endmodule

module MMU_Controller (
  input  Fault,
  input  Hit_iTLB,
  input  From_PC,
  input  From_Ex,
  input  Hit_dTLB,
  input  RAM_Ready,
  input  Clk,
  input  RST,
  input  [31:0] CR0,
  output Mux,
  output Mux_PW,
  output En_iTLB,
  output En_dTLB,
  output IF_Ready,
  output Stall,
  output Addr_On,
  output [1:0] PW_Controler,
  output En_Excep,
  output [1:0] En_MMU_Mux,
  output En_MMU
);

  wire and_3_out, and_4_out, d_ff_1_q, d_ff_2_q, or_1_out, or_2_out, or_3_out;
  wire [1:0] counter_1_q, pla_2_out;
  wire [3:0] and_1_out;
  wire [4:1] pla_1_out;
  wire [7:1] bit_extender_1_out;

  and and_1 (and_1_out[0], Hit_iTLB, bit_extender_1_out[1]);
  and and_2 (and_1_out[3], bit_extender_1_out[1], Hit_dTLB);
  Bit_Extender #(.in_width(32), .out_width(8), .\type ("zero")) bit_extender_1 (
    .in(CR0), .out({bit_extender_1_out, En_MMU}));
  or or_1 (or_1_out, and_1_out[3], and_1_out[0]);
  PLA #(.in_width(4), .out_width(5), .\table ("0000 00000 # N Hit\n0011 00101 # PHit\n1100 00000 # EHit\n1111 00000 # BHit\n0100 10010 # NHit_E\n0010 01110 # NHit_P\n0110 10010 # NHit_B")) pla_1 (
    .in({and_1_out[3], From_Ex, From_PC, and_1_out[0]}), .out({pla_1_out[4:3], Mux_PW, pla_1_out[1], Mux}));
  D_Flip_Flop d_ff_1 (.clk(Clk), .D(From_PC), .Q(d_ff_1_q), .reset(From_Ex));  // open: Qn, preset
  D_Flip_Flop d_ff_2 (.D(pla_2_out[1]), .clk(Clk), .Q(d_ff_2_q), .reset(d_ff_2_q));  // open: Qn, preset
  and and_3 (and_3_out, d_ff_1_q, RAM_Ready);
  and and_4 (and_4_out, RAM_Ready, Clk);
  PLA #(.out_width(3), .\table ("01 100 # PDE\n10 101 # PTE\n11 110 # Addr")) pla_2 (
    .in(counter_1_q), .out({En_Excep, pla_2_out}));
  Counter #(.max('h3), .width(2)) counter_1 (
    .load(or_1_out), .D(2'b11), .count(pla_1_out[1]), .Q(counter_1_q), .clk(and_4_out), .clr(or_2_out));  // open: carry, up
  or or_2 (or_2_out, d_ff_2_q, RST);
  and and_5 (En_iTLB, pla_1_out[3], bit_extender_1_out[1], pla_2_out[0]);
  and and_6 (En_dTLB, pla_1_out[4], bit_extender_1_out[1], pla_2_out[0]);
  Multiplexer #(.width(2)) multiplexer_1 (.in0(2'b00), .in1(counter_1_q), .out(PW_Controler), .sel(pla_1_out[1]));
  or or_3 (or_3_out, pla_2_out[1], ~En_MMU);  // OR_Gate
  and and_7 (IF_Ready, or_3_out, and_3_out);
  PLA #(.\table ("00 01 # MEM\n01 10 # IF\n1x 00 # En")) pla_3 (.in({En_MMU, Mux_PW}), .out(En_MMU_Mux));
  and and_8 (Stall, ~Fault, En_MMU, pla_1_out[1], ~pla_2_out[1]);  // AND_Gate
  or or_4 (Addr_On, pla_2_out[1], ~En_MMU);  // OR_Gate

  // Notes on the sheet:
  //   En_MMU
  //   En_TLBs
  //   Control Mux to Enable and Desable MMU
endmodule

module Exception_Generator_MMU (
  input  [31:0] Adress_In,
  input  [1:0] RoW,
  input  Kernel,
  input  En_MMU,
  input  En_Excep,
  input  Final_Addr,
  input  Alignment_Fault,
  output [31:0] Adress_Out,
  output [31:0] Excep_Code,
  output Exception
);

  wire and_1_out, and_2_out, or_1_out, pla_1_out, pla_2_out;
  wire [1:0] multiplexer_1_out;
  wire [7:0] bit_extender_2_out;
  wire [31:0] bit_extender_1_out, bit_extender_3_out, multiplexer_2_out, pull_resistor_1_node;

  assign bit_extender_1_out = {{12{1'b0}}, Adress_In[31:12]};  // Bit_Extender bit_extender_1
  Shifter #(.width(32)) shifter_1 (.in(bit_extender_1_out), .\dist (5'b01100), .out(Adress_Out));
  PLA #(.in_width(9), .out_width(1), .\table ("xxxxxxxx0 1 # NoP\n1xxxxxx11 1 # ROnly")) pla_1 (
    .in({RoW[0], bit_extender_2_out}), .out(pla_1_out));
  Bit_Extender #(.in_width(12), .out_width(8), .\type ("zero")) bit_extender_2 (
    .in(Adress_In[11:0]), .out(bit_extender_2_out));
  PLA #(.in_width(9), .out_width(1), .\table ("xxxxxx1x1 1 # KOnly")) pla_2 (
    .in({RoW[0], bit_extender_2_out}), .out(pla_2_out));
  or or_1 (or_1_out, pla_1_out, and_1_out);
  and and_1 (and_1_out, pla_2_out, ~Kernel);  // AND_Gate
  assign bit_extender_3_out = {{30{1'b0}}, multiplexer_1_out};  // Bit_Extender bit_extender_3
  Multiplexer #(.enable("true"), .width(2)) multiplexer_1 (
    .in0(2'b01), .in1(2'b10), .out(multiplexer_1_out), .sel(RoW[0]), .en(or_1_out));
  Multiplexer #(.width(32)) multiplexer_2 (
    .in0(bit_extender_3_out), .in1(32'h6), .out(multiplexer_2_out), .sel(Alignment_Fault));
  and and_2 (and_2_out, or_1_out, RoW[1], En_MMU, En_Excep, ~Final_Addr);  // AND_Gate
  Pull_Resistor pull_resistor_1 (.node(pull_resistor_1_node));
  Multiplexer #(.width(32)) multiplexer_3 (
    .in0(pull_resistor_1_node), .in1(multiplexer_2_out), .out(Excep_Code), .sel(Exception));
  or or_2 (Exception, and_2_out, Alignment_Fault);
endmodule

// VHDL entity TLB_LRU, as the project stores it:
-- =============================================================================
--  TLB_LRU.vhd
--  Translation Lookaside Buffer de 32 bits con reemplazo LRU
--  Optimizado para simulación en Logisim / GHDL
-- =============================================================================
--  ARQUITECTURA:
--    · Lookup COMBINACIONAL (asíncrono): responde sin esperar el clock,
--      ideal para simulación en Logisim.
--    · Escritura y actualización de edad LRU SÍNCRONA (flanco de subida).
--    · 64 entradas. Cada entrada guarda:
--        valid  (1 bit)
--        vpn    (20 bits, virt_addr[31:12])
--        pcid_k (8 bits,  pcid[7:0])
--        frame  (32 bits)
--        age    (6 bits, 0 = LRU, 63 = MRU)
--
--  POLÍTICA LRU (orden relativo siempre preservado):
--    · En HIT  → sea A = age[hit_idx] ANTES de promover.
--                age[hit_idx] = MAX
--                age[i]-- SOLO si age[i] > A   ← clave: no tocar entradas
--                                                  ya más viejas que hit
--    · En WRITE → sea A = age[víctima] ANTES de reemplazar.
--                 se inserta con age = MAX
--                 age[i]-- SOLO si valid[i] AND age[i] > A
--    · Prioridad: write_en > lookup hit (si ambas llegan al mismo ciclo)
--
--  ¿Por qué? Si decrementaras TODAS las entradas en cada hit, después de
--  suficientes hits en la misma entrada todas las demás llegarían a 0 y
--  perderías el orden relativo entre ellas (empate masivo en LRU).
-- =============================================================================

library IEEE;
use IEEE.STD_LOGIC_1164.ALL;
use IEEE.NUMERIC_STD.ALL;

entity TLB_LRU is
    Generic (
        -- Parámetros: 64 entradas (puedes ajustar)
        NUM_ENTRIES   : integer := 64;  -- 64 entradas en la TLB

        -- Reducimos la comparación a VPN y PCID pequeño (más realista)
        VPN_HIGH      : integer := 31;
        VPN_LOW       : integer := 12;  -- página de 4 KB → 20 bits de VPN
        PCID_LOW_BITS : integer := 7    -- usamos 8 bits de PCID (bits 7..0)
    );
    Port (
        clk           : in  STD_LOGIC;
        reset         : in  STD_LOGIC;

        -- Búsqueda (ASÍNCRONA combinacional para simulación / Logisim)
        lookup_en     : in  STD_LOGIC;                      -- Habilitar búsqueda
        pcid          : in  STD_LOGIC_VECTOR(31 downto 0);  -- Process-Context ID
        virt_addr     : in  STD_LOGIC_VECTOR(31 downto 0);  -- Dirección virtual (32 bits)
        hit           : out STD_LOGIC;                      -- '1' si encontró
        phys_frame    : out STD_LOGIC_VECTOR(31 downto 0);  -- Marco físico (32 bits)

        -- Escritura (SÍNCRONA con reemplazo LRU automático)
        write_en      : in  STD_LOGIC;                      -- Habilitar escritura
        write_phys    : in  STD_LOGIC_VECTOR(31 downto 0)   -- Marco físico a insertar
    );
end TLB_LRU;

architecture Behavioral of TLB_LRU is

    -- -------------------------------------------------------------------------
    -- Constantes derivadas
    -- -------------------------------------------------------------------------
    constant VPN_BITS  : integer := VPN_HIGH - VPN_LOW + 1;  -- 20
    constant PCID_BITS : integer := PCID_LOW_BITS + 1;        -- 8  (bits 7..0)
    constant AGE_BITS  : integer := 6;                        -- log2(64) = 6
    constant MAX_AGE   : integer := NUM_ENTRIES - 1;          -- 63

    -- -------------------------------------------------------------------------
    -- Tipos de arrays para la tabla TLB
    -- -------------------------------------------------------------------------
    type t_vpn   is array(0 to NUM_ENTRIES-1) of std_logic_vector(VPN_BITS-1  downto 0);
    type t_pcid  is array(0 to NUM_ENTRIES-1) of std_logic_vector(PCID_BITS-1 downto 0);
    type t_frame is array(0 to NUM_ENTRIES-1) of std_logic_vector(31 downto 0);
    type t_age   is array(0 to NUM_ENTRIES-1) of unsigned(AGE_BITS-1 downto 0);
    type t_valid is array(0 to NUM_ENTRIES-1) of std_logic;

    -- -------------------------------------------------------------------------
    -- Registros de la TLB
    -- -------------------------------------------------------------------------
    signal tlb_valid : t_valid;
    signal tlb_vpn   : t_vpn;
    signal tlb_pcid  : t_pcid;
    signal tlb_frame : t_frame;
    signal tlb_age   : t_age;

    -- -------------------------------------------------------------------------
    -- Señales de resultado del bloque combinacional
    -- (leídas por el bloque síncrono para actualizar la edad en HIT)
    -- -------------------------------------------------------------------------
    signal s_hit_found : std_logic;
    signal s_hit_idx   : integer range 0 to NUM_ENTRIES-1;

begin

    -- =========================================================================
    -- BLOQUE 1: Lookup combinacional (asíncrono)
    -- =========================================================================
    -- Responde en el mismo ciclo de simulación sin esperar un flanco de clock.
    -- Recorre todas las entradas en paralelo (síntesis) o en delta-cycles
    -- (simulación) y devuelve hit + phys_frame.
    -- También actualiza las señales internas s_hit_found / s_hit_idx que
    -- serán leídas por el bloque síncrono para el aging LRU en hit.
    -- =========================================================================
    comb_lookup : process(lookup_en, virt_addr, pcid,
                          tlb_valid, tlb_vpn, tlb_pcid, tlb_frame)
        variable v_vpn   : std_logic_vector(VPN_BITS-1  downto 0);
        variable v_pcid  : std_logic_vector(PCID_BITS-1 downto 0);
        variable v_found : std_logic;
        variable v_frame : std_logic_vector(31 downto 0);
        variable v_idx   : integer range 0 to NUM_ENTRIES-1;
    begin
        -- Extraer campos de comparación
        v_vpn  := virt_addr(VPN_HIGH downto VPN_LOW);
        v_pcid := pcid(PCID_LOW_BITS downto 0);

        -- Valores por defecto (miss)
        v_found := '0';
        v_frame := (others => '0');
        v_idx   := 0;

        -- Recorrido de las 64 entradas (en síntesis: lógica paralela)
        if lookup_en = '1' then
            for i in 0 to NUM_ENTRIES-1 loop
                if tlb_valid(i) = '1'
                   and tlb_vpn(i)  = v_vpn
                   and (tlb_pcid(i) = v_pcid or tlb_frame(i)(3) = '1')
                then
                    v_found := '1';
                    v_frame := tlb_frame(i);
                    v_idx   := i;
                    -- No hay break en VHDL; si hubiera dos hits (no debería)
                    -- el último índice gana. En una TLB correcta no hay duplicados.
                end if;
            end loop;
        end if;

        -- Salidas principales
        hit        <= v_found;
        phys_frame <= v_frame;

        -- Señales internas para el bloque síncrono
        s_hit_found <= v_found;
        s_hit_idx   <= v_idx;
    end process comb_lookup;


    -- =========================================================================
    -- BLOQUE 2: Actualización síncrona de la TLB y política LRU
    -- =========================================================================
    -- En cada flanco de subida de clk:
    --   · reset  → invalida todo
    --   · write_en = '1' → inserta nueva entrada con LRU replacement
    --   · write_en = '0' y hit = '1' → promueve la entrada a MRU
    -- Prioridad: write_en > hit (si llegan juntos, se procesa la escritura).
    -- =========================================================================
    sync_tlb : process(clk)
        variable v_vpn        : std_logic_vector(VPN_BITS-1  downto 0);
        variable v_pcid_w     : std_logic_vector(PCID_BITS-1 downto 0);
        variable v_target     : integer range 0 to NUM_ENTRIES-1;
        variable v_lru_idx    : integer range 0 to NUM_ENTRIES-1;
        variable v_min_age    : unsigned(AGE_BITS-1 downto 0);
        variable v_free_found : boolean;
        variable v_free_idx   : integer range 0 to NUM_ENTRIES-1;
        -- Captura la edad de la víctima/hit ANTES de sobreescribirla,
        -- necesaria para el decremento selectivo correcto.
        variable v_victim_age : unsigned(AGE_BITS-1 downto 0);
    begin
        if rising_edge(clk) then

            -- -----------------------------------------------------------------
            -- Reset: invalida toda la tabla y pone las edades a 0
            -- -----------------------------------------------------------------
            if reset = '1' then
                for i in 0 to NUM_ENTRIES-1 loop
                    tlb_valid(i) <= '0';
                    tlb_age(i)   <= (others => '0');
                end loop;

            -- -----------------------------------------------------------------
            -- Escritura con reemplazo LRU
            -- -----------------------------------------------------------------
            elsif write_en = '1' then
                v_vpn    := virt_addr(VPN_HIGH downto VPN_LOW);
                v_pcid_w := pcid(PCID_LOW_BITS downto 0);

                -- Paso 1: Buscar entrada libre (inválida) o la de menor edad
                v_free_found := false;
                v_free_idx   := 0;
                v_min_age    := (others => '1');  -- inicializar al máximo
                v_lru_idx    := 0;

                for i in 0 to NUM_ENTRIES-1 loop
                    -- Primera entrada inválida encontrada = candidata gratis
                    if tlb_valid(i) = '0' and not v_free_found then
                        v_free_found := true;
                        v_free_idx   := i;
                    end if;
                    -- Mínima edad (LRU real)
                    if tlb_age(i) < v_min_age then
                        v_min_age := tlb_age(i);
                        v_lru_idx := i;
                    end if;
                end loop;

                -- Paso 2: Elegir víctima y capturar su edad actual
                if v_free_found then
                    v_target     := v_free_idx;
                    v_victim_age := tlb_age(v_free_idx); -- 0 si era inválida
                else
                    v_target     := v_lru_idx;
                    v_victim_age := v_min_age;            -- edad LRU real
                end if;

                -- Paso 3: Insertar la nueva entrada como MRU
                tlb_vpn(v_target)   <= v_vpn;
                tlb_pcid(v_target)  <= v_pcid_w;
                tlb_frame(v_target) <= write_phys;
                tlb_valid(v_target) <= '1';
                tlb_age(v_target)   <= to_unsigned(MAX_AGE, AGE_BITS);

                -- Paso 4: Decrementar SOLO las entradas más recientes que la víctima.
                --   Invariante: si age[i] <= v_victim_age, esas entradas ya eran
                --   más viejas que la víctima y no deben cambiar su posición relativa.
                for i in 0 to NUM_ENTRIES-1 loop
                    if i /= v_target then
                        if tlb_valid(i) = '1' and tlb_age(i) > v_victim_age then
                            tlb_age(i) <= tlb_age(i) - 1;
                        end if;
                    end if;
                end loop;

            -- -----------------------------------------------------------------
            -- Hit: promover la entrada encontrada a MRU.
            -- CORRECCIÓN LRU: solo decrementan las entradas cuya edad sea
            -- MAYOR que la edad actual de la entrada en hit.  Las entradas
            -- que ya eran más viejas que hit conservan su posición relativa.
            -- -----------------------------------------------------------------
            elsif lookup_en = '1' and s_hit_found = '1' then
                -- Capturar la edad actual del hit (antes de promoverla)
                v_victim_age := tlb_age(s_hit_idx);

                for i in 0 to NUM_ENTRIES-1 loop
                    if i = s_hit_idx then
                        -- Entrada accedida → MRU
                        tlb_age(i) <= to_unsigned(MAX_AGE, AGE_BITS);
                    elsif tlb_valid(i) = '1' and tlb_age(i) > v_victim_age then
                        -- Solo las entradas más recientes que hit pierden un puesto
                        tlb_age(i) <= tlb_age(i) - 1;
                        -- Las entradas con age <= v_victim_age ya eran más viejas
                        -- que hit: su orden relativo entre sí no debe cambiar.
                    end if;
                end loop;
            end if;

        end if;
    end process sync_tlb;

end Behavioral;

-- =============================================================================
-- NOTAS DE USO
-- =============================================================================
--
--  1. LOOKUP (asíncrono):
--       · Pon lookup_en = '1', virt_addr y pcid en los pines.
--       · hit y phys_frame responden sin esperar el clock.
--       · La actualización LRU del hit se efectúa en el siguiente flanco.
--
--  2. ESCRITURA (síncrona):
--       · Pon write_en = '1', virt_addr, pcid y write_phys en los pines.
--       · La inserción y el reemplazo LRU ocurren en el flanco de subida.
--       · write_en tiene prioridad sobre lookup_en si llegan juntos.
--
--  3. RESET:
--       · reset = '1' (síncrono) invalida todas las entradas en el
--         siguiente flanco de subida.
--
--  4. AJUSTE DE TAMAÑO:
--       · Para una TLB más pequeña (y más rápida en Logisim) baja
--         NUM_ENTRIES a 16 o 32.
--       · Ajusta AGE_BITS = ceil(log2(NUM_ENTRIES)):
--           16 entradas → AGE_BITS = 4
--           32 entradas → AGE_BITS = 5
--           64 entradas → AGE_BITS = 6  (valor actual)
--
--  5. LOGISIM:
--       · Compila con GHDL y exporta el netlist.
--       · El loop de 64 entradas genera lógica paralela; si el simulador
--         va lento, reduce NUM_ENTRIES a 16 y ajusta AGE_BITS.
-- =============================================================================
