// Logisim project Unidad_Aritmetica.circ as structural Verilog: 2 circuits, main circuit ALU
module ALU (
  input  [31:0] A,
  input  [3:0] Op,
  input  [31:0] B,
  output [31:0] RES,
  output [31:0] Carry_Out
);

  wire adder_1_cout, or_1_out, subtractor_1_bout;
  wire [4:0] bit_extender_1_out, bit_extender_2_out;
  wire [31:0] adder_1_out, and_1_out, bit_extender_3_out, demultiplexer_1_out0, demultiplexer_1_out1,
       demultiplexer_1_out2, demultiplexer_1_out3, demultiplexer_1_out4, demultiplexer_1_out5,
       demultiplexer_1_out6, demultiplexer_1_out7, demultiplexer_1_out8, demultiplexer_2_out0,
       demultiplexer_2_out1, demultiplexer_2_out2, demultiplexer_2_out3, demultiplexer_2_out4,
       demultiplexer_2_out5, demultiplexer_2_out6, demultiplexer_2_out7, demultiplexer_2_out8, divider_1_out,
       divider_1_rem, multiplier_1_cout, multiplier_1_out, nor_1_out, or_2_out, shifter_1_out, shifter_2_out,
       subtractor_1_out, xor_1_out;

  Demultiplexer #(.select(4), .width(32)) demultiplexer_1 (
    .out0(demultiplexer_1_out0), .out1(demultiplexer_1_out1), .out2(demultiplexer_1_out2),
    .out3(demultiplexer_1_out3), .out4(demultiplexer_1_out4), .out5(demultiplexer_1_out5),
    .out6(demultiplexer_1_out6), .out7(demultiplexer_1_out7), .out8(demultiplexer_1_out8), .in(A), .sel(Op));  // open: out9, out10, out11, out12, out13, out14, out15
  Demultiplexer #(.select(4), .width(32)) demultiplexer_2 (
    .out0(demultiplexer_2_out0), .out1(demultiplexer_2_out1), .out2(demultiplexer_2_out2),
    .out3(demultiplexer_2_out3), .out4(demultiplexer_2_out4), .out5(demultiplexer_2_out5),
    .out6(demultiplexer_2_out6), .out7(demultiplexer_2_out7), .out8(demultiplexer_2_out8), .in(B), .sel(Op));  // open: out9, out10, out11, out12, out13, out14, out15
  Adder #(.width(32)) adder_1 (
    .a(demultiplexer_1_out0), .b(demultiplexer_2_out0), .out(adder_1_out), .cout(adder_1_cout));  // open: cin
  Subtractor #(.width(32)) subtractor_1 (
    .a(demultiplexer_1_out1), .b(demultiplexer_2_out1), .out(subtractor_1_out), .bout(subtractor_1_bout));  // open: bin
  Multiplier #(.width(32)) multiplier_1 (
    .a(demultiplexer_1_out2), .b(demultiplexer_2_out2), .out(multiplier_1_out), .cout(multiplier_1_cout));  // open: cin
  Divider #(.width(32)) divider_1 (
    .a(demultiplexer_1_out3), .b(demultiplexer_2_out3), .out(divider_1_out), .rem(divider_1_rem));  // open: upper
  assign nor_1_out = ~(demultiplexer_1_out4 | demultiplexer_2_out4);  // NOR_Gate nor_1, 32 bits wide
  assign and_1_out = demultiplexer_1_out5 & demultiplexer_2_out5;  // AND_Gate and_1, 32 bits wide
  assign xor_1_out = demultiplexer_1_out6 ^ demultiplexer_2_out6;  // XOR_Gate xor_1, 32 bits wide
  Shifter #(.shift("lr"), .width(32)) shifter_1 (
    .in(demultiplexer_1_out7), .\dist (bit_extender_1_out), .out(shifter_1_out));
  Bit_Extender #(.in_width(32), .out_width(5), .\type ("zero")) bit_extender_1 (
    .in(demultiplexer_2_out7), .out(bit_extender_1_out));
  Shifter #(.width(32)) shifter_2 (.in(demultiplexer_1_out8), .\dist (bit_extender_2_out), .out(shifter_2_out));
  Bit_Extender #(.in_width(32), .out_width(5), .\type ("zero")) bit_extender_2 (
    .in(demultiplexer_2_out8), .out(bit_extender_2_out));
  Multiplexer #(.select(4), .width(32)) multiplexer_1 (
    .in0(adder_1_out), .in1(subtractor_1_out), .in2(multiplier_1_out), .in3(divider_1_out), .in4(nor_1_out),
    .in5(and_1_out), .in6(xor_1_out), .in7(shifter_1_out), .in8(shifter_2_out), .out(RES), .sel(Op));  // open: in9, in10, in11, in12, in13, in14, in15
  or or_1 (or_1_out, subtractor_1_bout, adder_1_cout);
  assign or_2_out = multiplier_1_cout | divider_1_rem;  // OR_Gate or_2, 32 bits wide
  assign bit_extender_3_out = {{31{1'b0}}, or_1_out};  // Bit_Extender bit_extender_3
  assign Carry_Out = bit_extender_3_out | or_2_out;  // OR_Gate or_3, 32 bits wide
endmodule

module Branch (
  input  [31:0] A,
  input  [31:0] Carry,
  input  [31:0] B,
  input  En,
  input  Clk,
  input  [3:0] Sel,
  input  [31:0] Data_Flags,
  input  [3:0] W,
  input  REGE_En,
  output Branch_Out,
  output [31:0] Carry_Out
);

  wire comparator_2_eq, comparator_5_eq, comparator_5_gt, comparator_6_eq, comparator_6_lt, comparator_7_eq,
       comparator_7_gt, or_4_out, or_5_out, plarom_1_p1;
  wire [1:0] plarom_1_p5;
  wire [2:0] bit_extender_1_out;
  wire [7:0] bit_extender_2_out, comparator_1_eq, multiplexer_1_out, register_1_q;
  wire [31:0] demultiplexer_1_out0, demultiplexer_1_out1, demultiplexer_1_out2, demultiplexer_1_out3,
       demultiplexer_1_out4, demultiplexer_1_out5, demultiplexer_2_out0, demultiplexer_2_out1,
       demultiplexer_2_out2, demultiplexer_2_out3, demultiplexer_2_out4, demultiplexer_2_out5,
       multiplexer_2_out;

  Demultiplexer #(.select(3), .width(32)) demultiplexer_1 (
    .out0(demultiplexer_1_out0), .out1(demultiplexer_1_out1), .out2(demultiplexer_1_out2),
    .out3(demultiplexer_1_out3), .out4(demultiplexer_1_out4), .out5(demultiplexer_1_out5), .in(A),
    .sel(bit_extender_1_out));  // open: out6, out7
  Bit_Extender #(.in_width(4), .out_width(3), .\type ("zero")) bit_extender_1 (.in(Sel), .out(bit_extender_1_out));
  // PlaRom #(.Contents("2 1 1 2 2 1 2 1 0 1 1 0"), .Select("high"), .\and (2), .outputs(2)) plarom_1: pin names not known; wires that end beside it: plarom_1_p1, plarom_1_p1, W, REGE_En, plarom_1_p5
  Pull_Resistor pull_resistor_1 (.node(plarom_1_p5));
  Demultiplexer #(.select(3), .width(32)) demultiplexer_2 (
    .out0(demultiplexer_2_out0), .out1(demultiplexer_2_out1), .out2(demultiplexer_2_out2),
    .out3(demultiplexer_2_out3), .out4(demultiplexer_2_out4), .out5(demultiplexer_2_out5), .in(B),
    .sel(bit_extender_1_out));  // open: out6, out7
  Comparator #(.mode("unsigned"), .width(32)) comparator_1 (
    .a(demultiplexer_1_out0), .b(demultiplexer_2_out0), .eq(comparator_1_eq[0]));  // open: gt, lt
  Comparator #(.mode("unsigned"), .width(32)) comparator_2 (
    .a(demultiplexer_1_out1), .b(demultiplexer_2_out1), .eq(comparator_2_eq));  // open: gt, lt
  Comparator #(.mode("unsigned"), .width(32)) comparator_3 (
    .a(demultiplexer_1_out2), .b(demultiplexer_2_out2), .gt(comparator_1_eq[2]));  // open: eq, lt
  Comparator #(.mode("unsigned"), .width(32)) comparator_4 (
    .a(demultiplexer_1_out3), .b(demultiplexer_2_out3), .lt(comparator_1_eq[3]));  // open: gt, eq
  Comparator #(.mode("unsigned"), .width(32)) comparator_5 (
    .a(demultiplexer_1_out4), .b(demultiplexer_2_out4), .gt(comparator_5_gt), .eq(comparator_5_eq));  // open: lt
  Comparator #(.mode("unsigned"), .width(32)) comparator_6 (
    .a(demultiplexer_1_out5), .b(demultiplexer_2_out5), .eq(comparator_6_eq), .lt(comparator_6_lt));  // open: gt
  Comparator #(.mode("unsigned"), .width(32)) comparator_7 (
    .a(Carry), .b(32'h1), .gt(comparator_7_gt), .eq(comparator_7_eq));  // open: lt
  Comparator #(.mode("unsigned"), .width(32)) comparator_8 (
    .a(Carry), .b({32{1'b0}}), .eq(comparator_1_eq[7]));  // open: gt, lt
  not not_1 (comparator_1_eq[1], comparator_2_eq);
  or or_1 (comparator_1_eq[4], comparator_5_gt, comparator_5_eq);
  or or_2 (comparator_1_eq[5], comparator_6_eq, comparator_6_lt);
  or or_3 (comparator_1_eq[6], comparator_7_gt, comparator_7_eq);
  Multiplexer #(.width(8)) multiplexer_1 (
    .in0(comparator_1_eq), .in1(bit_extender_2_out), .out(multiplexer_1_out), .sel(plarom_1_p5[0]));
  Bit_Extender #(.in_width(32), .out_width(8), .\type ("zero")) bit_extender_2 (
    .in(Data_Flags), .out(bit_extender_2_out));
  or or_4 (or_4_out, plarom_1_p5[0], En);
  Multiplexer #(.width(32)) multiplexer_2 (
    .in0(Carry), .in1(Data_Flags), .out(multiplexer_2_out), .sel(plarom_1_p5[1]));
  Register register_1 (.D(multiplexer_1_out), .en(or_4_out), .Q(register_1_q), .clk(Clk));  // open: clr
  or or_5 (or_5_out, En, plarom_1_p5[1]);
  Multiplexer #(.select(3)) multiplexer_3 (
    .in0(register_1_q[0]), .in1(register_1_q[1]), .in2(register_1_q[2]), .in3(register_1_q[3]),
    .in4(register_1_q[4]), .in5(register_1_q[5]), .in6(register_1_q[6]), .in7(register_1_q[7]),
    .out(Branch_Out), .sel(bit_extender_1_out));
  Register #(.width(32)) register_2 (.D(multiplexer_2_out), .en(or_5_out), .Q(Carry_Out), .clk(Clk));  // open: clr

  // Notes on the sheet:
  //   =
  //   !=
  //   >
  //   <
  //   >=
  //   <=
  //   O
  //   NO
endmodule
