// Logisim project Keyboard_Controller.circ as structural Verilog: 4 circuits, main circuit Keyboard_Main
module Keyboard_Main (
  input  [6:0] Ctrl_Down,
  input  [63:0] Data_In,
  input  [31:0] Addr_In,
  input  Data_Available,
  input  [6:0] Data_Keyboard,
  output [31:0] Addr_To_RAM,
  output [1:0] Ctrl_Up,
  output [63:0] Data_Out,
  output Clk,
  output Cls,
  output Read
);

  wire IRQ, keyboard_controller_1_clean_regs, msi_sys_1_bus_req, msi_sys_1_msi, tlp_receptor_1_dma_ack,
       tlp_receptor_1_ecam, tlp_receptor_1_en_read_cpu, tlp_receptor_1_en_write_cpu, tlp_receptor_1_mmio,
       tlp_receptor_1_rst;
  wire [15:0] endpoint_ecam_1_comand, keyboard_controller_1_status, M_Config;
  wire [31:0] endpoint_ecam_1_bar_out_0, endpoint_ecam_1_data_out, keyboard_controller_1_data_out, MA, MD,
       msi_sys_1_addr, msi_sys_1_data_out, multiplexer_1_out, multiplexer_2_out,
       registers_bar0_keyboard_1_comand_out, registers_bar0_keyboard_1_data_out;

  TLP_Receptor tlp_receptor_1 (
    .Bus_REQ(msi_sys_1_bus_req), .En_Write(msi_sys_1_msi), .Ctrl_Downstream(Ctrl_Down),
    .ECAM(tlp_receptor_1_ecam), .MMIO(tlp_receptor_1_mmio), .En_Write_CPU(tlp_receptor_1_en_write_cpu),
    .En_Read_CPU(tlp_receptor_1_en_read_cpu), .DMA_ACK(tlp_receptor_1_dma_ack), .Clk(Clk),
    .RST(tlp_receptor_1_rst), .Ctrl_Upstream(Ctrl_Up));
  EndPoint_ECAM endpoint_ecam_1 (
    .Write(tlp_receptor_1_en_write_cpu), .RST(tlp_receptor_1_rst), .Clk(Clk), .Data_In(Data_In),
    .Addr(Addr_In), .Is_ECAM(tlp_receptor_1_ecam), .Read(tlp_receptor_1_en_read_cpu),
    .Status(keyboard_controller_1_status), .Vendor_Device(32'h7a320004), .Class_Code(24'h90000),
    .Header_Type({8{1'b0}}), .ERBA({32{1'b1}}), .In_BAR_0(32'h8), .In_BAR_1({32{1'b0}}),
    .In_BAR_2({32{1'b0}}), .In_BAR_3({32{1'b0}}), .Next_Pointer({8{1'b1}}), .MSI_Cant(3'b000),
    .BAR_Out_0(endpoint_ecam_1_bar_out_0), .Data_Out(endpoint_ecam_1_data_out),
    .Comand(endpoint_ecam_1_comand), .M_Config(M_Config), .MA(MA), .MD(MD));  // open: BAR_Out_1, BAR_Out_2, BAR_Out_3
  Registers_BAR0_Keyboard registers_bar0_keyboard_1 (
    .Clean_Reg(keyboard_controller_1_clean_regs), .RST(tlp_receptor_1_rst), .Clk(Clk),
    .Read(tlp_receptor_1_en_read_cpu), .Write(tlp_receptor_1_en_write_cpu), .Data_In(Data_In),
    .Addr(Addr_In), .BAR_0(endpoint_ecam_1_bar_out_0), .BAR_0_REQ(32'h8), .MMIO(tlp_receptor_1_mmio),
    .Ctrl(endpoint_ecam_1_comand), .Data_Keyboard(keyboard_controller_1_data_out),
    .Data_Out(registers_bar0_keyboard_1_data_out), .Comand_Out(registers_bar0_keyboard_1_comand_out));
  Multiplexer #(.width(32)) multiplexer_1 (
    .in0(endpoint_ecam_1_data_out), .in1(registers_bar0_keyboard_1_data_out), .out(multiplexer_1_out),
    .sel(tlp_receptor_1_mmio));
  assign Addr_To_RAM = msi_sys_1_msi ? msi_sys_1_addr : 32'bz;  // Controlled_Buffer controlled_buffer_1
  Multiplexer #(.width(32)) multiplexer_2 (
    .in0(multiplexer_1_out), .in1(msi_sys_1_data_out), .out(multiplexer_2_out), .sel(msi_sys_1_msi));
  Keyboard_Controller keyboard_controller_1 (
    .Data_Available(Data_Available), .Clk(Clk), .RST(tlp_receptor_1_rst), .Ctrl(endpoint_ecam_1_comand),
    .Comand(registers_bar0_keyboard_1_comand_out), .Keyboard_Data(Data_Keyboard),
    .Status(keyboard_controller_1_status), .Clean(Cls), .Clean_Regs(keyboard_controller_1_clean_regs),
    .Read_Keyboard(Read), .IRQ(IRQ), .Data_Out(keyboard_controller_1_data_out));
  MSI_Sys msi_sys_1 (
    .M_config(M_Config), .Code({5{1'b0}}), .MD(MD), .IRQ(IRQ), .CLK(Clk), .MA(MA),
    .DMA_ACK(tlp_receptor_1_dma_ack), .Addr(msi_sys_1_addr), .MSI(msi_sys_1_msi),
    .Bus_REQ(msi_sys_1_bus_req), .Data_Out(msi_sys_1_data_out));
  assign Data_Out = {{32{1'b0}}, multiplexer_2_out};  // Bit_Extender bit_extender_1
endmodule

module Keyboard_Controller (
  input  RST,
  input  [15:0] Ctrl,
  input  [31:0] Comand,
  input  Data_Available,
  input  Clk,
  input  [6:0] Keyboard_Data,
  output [15:0] Status,
  output Clean,
  output Clean_Regs,
  output Read_Keyboard,
  output IRQ,
  output [31:0] Data_Out
);

  wire and_1_out, and_2_out, and_3_out, and_4_out, Buffer_IRQ_qn, or_1_out, or_3_out, or_4_out,
       Pending_Rearm_q, Service_IRQ_qn;

  and and_1 (and_1_out, Ctrl[0], Comand[0]);
  or or_1 (or_1_out, Comand[0], Comand[1]);
  or or_2 (Clean, RST, ~Ctrl[0], and_1_out);  // OR_Gate
  and and_2 (and_2_out, Data_Available, Buffer_IRQ_qn, Service_IRQ_qn);
  or or_3 (or_3_out, and_2_out, and_3_out);
  and and_3 (and_3_out, Data_Available, Pending_Rearm_q);
  and and_4 (and_4_out, Ctrl[0], Comand[1]);
  assign Data_Out = {{25{1'b0}}, Keyboard_Data};  // Bit_Extender bit_extender_1
  D_Flip_Flop d_ff_1 (.D(or_1_out), .clk(Clk), .Q(Clean_Regs), .reset(RST));  // open: Qn, preset
  D_Flip_Flop Buffer_IRQ (.D(or_3_out), .clk(Clk), .Q(IRQ), .Qn(Buffer_IRQ_qn), .reset(Clean));  // open: preset
  D_Flip_Flop Service_IRQ (.clk(Clk), .Qn(Service_IRQ_qn), .preset(IRQ), .reset(or_4_out));  // open: D, Q
  or or_4 (or_4_out, Clean, Comand[1]);
  D_Flip_Flop Pending_Rearm (.D(and_4_out), .clk(Clk), .Q(Pending_Rearm_q), .reset(Clean));  // open: Qn, preset

  assign Read_Keyboard = Comand[1];
  assign Status = Ctrl;
endmodule

module Registers_BAR0_Keyboard (
  input  [31:0] Addr,
  input  Clean_Reg,
  input  RST,
  input  Clk,
  input  Read,
  input  Write,
  input  [63:0] Data_In,
  input  MMIO,
  input  [31:0] Data_Keyboard,
  input  [15:0] Ctrl,
  input  [31:0] BAR_0,
  input  [31:0] BAR_0_REQ,
  output [31:0] Data_Out,
  output [31:0] Comand_Out
);

  wire and_1_out, and_2_out, and_3_out, and_5_out, comparator_1_eq, comparator_1_gt, comparator_2_eq,
       comparator_2_gt, decoder_1_out0, Enable, or_1_out, or_2_out, or_3_out;
  wire [31:0] adder_1_out, bit_extender_1_out;

  or or_1 (or_1_out, Clean_Reg, RST);
  and and_1 (and_1_out, Read, Enable);
  and and_2 (and_2_out, Enable, Write);
  Bit_Extender #(.in_width(64), .out_width(32), .\type ("zero")) bit_extender_1 (
    .in(Data_In), .out(bit_extender_1_out));
  Decoder #(.select(2)) decoder_1 (.out0(decoder_1_out0), .sel(Addr[3:2]), .en(and_2_out));  // open: out1, out2, out3
  Adder #(.width(32)) adder_1 (.a(BAR_0), .b(BAR_0_REQ), .out(adder_1_out));  // open: cin, cout
  and and_3 (and_3_out, MMIO, Ctrl[0]);
  or or_2 (or_2_out, comparator_1_gt, comparator_1_eq);
  Comparator #(.mode("unsigned"), .width(32)) comparator_1 (
    .a(Addr), .b(BAR_0), .gt(comparator_1_gt), .eq(comparator_1_eq));  // open: lt
  or or_3 (or_3_out, comparator_2_gt, comparator_2_eq);
  Comparator #(.mode("unsigned"), .width(32)) comparator_2 (
    .a(adder_1_out), .b(Addr), .gt(comparator_2_gt), .eq(comparator_2_eq));  // open: lt
  and and_4 (Enable, and_3_out, and_5_out);
  and and_5 (and_5_out, or_2_out, or_3_out);
  Register #(.width(32)) Comand (
    .D(bit_extender_1_out), .en(decoder_1_out0), .clk(Clk), .Q(Comand_Out), .clr(or_1_out));
  Multiplexer #(.enable("true"), .select(2), .width(32)) multiplexer_1 (
    .in0(Comand_Out), .in1(Data_Keyboard), .out(Data_Out), .sel(Addr[3:2]), .en(and_1_out));  // open: in2, in3
endmodule

module A (
  input  RST,
  input  [15:0] Ctrl,
  input  [31:0] Comand,
  input  Data_Available,
  input  Clk,
  input  [6:0] Keyboard_Data,
  output [15:0] Status,
  output Clean,
  output Clean_Regs,
  output Read_Keyboard,
  output IRQ,
  output [31:0] Data_Out
);

  wire and_1_out, and_2_out, and_4_out, d_ff_2_q, or_1_out, or_3_out;

  and and_1 (and_1_out, Ctrl[0], Comand[0]);
  D_Flip_Flop d_ff_1 (.D(or_1_out), .clk(Clk), .Q(Clean_Regs));  // open: Qn, preset, reset
  or or_1 (or_1_out, Comand[0], Comand[1]);
  and and_2 (and_2_out, Ctrl[0], Data_Available);
  or or_2 (Clean, RST, ~Ctrl[0], and_1_out);  // OR_Gate
  and and_3 (Read_Keyboard, Ctrl[0], ~d_ff_2_q);  // AND_Gate
  and and_4 (and_4_out, and_2_out, ~d_ff_2_q);  // AND_Gate
  assign Data_Out = {{25{1'b0}}, Keyboard_Data};  // Bit_Extender bit_extender_1
  D_Flip_Flop Buffer_IRQ (.D(and_4_out), .clk(Clk), .Q(IRQ), .reset(Clean));  // open: Qn, preset
  D_Flip_Flop d_ff_2 (.clk(Clk), .Q(d_ff_2_q), .preset(IRQ), .reset(or_3_out));  // open: D, Qn
  or or_3 (or_3_out, Clean, Comand[1]);

  assign Status = Ctrl;

  // Notes on the sheet:
  //   Service_IRQ
endmodule
