// Logisim project Main_Memories.circ as structural Verilog: 2 circuits, main circuit ROM_BIOS
module ROM_BIOS (
  input  [19:0] Addr,
  output [63:0] Data_Out
);

  // ROM #(.addrWidth(20), .line("octo"), .misaligned("true")) rom_1: pin names not known; wires that end beside it: Addr, Data_Out[31:24], Data_Out[23:16], Data_Out[15:8], Data_Out[7:0], Data_Out[63:56], Data_Out[55:48], Data_Out[47:40], Data_Out[39:32]

  // Notes on the sheet:
  //   contents of rom_1 (hex, n*v repeats v):
  //   8d e0 0 4 82 20 10 0 c 20 0 0 8c 20 4 0 8d 20 3 50 52 23 0 0 52 32 0 4 c 40 0 2 53 34 0 0 c 30 0 0
  //   8c 30 4 0 8d 30 3 54 12 34 0 0 d 40 0 1 c 50 0 3f 7 45 40 0 c 50 0 0 8c 50 4 0 8d 50 3 55 12 55 0 0
  //   3 45 0 0 8c f0 ff f0 8d f0 0 7c f f 0 0 12 35 0 0 c 60 0 0 8c 60 4 0 8d 60 3 56 2 56 50 0 13 52 0 0
  //   13 34 0 0 8d e0 ff fc 11 0 0 0 8d e0 0 c 53 e8 ff fc 53 e9 ff f8 c 80 0 1 53 18 0 4 52 12 0 10 c 90
  //   0 0 8c 90 4 0 8d 90 3 50 53 92 0 0 c 20 0 7e c 30 0 0 8c 30 ff f0 8d 30 0 0 8c f0 ff f0 8d f0 1e e0
  //   10 f 0 0 52 91 0 0 53 18 0 0 52 e9 ff f8 52 e8 ff fc 8d e0 ff f4 11 0 0 0 8d e0 0 10 53 e8 ff fc 53
  //   e9 ff f8 53 ea ff f4 c 10 0 0 8c 10 0 9 8d 10 0 0 8c f0 ff f0 8d f0 1c 24 10 f 0 0 82 10 80 0 c 90 0
  //   0 3 89 0 0 8c f0 ff f0 8d f0 1 e8 f 2f 0 0 c 10 0 14 4 81 20 0 c 30 0 0 8c 30 4 0 8d 30 2 d8 52 33 0
  //   0 2 32 20 0 12 23 0 10 a 31 10 0 12 23 0 11 c 40 0 f a 34 30 0 6 31 10 0 12 22 0 12 c 30 0 c a 23 20
  //   0 6 11 10 0 6 12 10 0 6 11 10 0 c 20 0 0 8c 20 e0 0 8d 20 0 4 6 12 20 0 6 22 20 0 c 90 0 1 53 29 0 0
  //   c 20 0 0 8c 20 e0 0 8d 20 0 10 6 12 20 0 6 22 20 0 52 22 0 0 c a0 0 0 8c a0 4 0 8d a0 3 50 53 a2 0 0
  //   c 20 0 0 8c 20 e0 0 8d 20 0 0 6 12 10 0 6 11 10 0 c 20 0 7e c 30 0 0 8c 30 ff f0 8d 30 0 0 8c f0 ff
  //   f0 8d f0 1e e0 10 f 0 0 52 a1 0 0 53 19 0 0 c 10 0 0 8c 10 4 0 8d 10 3 96 13 19 0 0 c 10 0 0 8c 10 0
  //   0 8d 10 ff ff 8 81 10 0 c 20 0 1f 9 12 10 0 52 ea ff f4 52 e9 ff f8 52 e8 ff fc 8d e0 ff f0 11 0 0 0
  //   8d e0 0 24 53 e8 ff f4 53 e9 ff f0 53 ea ff ec 53 eb ff e8 53 ec ff e4 53 ed ff e0 c a0 0 0 8c a0 0
  //   0 8d a0 ff ff c 40 0 0 53 e1 ff fc 3 14 0 0 8c f0 ff f0 8d f0 6 30 f f 0 0 c 50 0 1 3 25 0 0 8c f0
  //   ff f0 8d f0 6 30 f 2f 0 0 52 e1 ff fc 13 14 0 0 14 81 0 0 c 30 0 4 7 13 10 0 3 14 0 0 8c f0 ff f0 8d
  //   f0 2 b4 f 1f 0 0 c 10 0 0 8c 10 4 0 8d 10 0 40 8c f0 ff f0 8d f0 6 20 e f 0 0 d 20 ff ff 53 e2 ff f8
  //   c d0 0 0 8c d0 4 0 8d d0 3 55 c 90 0 0 8c 90 4 0 8d 90 3 54 c 60 0 0 8c 60 4 0 8d 60 3 56 c 70 0 3f
  //   c b0 0 c 82 40 10 0 82 40 a0 0 8c f0 ff f0 8d f0 3 0 e f 0 0 1 0 0 0 12 d2 0 0 12 93 0 0 3 23 0 0 8c
  //   f0 ff f0 8d f0 2 fc f f 0 0 12 d2 0 0 12 93 0 0 82 50 c0 0 3 23 0 0 8c f0 ff f0 8d f0 3 38 f 1f 0 0
  //   82 40 c0 0 3 23 0 0 8c f0 ff f0 8d f0 5 74 f f 0 0 12 d2 0 0 2 26 20 0 12 28 0 0 12 d2 0 0 d 20 0 1
  //   7 27 20 0 13 d2 0 0 3 b8 0 0 8c f0 ff f0 8d f0 3 a8 f 2f 0 0 c 20 0 8 3 82 0 0 8c f0 ff f0 8d f0 3
  //   bc f f 0 0 c 20 0 a 3 82 0 0 8c f0 ff f0 8d f0 4 64 f 1f 0 0 8c f0 ff f0 8d f0 4 e0 e f 0 0 c 20 0
  //   7f 3 82 0 0 8c f0 ff f0 8d f0 4 50 f 1f 0 0 3 a5 0 0 8c f0 ff f0 8d f0 4 ac f 2f 0 0 82 b0 90 0 82
  //   a0 b0 0 d b0 ff ff 3 1a 0 0 8c f0 ff f0 8d f0 3 f8 f 3f 0 0 82 b0 a0 0 8c f0 ff f0 8d f0 4 34 e f 0
  //   0 c 10 0 0 8c 10 4 0 8d 10 0 6d 82 50 20 0 8c f0 ff f0 8d f0 d f0 10 f 0 0 c 70 0 3f c 60 0 0 8c 60
  //   4 0 8d 60 3 56 c 50 0 1 c 40 0 0 82 b0 a0 0 82 b0 10 0 82 90 b0 0 c 90 0 0 8c 90 4 0 8d 90 3 54 8c
  //   f0 ff f0 8d f0 4 ac e f 0 0 c 20 0 d 3 82 0 0 8c f0 ff f0 8d f0 4 e0 f f 0 0 82 80 20 0 d 20 ff e0 c
  //   30 0 ff 7 23 20 0 c 30 0 5e 3 32 0 0 8c f0 ff f0 8d f0 4 ac f 4f 0 0 52 e2 ff f8 3 a2 0 0 8c f0 ff
  //   f0 8d f0 4 ac f 3f 0 0 52 e2 ff fc 2 2a 20 0 13 28 0 0 d a0 0 1 c 20 0 d 3 82 0 0 8c f0 ff f0 8d f0
  //   5 74 f f 0 0 c 20 0 a 3 82 0 0 8c f0 ff f0 8d f0 3 18 f 1f 0 0 8c f0 ff f0 8d f0 5 74 e f 0 0 82 50
  //   20 0 c 30 0 a 3 83 0 0 8c f0 ff f0 8d f0 4 fc f f 0 0 82 40 20 0 82 50 30 0 c c0 0 d 3 8c 0 0 8c f0
  //   ff f0 8d f0 5 18 f f 0 0 82 40 30 0 3 8c 0 0 8c f0 ff f0 8d f0 5 e0 f 1f 0 0 12 d2 0 0 12 93 0 0 3
  //   23 0 0 8c f0 ff f0 8d f0 5 70 f f 0 0 12 d2 0 0 2 26 20 0 12 22 0 0 c 30 0 a 3 23 0 0 8c f0 ff f0 8d
  //   f0 5 70 f 1f 0 0 12 d2 0 0 d 20 0 1 7 27 20 0 13 d2 0 0 82 50 c0 0 3 1a 0 0 8c f0 ff f0 8d f0 5 c0 f
  //   3f 0 0 52 e3 ff fc 2 3a 20 0 13 24 0 0 2 31 10 0 82 40 20 0 8c f0 ff f0 8d f0 d f0 10 f 0 0 c 70 0
  //   3f c 60 0 0 8c 60 4 0 8d 60 3 56 c 50 0 1 c 40 0 0 82 a0 10 0 7 c5 20 0 3 24 0 0 8c f0 ff f0 8d f0 3
  //   0 f f 0 0 8c f0 ff f0 8d f0 6 4 e f 0 0 6 23 20 0 6 22 c0 0 3 1a 0 0 8c f0 ff f0 8d f0 5 84 f 2f 0 0
  //   8c f0 ff f0 8d f0 5 c0 e f 0 0 52 e1 ff fc 2 1a 10 0 c 20 0 0 13 12 0 0 c 10 0 0 8c 10 4 0 8d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
endmodule

module Memory (
  input  [31:0] Addr,
  input  RST,
  input  Read_En,
  input  [7:0] Write_Flags,
  input  Clk,
  input  [63:0] Data_In,
  input  Write_En,
  output RAM_Ready,
  output [63:0] out_9
);

  wire decoder_1_out0, decoder_1_out1, decoder_1_out2, decoder_1_out3;
  wire [7:0] ram_1_p5, ram_1_p6, ram_1_p7, ram_1_p8, ram_1_p9, ram_1_p10, ram_1_p11, ram_1_p12, ram_2_p5,
       ram_3_p5, ram_3_p6, ram_3_p7, ram_3_p8, ram_3_p9, ram_3_p10, ram_3_p11, ram_3_p12, ram_4_p5, ram_4_p6,
       ram_4_p7, ram_4_p8, ram_4_p9, ram_4_p10, ram_4_p11, ram_4_p12, undriven, undriven_2, undriven_3,
       undriven_4, undriven_5, undriven_6, undriven_7;

  Decoder #(.select(2)) decoder_1 (
    .out0(decoder_1_out0), .out1(decoder_1_out1), .out2(decoder_1_out2), .out3(decoder_1_out3),
    .sel(Addr[31:30]), .en(Write_En));
  // RAM #(.addrWidth(30), .clearpin("true"), .enables("line"), .line("octo"), .misaligned("true")) ram_1: pin names not known; wires that end beside it: Addr[29:0], decoder_1_out3, Clk, RST, ram_1_p5, ram_1_p6, ram_1_p7, ram_1_p8, ram_1_p9, ram_1_p10, ram_1_p11, ram_1_p12
  // RAM #(.addrWidth(30), .clearpin("true"), .enables("line"), .line("octo"), .misaligned("true")) ram_2: pin names not known; wires that end beside it: Addr[29:0], decoder_1_out0, Clk, RST, ram_2_p5
  // RAM #(.addrWidth(30), .clearpin("true"), .enables("line"), .line("octo"), .misaligned("true")) ram_3: pin names not known; wires that end beside it: Addr[29:0], decoder_1_out1, Clk, RST, ram_3_p5, ram_3_p6, ram_3_p7, ram_3_p8, ram_3_p9, ram_3_p10, ram_3_p11, ram_3_p12
  // RAM #(.addrWidth(30), .clearpin("true"), .enables("line"), .line("octo"), .misaligned("true")) ram_4: pin names not known; wires that end beside it: Addr[29:0], decoder_1_out2, Clk, RST, ram_4_p5, ram_4_p6, ram_4_p7, ram_4_p8, ram_4_p9, ram_4_p10, ram_4_p11, ram_4_p12
  Multiplexer #(.enable("true"), .select(2), .width(64)) multiplexer_1 (
    .in0({ram_3_p11, ram_3_p10, ram_3_p9, ram_3_p8, ram_3_p7, ram_3_p6, ram_3_p5, ram_2_p5}),
    .in1({ram_4_p11, ram_4_p10, ram_4_p9, ram_4_p8, ram_4_p7, ram_4_p6, ram_4_p5, ram_3_p12}),
    .in2({undriven_7, undriven_6, undriven_5, undriven_4, undriven_3, undriven_2, undriven, ram_4_p12}),
    .in3({ram_1_p12, ram_1_p11, ram_1_p10, ram_1_p9, ram_1_p8, ram_1_p7, ram_1_p6, ram_1_p5}), .out(out_9),
    .sel(Addr[31:30]), .en(Read_En));

  assign Data_In[47:40] = Data_In[55:48];
  assign RAM_Ready = 1'b1;

  // Other names for the same wires on the sheet: Sel[1:0] = Addr[31:30]
endmodule
