// Logisim project ECAMs.circ as structural Verilog: 4 circuits, main circuit ECAM_Mapper
module ECAM_Mapper (
  input  [31:0] Addr,
  output Is_ECAM,
  output [11:0] Reg_sel,
  output [2:0] Func,
  output [4:0] Disp,
  output [5:0] Bus_Dir
);

  Comparator #(.mode("unsigned"), .width(6)) comparator_1 (
    .a(Addr[31:26]), .b(6'b111000), .eq(Is_ECAM));  // open: gt, lt

  assign Bus_Dir = Addr[25:20];
  assign Disp = Addr[19:15];
  assign Func = Addr[14:12];
  assign Reg_sel = Addr[11:0];

  // Notes on the sheet:
  //   ECAM=E00 a E3F
endmodule

module Port_ECAM (
  input  Read,
  input  Is_ECAM,
  input  RST,
  input  Clk,
  input  [63:0] Data_In,
  input  [11:0] Addr,
  input  [15:0] Status,
  input  [31:0] Vendor_Device,
  input  [23:0] Class_Code,
  input  [7:0] Header_Type,
  input  [11:0] Capabilities_Pointer,
  output [31:0] Data_Out,
  output [15:0] Comand,
  output [31:0] PSS0_Out,
  output [31:0] Base_Limit
);

  wire and_3_out, and_4_out, and_5_out, comparator_2_eq, comparator_2_gt, CP, decoder_1_out0, decoder_1_out2,
       Not_Common, Read_t;
  wire [2:0] and_2_out, pla_2_out;
  wire [3:0] pla_1_out;
  wire [31:0] bit_extender_1_out, bit_extender_2_out, common_ecam_1_data_out, multiplexer_1_out;

  Bit_Extender #(.in_width(64), .out_width(32), .\type ("zero")) bit_extender_1 (
    .in(Data_In), .out(bit_extender_1_out));
  and and_1 (Read_t, Read, Is_ECAM);
  Comparator #(.mode("unsigned"), .width(12)) comparator_1 (.a(12'h10), .b(Addr), .gt(and_2_out[1]));  // open: eq, lt
  Comparator #(.mode("unsigned"), .width(12)) comparator_2 (
    .a(Addr), .b(Capabilities_Pointer), .gt(comparator_2_gt), .eq(comparator_2_eq));  // open: lt
  assign bit_extender_2_out = {{20{1'b0}}, Capabilities_Pointer};  // Bit_Extender bit_extender_2
  and and_2 (and_2_out[0], Is_ECAM, ~Read_t);  // AND_Gate
  or or_1 (and_2_out[2], comparator_2_gt, comparator_2_eq);
  PLA #(.in_width(3), .out_width(4), .\table ("010 0000 # Com\n000 1001 # NCom\n100 0110 # CP")) pla_1 (
    .in(and_2_out), .out(pla_1_out));
  PLA #(.in_width(3), .out_width(3), .\table ("xx0 000 # NOT\n001 010 # NCom\n011 100 # Com\n101 001 # CP")) pla_2 (
    .in(and_2_out), .out(pla_2_out));
  and and_3 (and_3_out, ~Read_t, Not_Common);  // AND_Gate
  Decoder #(.select(2)) decoder_1 (
    .out0(decoder_1_out0), .out2(decoder_1_out2), .sel(Addr[3:2]), .en(and_3_out));  // open: out1, out3
  Register #(.width(32)) PSS0 (.D(bit_extender_1_out), .en(decoder_1_out0), .clk(Clk), .Q(PSS0_Out), .clr(RST));
  Register #(.width(32)) MBase_MLimit (
    .D(bit_extender_1_out), .en(decoder_1_out2), .clk(Clk), .Q(Base_Limit), .clr(RST));
  and and_4 (and_4_out, pla_1_out[3], Read_t);
  and and_5 (and_5_out, Read_t, pla_1_out[2]);
  or or_2 (CP, and_5_out, pla_2_out[0]);
  or or_3 (Not_Common, and_4_out, pla_2_out[1]);
  Common_ECAM common_ecam_1 (
    .Is_Common_ECAM(pla_2_out[2]), .Clk(Clk), .RST(RST), .Data_In(bit_extender_1_out), .Addr(Addr),
    .Read(Read_t), .Vendor_Device(Vendor_Device), .Status(Status), .Class_Code(Class_Code),
    .Header_Type(Header_Type), .Comand_Out(Comand), .Data_Out(common_ecam_1_data_out));
  Multiplexer #(.enable("true"), .select(2), .width(32)) multiplexer_1 (
    .in0(PSS0_Out), .in1(bit_extender_2_out), .in2(Base_Limit), .out(multiplexer_1_out), .sel(Addr[3:2]),
    .en(Not_Common));  // open: in3
  Multiplexer #(.enable("true"), .select(2), .width(32)) multiplexer_2 (
    .in0(common_ecam_1_data_out), .in1(multiplexer_1_out), .out(Data_Out), .sel(pla_1_out[1:0]), .en(Read_t));  // open: in2, in3
endmodule

module EndPoint_ECAM (
  input  Is_ECAM,
  input  Read,
  input  Write,
  input  RST,
  input  Clk,
  input  [63:0] Data_In,
  input  [31:0] Addr,
  input  [15:0] Status,
  input  [31:0] Vendor_Device,
  input  [23:0] Class_Code,
  input  [7:0] Header_Type,
  input  [31:0] ERBA,
  input  [31:0] In_BAR_0,
  input  [31:0] In_BAR_1,
  input  [31:0] In_BAR_2,
  input  [31:0] In_BAR_3,
  input  [7:0] Next_Pointer,
  input  [2:0] MSI_Cant,
  output [31:0] Data_Out,
  output [15:0] Comand,
  output [31:0] BAR_Out_0,
  output [31:0] BAR_Out_1,
  output [31:0] BAR_Out_2,
  output [31:0] BAR_Out_3,
  output [15:0] M_Config,
  output [31:0] MA,
  output [31:0] MD
);

  wire and_6_out, and_7_out, Common, comparator_1_gt, comparator_2_eq, comparator_2_gt, comparator_3_eq,
       comparator_4_eq, comparator_5_eq, comparator_6_eq, CP, decoder_1_out0, decoder_1_out1, decoder_1_out2,
       decoder_1_out3, NCommon, or_1_out, Read_t, Write_t;
  wire [1:0] pla_2_out;
  wire [2:0] pla_1_out;
  wire [11:0] Addr_t;
  wire [31:0] BAR_0_q, BAR_1_q, BAR_2_q, BAR_3_q, bit_extender_1_out, bit_extender_3_out,
       common_ecam_1_data_out, msi_registers_1_data_out, multiplexer_5_out;

  Bit_Extender #(.in_width(64), .out_width(32), .\type ("zero")) bit_extender_1 (
    .in(Data_In), .out(bit_extender_1_out));
  Bit_Extender #(.in_width(32), .out_width(12), .\type ("zero")) bit_extender_2 (.in(Addr), .out(Addr_t));
  and and_1 (Read_t, Is_ECAM, Read);
  and and_2 (Write_t, Is_ECAM, ~Read, Write);  // AND_Gate
  Comparator #(.mode("unsigned"), .width(12)) comparator_1 (
    .a(12'h10), .b(Addr_t), .gt(comparator_1_gt));  // open: eq, lt
  Comparator #(.mode("unsigned"), .width(12)) comparator_2 (
    .a(Addr_t), .b(12'h30), .gt(comparator_2_gt), .eq(comparator_2_eq));  // open: lt
  or or_1 (or_1_out, comparator_2_gt, comparator_2_eq);
  and and_3 (Common, comparator_1_gt, ~or_1_out);  // AND_Gate
  and and_4 (NCommon, ~comparator_1_gt, ~or_1_out);  // AND_Gate
  and and_5 (CP, ~comparator_1_gt, or_1_out);  // AND_Gate
  and and_6 (and_6_out, Write_t, NCommon);
  Decoder #(.select(2)) decoder_1 (
    .out0(decoder_1_out0), .out1(decoder_1_out1), .out2(decoder_1_out2), .out3(decoder_1_out3),
    .sel(Addr_t[3:2]), .en(and_6_out));
  and and_7 (and_7_out, Write_t, Common);
  assign bit_extender_3_out = {{20{1'b0}}, 12'h30};  // Bit_Extender bit_extender_3
  Register #(.width(32)) BAR_0 (.D(bit_extender_1_out), .en(decoder_1_out0), .clk(Clk), .Q(BAR_0_q), .clr(RST));
  Register #(.width(32)) BAR_1 (.D(bit_extender_1_out), .en(decoder_1_out1), .clk(Clk), .Q(BAR_1_q), .clr(RST));
  Register #(.width(32)) BAR_2 (.D(bit_extender_1_out), .en(decoder_1_out2), .clk(Clk), .Q(BAR_2_q), .clr(RST));
  Register #(.width(32)) BAR_3 (.D(bit_extender_1_out), .en(decoder_1_out3), .clk(Clk), .Q(BAR_3_q), .clr(RST));
  Common_ECAM common_ecam_1 (
    .Is_Common_ECAM(and_7_out), .Clk(Clk), .RST(RST), .Data_In(bit_extender_1_out), .Addr(Addr_t),
    .Read(Read_t), .Vendor_Device(Vendor_Device), .Status(Status), .Class_Code(Class_Code),
    .Header_Type(Header_Type), .Comand_Out(Comand), .Data_Out(common_ecam_1_data_out));
  Comparator #(.mode("unsigned"), .width(32)) comparator_3 (
    .a(BAR_0_q), .b({32{1'b1}}), .eq(comparator_3_eq));  // open: gt, lt
  Comparator #(.mode("unsigned"), .width(32)) comparator_4 (
    .a(BAR_1_q), .b({32{1'b1}}), .eq(comparator_4_eq));  // open: gt, lt
  Comparator #(.mode("unsigned"), .width(32)) comparator_5 (
    .a(BAR_2_q), .b({32{1'b1}}), .eq(comparator_5_eq));  // open: gt, lt
  Comparator #(.mode("unsigned"), .width(32)) comparator_6 (
    .a(BAR_3_q), .b({32{1'b1}}), .eq(comparator_6_eq));  // open: gt, lt
  MSI_Registers msi_registers_1 (
    .Read(Read_t), .Write(Write_t), .Addr(Addr_t), .Is_CP(CP), .Next_Pointer(Next_Pointer), .Cant(MSI_Cant),
    .RST(RST), .CLK(Clk), .Data_In(bit_extender_1_out), .M_config(M_Config), .MA_Out(MA), .MD_Out(MD),
    .Data_Out(msi_registers_1_data_out));
  PLA #(.in_width(4), .out_width(3), .\table ("0100 000 # 0\n0101 001 # 1\n0110 010 # 2\n0111 011 # 3\n1000 100 # ERBA\n1001 101 # CP")) pla_1 (
    .in(Addr_t[5:2]), .out(pla_1_out));
  Multiplexer #(.width(32)) multiplexer_1 (.in0(BAR_0_q), .in1(In_BAR_0), .out(BAR_Out_0), .sel(comparator_3_eq));
  Multiplexer #(.width(32)) multiplexer_2 (.in0(BAR_1_q), .in1(In_BAR_1), .out(BAR_Out_1), .sel(comparator_4_eq));
  Multiplexer #(.width(32)) multiplexer_3 (.in0(BAR_2_q), .in1(In_BAR_2), .out(BAR_Out_2), .sel(comparator_5_eq));
  Multiplexer #(.width(32)) multiplexer_4 (.in0(BAR_3_q), .in1(In_BAR_3), .out(BAR_Out_3), .sel(comparator_6_eq));
  PLA #(.in_width(3), .\table ("001 00 # C\n010 01 # NC\n100 10 # CP\n000 11 # NOT")) pla_2 (
    .in({CP, NCommon, Common}), .out(pla_2_out));
  Multiplexer #(.enable("true"), .select(3), .width(32)) multiplexer_5 (
    .in0(BAR_Out_0), .in1(BAR_Out_1), .in2(BAR_Out_2), .in3(BAR_Out_3), .in4(ERBA), .in5(bit_extender_3_out),
    .out(multiplexer_5_out), .sel(pla_1_out), .en(NCommon));  // open: in6, in7
  Multiplexer #(.enable("true"), .select(2), .width(32)) multiplexer_6 (
    .in0(common_ecam_1_data_out), .in1(multiplexer_5_out), .in2(msi_registers_1_data_out), .in3({32{1'b0}}),
    .out(Data_Out), .sel(pla_2_out), .en(Read_t));
endmodule

module Common_ECAM (
  input  [11:0] Addr,
  input  Read,
  input  Is_Common_ECAM,
  input  Clk,
  input  RST,
  input  [31:0] Data_In,
  input  [31:0] Vendor_Device,
  input  [15:0] Status,
  input  [23:0] Class_Code,
  input  [7:0] Header_Type,
  output [15:0] Comand_Out,
  output [31:0] Data_Out
);

  wire and_1_out, decoder_1_out1;
  wire [15:0] bit_extender_1_out;

  and and_1 (and_1_out, Is_Common_ECAM, ~Read);  // AND_Gate
  Decoder #(.select(2)) decoder_1 (.out1(decoder_1_out1), .sel(Addr[3:2]), .en(and_1_out));  // open: out0, out2, out3
  Bit_Extender #(.in_width(32), .\type ("zero")) bit_extender_1 (.in(Data_In), .out(bit_extender_1_out));
  Register #(.width(16)) Command (.D(bit_extender_1_out), .en(decoder_1_out1), .clk(Clk), .Q(Comand_Out), .clr(RST));
  Multiplexer #(.enable("true"), .select(2), .width(32)) multiplexer_1 (
    .in0(Vendor_Device), .in1({Status, Comand_Out}), .in2({Header_Type, Class_Code}), .out(Data_Out),
    .sel(Addr[3:2]), .en(Read));  // open: in3
endmodule
