// Logisim project IO_Interface.circ as structural Verilog: 5 circuits, main circuit Root_Complex
module Root_Complex (
  input  [31:0] Data_In,
  input  [31:0] Addr,
  input  RST,
  input  Clk,
  input  [31:0] Addr_From_Perif_1,
  input  En_Read,
  input  [31:0] Data_From_Perif_1,
  input  En_Write_1,
  input  DMA_REQ_1,
  input  RAM_ACK,
  input  [31:0] Addr_From_Perif_2,
  input  [31:0] Data_From_Perif_2,
  input  En_Write_2,
  input  DMA_REQ_2,
  input  [31:0] Addr_From_Perif_3,
  input  [31:0] Data_From_Perif_3,
  input  En_Write_3,
  input  DMA_REQ_3,
  output [31:0] Data_Out,
  output [31:0] Addr_To_CPU,
  output Is_RAM,
  output [31:0] Addr_To_Perif_1,
  output [31:0] Data_To_Perif_1,
  output Write_REQ,
  output En_Read_To_Perif_1,
  output Read_REQ,
  output DMA_ACK_1,
  output [31:0] Addr_To_Perif_2,
  output Bus_REQ,
  output [31:0] Data_To_Perif_2,
  output En_Read_To_Perif_2,
  output DMA_ACK_2,
  output [31:0] Addr_To_Perif_3,
  output [31:0] Data_To_Perif_3,
  output En_Read_To_Perif_3,
  output DMA_ACK_3
);

  wire and_2_out, comparator_1_eq, decoder_1_out1, decoder_1_out2, decoder_1_out3, decoder_2_out0,
       decoder_2_out1, decoder_2_out2, Device_ECAM, dma_controller_1_dma_ack_1, dma_controller_1_dma_ack_2,
       dma_controller_1_dma_ack_3, nor_1_out, or_2_out, port_module_1_bus_req, port_module_1_device_ecam,
       port_module_1_internal_ecam, port_module_1_this_port_mmio, port_module_2_bus_req,
       port_module_2_device_ecam, port_module_2_internal_ecam, port_module_2_this_port_mmio,
       port_module_3_bus_req, port_module_3_device_ecam, port_module_3_internal_ecam,
       port_module_3_this_port_mmio, t_ff_1_qn;
  wire [1:0] Sel;
  wire [2:0] bit_extender_1_out;
  wire [4:0] register_1_q;
  wire [31:0] port_module_1_addr_to_cpu, port_module_1_data_to_cpu, port_module_2_addr_to_cpu,
       port_module_2_data_to_cpu, port_module_3_addr_to_cpu, port_module_3_data_to_cpu;

  and and_1 (Read_REQ, ~Write_REQ, RAM_ACK);  // AND_Gate
  Bit_Extender #(.in_width(5), .out_width(3), .\type ("zero")) bit_extender_1 (
    .in(Addr[19:15]), .out(bit_extender_1_out));
  DMA_Controller dma_controller_1 (
    .Clk(Clk), .RST(RST), .RAM_ACK(RAM_ACK), .Bus_REQ_1(port_module_1_bus_req),
    .Bus_REQ_2(port_module_2_bus_req), .Bus_REQ_3(port_module_3_bus_req), .RAM_REQ(Bus_REQ),
    .DMA_ACK_1(dma_controller_1_dma_ack_1), .DMA_ACK_2(dma_controller_1_dma_ack_2),
    .DMA_ACK_3(dma_controller_1_dma_ack_3), .Sel(Sel));
  Comparator #(.mode("unsigned"), .width(6)) comparator_1 (
    .a(Addr[31:26]), .b(6'b111000), .eq(comparator_1_eq));  // open: gt, lt
  Decoder #(.select(3)) decoder_1 (
    .out1(decoder_1_out1), .out2(decoder_1_out2), .out3(decoder_1_out3), .sel(bit_extender_1_out),
    .en(Device_ECAM));  // open: out0, out4, out5, out6, out7
  Register #(.width(5)) register_1 (.D(Addr[19:15]), .en(and_2_out), .clk(Clk), .Q(register_1_q), .clr(RST));
  and and_2 (and_2_out, comparator_1_eq, t_ff_1_qn);
  Decoder #(.select(3)) decoder_2 (
    .out0(decoder_2_out0), .out1(decoder_2_out1), .out2(decoder_2_out2), .sel(Addr[14:12]), .en(or_2_out));  // open: out3, out4, out5, out6, out7
  T_Flip_Flop t_ff_1 (.T(and_2_out), .clk(Clk), .Qn(t_ff_1_qn), .reset(RST));  // open: Q, preset
  or or_1 (Device_ECAM, port_module_3_device_ecam, port_module_2_device_ecam, port_module_1_device_ecam);
  and and_3 (Is_RAM, ~or_2_out, nor_1_out);  // AND_Gate
  nor nor_1 (nor_1_out, port_module_3_this_port_mmio, port_module_2_this_port_mmio, port_module_1_this_port_mmio);
  or or_2 (or_2_out, port_module_3_internal_ecam, port_module_2_internal_ecam, port_module_1_internal_ecam);
  assign Data_Out = port_module_3_data_to_cpu | port_module_2_data_to_cpu | port_module_1_data_to_cpu;  // OR_Gate or_3, 32 bits wide
  assign Addr_To_CPU = port_module_3_addr_to_cpu | port_module_2_addr_to_cpu | port_module_1_addr_to_cpu;  // OR_Gate or_4, 32 bits wide
  Multiplexer #(.enable("true"), .select(2)) multiplexer_1 (
    .in0(En_Write_1), .in1(En_Write_2), .in2(DMA_REQ_2), .out(Write_REQ), .sel(Sel), .en(RAM_ACK));  // open: in3
  Port_Module port_module_1 (
    .Addr_From_CPU(Addr), .Data_In_From_CPU(Data_In), .Read(En_Read), .This_ECAM(decoder_2_out0), .RST(RST),
    .Clk(Clk), .Device_ID(register_1_q), .Is_ECAM(comparator_1_eq), .This_Port_Device(decoder_1_out1),
    .DMA_ACK_From_CPU(dma_controller_1_dma_ack_1), .Data_From_Perif(Data_From_Perif_1),
    .En_Write(En_Write_1), .DMA_REQ(DMA_REQ_1), .Addr_From_Perif(Addr_From_Perif_1),
    .Device_ECAM(port_module_1_device_ecam), .This_Port_MMIO(port_module_1_this_port_mmio),
    .Data_To_CPU(port_module_1_data_to_cpu), .Internal_ECAM(port_module_1_internal_ecam),
    .Bus_REQ(port_module_1_bus_req), .Addr_To_CPU(port_module_1_addr_to_cpu), .En_Read(En_Read_To_Perif_1),
    .Addr_To_Perif(Addr_To_Perif_1), .Data_To_Perif(Data_To_Perif_1), .DMA_ACK(DMA_ACK_1));
  Port_Module port_module_2 (
    .Addr_From_CPU(Addr), .Data_In_From_CPU(Data_In), .Read(En_Read), .This_ECAM(decoder_2_out1), .RST(RST),
    .Clk(Clk), .Device_ID(register_1_q), .Is_ECAM(comparator_1_eq), .This_Port_Device(decoder_1_out2),
    .DMA_ACK_From_CPU(dma_controller_1_dma_ack_2), .Data_From_Perif(Data_From_Perif_2),
    .En_Write(En_Write_2), .DMA_REQ(DMA_REQ_2), .Addr_From_Perif(Addr_From_Perif_2),
    .Device_ECAM(port_module_2_device_ecam), .This_Port_MMIO(port_module_2_this_port_mmio),
    .Data_To_CPU(port_module_2_data_to_cpu), .Internal_ECAM(port_module_2_internal_ecam),
    .Bus_REQ(port_module_2_bus_req), .Addr_To_CPU(port_module_2_addr_to_cpu), .En_Read(En_Read_To_Perif_2),
    .Addr_To_Perif(Addr_To_Perif_2), .Data_To_Perif(Data_To_Perif_2), .DMA_ACK(DMA_ACK_2));
  Port_Module port_module_3 (
    .Addr_From_CPU(Addr), .Data_In_From_CPU(Data_In), .Read(En_Read), .This_ECAM(decoder_2_out2), .RST(RST),
    .Clk(Clk), .Device_ID(register_1_q), .Is_ECAM(comparator_1_eq), .This_Port_Device(decoder_1_out3),
    .DMA_ACK_From_CPU(dma_controller_1_dma_ack_3), .Data_From_Perif(Data_From_Perif_3),
    .En_Write(En_Write_3), .DMA_REQ(DMA_REQ_3), .Addr_From_Perif(Addr_From_Perif_3),
    .Device_ECAM(port_module_3_device_ecam), .This_Port_MMIO(port_module_3_this_port_mmio),
    .Data_To_CPU(port_module_3_data_to_cpu), .Internal_ECAM(port_module_3_internal_ecam),
    .Bus_REQ(port_module_3_bus_req), .Addr_To_CPU(port_module_3_addr_to_cpu), .En_Read(En_Read_To_Perif_3),
    .Addr_To_Perif(Addr_To_Perif_3), .Data_To_Perif(Data_To_Perif_3), .DMA_ACK(DMA_ACK_3));

  // Other names for the same wires on the sheet: Device[4:0] = Addr[19:15]; Data_To_CPU[31:0] = Data_Out;
  //   En_Write = Write_REQ; Not_RAM = Is_RAM

  // Notes on the sheet:
  //   ECAM=E00 a E3F
endmodule

module DMA_Controller (
  input  Clk,
  input  RST,
  input  RAM_ACK,
  input  Bus_REQ_1,
  input  Bus_REQ_2,
  input  Bus_REQ_3,
  output [1:0] Sel,
  output DMA_ACK_1,
  output DMA_ACK_2,
  output DMA_ACK_3,
  output RAM_REQ
);

  wire decoder_1_out0, decoder_1_out1, decoder_1_out2, nor_1_out;

  Counter #(.max('h2), .width(2)) counter_1 (
    .count(nor_1_out), .Q(Sel), .clk(Clk), .clr(RST));  // open: load, D, carry, up
  Decoder #(.select(2)) decoder_1 (
    .out0(decoder_1_out0), .out1(decoder_1_out1), .out2(decoder_1_out2), .sel(Sel), .en(RAM_ACK));  // open: out3
  nor nor_1 (nor_1_out, DMA_ACK_1, DMA_ACK_2, DMA_ACK_3);
  and and_1 (DMA_ACK_1, decoder_1_out0, Bus_REQ_1);
  and and_2 (DMA_ACK_2, decoder_1_out1, Bus_REQ_2);
  and and_3 (DMA_ACK_3, decoder_1_out2, Bus_REQ_3);
  or or_1 (RAM_REQ, Bus_REQ_1, Bus_REQ_2, Bus_REQ_3);
endmodule

module Port_Module (
  input  [31:0] Addr_From_CPU,
  input  [31:0] Data_In_From_CPU,
  input  Read,
  input  This_ECAM,
  input  RST,
  input  Clk,
  input  [4:0] Device_ID,
  input  [31:0] Data_From_Perif,
  input  Is_ECAM,
  input  This_Port_Device,
  input  En_Write,
  input  DMA_REQ,
  input  DMA_ACK_From_CPU,
  input  [31:0] Addr_From_Perif,
  output [31:0] Data_To_CPU,
  output En_Read,
  output [31:0] Addr_To_Perif,
  output Device_ECAM,
  output [31:0] Data_To_Perif,
  output This_Port_MMIO,
  output Internal_ECAM,
  output Bus_REQ,
  output DMA_ACK,
  output [31:0] Addr_To_CPU
);

  wire and_1_out, or_1_out;
  wire [1:0] pla_1_out;
  wire [11:0] bit_extender_1_out;
  wire [15:0] port_ecam_1_comand;
  wire [31:0] downstream_1_data_out, downstream_1_response_out, port_ecam_1_base_limit, port_ecam_1_data_out,
       port_ecam_1_pss0_out, upstream_1_data_to_cpu, upstream_1_data_to_perif;

  and and_1 (and_1_out, Read, This_ECAM);
  Multiplexer #(.enable("true"), .select(2), .width(32)) multiplexer_1 (
    .in0({32{1'b1}}), .in1(port_ecam_1_data_out), .in2(downstream_1_response_out),
    .in3(upstream_1_data_to_cpu), .out(Data_To_CPU), .sel(pla_1_out), .en(or_1_out));
  or or_1 (or_1_out, and_1_out, En_Write);
  PLA #(.in_width(3), .\table ("000 00 # NOP\n010 01 # ECAM\n100 10 # Device\n001 11 # DMA")) pla_1 (
    .in({This_Port_Device, This_ECAM, DMA_ACK_From_CPU}), .out(pla_1_out));
  Bit_Extender #(.in_width(32), .out_width(12), .\type ("zero")) bit_extender_1 (
    .in(Addr_From_CPU), .out(bit_extender_1_out));
  Downstream downstream_1 (
    .Base_Limit(port_ecam_1_base_limit), .This_Port_ECAM_Downstream(This_Port_Device),
    .Addr_CPU(Addr_From_CPU), .Data_In(Data_In_From_CPU), .PSS0(port_ecam_1_pss0_out),
    .Comand(port_ecam_1_comand), .Device_ID(Device_ID), .Is_ECAM(Is_ECAM), .Response(Data_From_Perif),
    .Response_Out(downstream_1_response_out), .Internal_ECAM(Internal_ECAM), .Device_ECAM(Device_ECAM),
    .This_Port_MMIO(This_Port_MMIO), .Addr_Out(Addr_To_Perif), .Data_Out(downstream_1_data_out));
  Upstream upstream_1 (
    .Comand(port_ecam_1_comand), .DMA_REQ(DMA_REQ), .DMA_ACK_From_CPU(DMA_ACK_From_CPU),
    .Addr_Perif(Addr_From_Perif), .Data_From_Perif(Data_From_Perif), .En_Write(En_Write),
    .Data_From_CPU(Data_In_From_CPU), .Data_To_Perif(upstream_1_data_to_perif), .Bus_REQ(Bus_REQ),
    .DMA_ACK(DMA_ACK), .Addr_To_CPU(Addr_To_CPU), .Data_To_CPU(upstream_1_data_to_cpu));
  Port_ECAM port_ecam_1 (
    .Read(Read), .Clk(Clk), .Data_In(Data_In_From_CPU), .Addr(bit_extender_1_out),
    .Vendor_Device({32{1'b1}}), .Is_ECAM(This_ECAM), .Class_Code({32{1'b1}}), .Header_Type({8{1'b1}}),
    .Capabilities_Pointer({12{1'b1}}), .RST(RST), .Data_Out(port_ecam_1_data_out),
    .Comand(port_ecam_1_comand), .PSS0_Out(port_ecam_1_pss0_out), .Base_Limit(port_ecam_1_base_limit));  // open: Status
  and and_2 (En_Read, Read, This_Port_Device);
  Multiplexer #(.width(32)) multiplexer_2 (
    .in0(downstream_1_data_out), .in1(upstream_1_data_to_perif), .out(Data_To_Perif), .sel(DMA_ACK));

  // Notes on the sheet:
  //   Vendor & Device
  //   Capabilities Pointer
  //   Class Code
  //   Header_Type
endmodule

module Downstream (
  input  This_Port_ECAM_Downstream,
  input  [15:0] Comand,
  input  [31:0] Base_Limit,
  input  [31:0] Addr_CPU,
  input  [31:0] Data_In,
  input  [31:0] Response,
  input  [31:0] PSS0,
  input  [4:0] Device_ID,
  input  Is_ECAM,
  output This_Port_MMIO,
  output [31:0] Addr_Out,
  output [31:0] Data_Out,
  output [31:0] Response_Out,
  output Internal_ECAM,
  output Device_ECAM
);

  wire and_1_out, and_2_out, and_3_out, and_5_out, comparator_1_eq, comparator_1_lt, comparator_2_eq,
       comparator_2_gt, comparator_3_lt, comparator_4_eq, comparator_4_gt, comparator_5_eq, comparator_6_eq,
       ECAM_Downstream, or_1_out, or_2_out, or_3_out;
  wire [7:0] bit_extender_1_out;

  Comparator #(.mode("unsigned"), .width(32)) comparator_1 (
    .a({Base_Limit[15:0], {16{1'b0}}}), .b(Addr_CPU), .eq(comparator_1_eq), .lt(comparator_1_lt));  // open: gt
  Comparator #(.mode("unsigned"), .width(32)) comparator_2 (
    .a({Base_Limit[31:16], {16{1'b1}}}), .b(Addr_CPU), .gt(comparator_2_gt), .eq(comparator_2_eq));  // open: lt
  assign bit_extender_1_out = {{2{1'b0}}, Addr_CPU[25:20]};  // Bit_Extender bit_extender_1
  or or_1 (or_1_out, comparator_1_eq, comparator_1_lt);
  or or_2 (or_2_out, comparator_2_gt, comparator_2_eq);
  Comparator #(.mode("unsigned")) comparator_3 (
    .a(PSS0[15:8]), .b(bit_extender_1_out), .lt(comparator_3_lt));  // open: gt, eq
  Comparator #(.mode("unsigned")) comparator_4 (
    .a(PSS0[23:16]), .b(bit_extender_1_out), .gt(comparator_4_gt), .eq(comparator_4_eq));  // open: lt
  Comparator #(.mode("unsigned")) comparator_5 (
    .a(PSS0[31:24]), .b(bit_extender_1_out), .eq(comparator_5_eq));  // open: gt, lt
  Comparator #(.mode("unsigned"), .width(5)) comparator_6 (
    .a(Addr_CPU[19:15]), .b(Device_ID), .eq(comparator_6_eq));  // open: gt, lt
  and and_1 (and_1_out, Comand[0], and_2_out);
  and and_2 (and_2_out, or_1_out, or_2_out);
  and and_3 (and_3_out, comparator_3_lt, or_3_out);
  or or_3 (or_3_out, comparator_4_gt, comparator_4_eq);
  and and_4 (ECAM_Downstream, and_3_out, Is_ECAM);
  and and_5 (and_5_out, comparator_5_eq, Is_ECAM);
  or or_4 (This_Port_MMIO, This_Port_ECAM_Downstream, and_1_out, ECAM_Downstream);
  Multiplexer #(.width(32)) multiplexer_1 (.in0({32{1'b0}}), .in1(Addr_CPU), .out(Addr_Out), .sel(This_Port_MMIO));
  Multiplexer #(.width(32)) multiplexer_2 (.in0({32{1'b0}}), .in1(Data_In), .out(Data_Out), .sel(This_Port_MMIO));
  Multiplexer #(.width(32)) multiplexer_3 (.in0({32{1'b1}}), .in1(Response), .out(Response_Out), .sel(This_Port_MMIO));
  and and_6 (Internal_ECAM, and_5_out, comparator_6_eq);
  and and_7 (Device_ECAM, and_5_out, ~comparator_6_eq);  // AND_Gate

  // Notes on the sheet:
  //   MMIO Normal
  //   Secondary
  //   Subordinate
  //   Primary
  //   ECAM
endmodule

module Upstream (
  input  [15:0] Comand,
  input  DMA_REQ,
  input  DMA_ACK_From_CPU,
  input  [31:0] Addr_Perif,
  input  [31:0] Data_From_Perif,
  input  En_Write,
  input  [31:0] Data_From_CPU,
  output Bus_REQ,
  output DMA_ACK,
  output [31:0] Addr_To_CPU,
  output [31:0] Data_To_CPU,
  output [31:0] Data_To_Perif
);

  and and_1 (Bus_REQ, Comand[1], DMA_REQ);
  Multiplexer #(.width(32)) multiplexer_1 (.in0({32{1'b0}}), .in1(Addr_Perif), .out(Addr_To_CPU), .sel(DMA_ACK));
  Multiplexer #(.enable("true"), .width(32)) multiplexer_2 (
    .in0({32{1'b0}}), .in1(Data_From_Perif), .out(Data_To_CPU), .sel(DMA_ACK), .en(En_Write));
  Multiplexer #(.width(32)) multiplexer_3 (.in0({32{1'b0}}), .in1(Data_From_CPU), .out(Data_To_Perif), .sel(DMA_ACK));
  and and_2 (DMA_ACK, Bus_REQ, DMA_ACK_From_CPU);
endmodule
