// Logisim project Root_Complex.circ as structural Verilog: 6 circuits, main circuit Root_Complex
module Root_Complex (
  input  [63:0] Data_In,
  input  Read,
  input  Write,
  input  Clk,
  input  RST,
  input  [31:0] Addr,
  input  [63:0] Data_To_Up_1,
  input  [31:0] Addr_To_Up_1,
  input  [1:0] Ctrl_Up_1,
  input  DMA_ACK,
  input  [63:0] Data_To_Up_2,
  input  [31:0] Addr_To_Up_2,
  input  [1:0] Ctrl_Up_2,
  input  [63:0] Data_To_Up_3,
  input  [31:0] Addr_To_Up_3,
  input  [1:0] Ctrl_Up_3,
  output [31:0] Addr_To_CPU,
  output [63:0] Data_Out,
  output Is_RAM,
  output RAM_Write,
  output [31:0] Addr_To_Down_1,
  output [63:0] Data_To_Down_1,
  output [6:0] Ctrl_Down_1,
  output RAM_Read,
  output [31:0] Addr_To_Down_2,
  output Bus_REQ,
  output [63:0] Data_To_Down_2,
  output [6:0] Ctrl_Down_2,
  output [31:0] Addr_To_Down_3,
  output [63:0] Data_To_Down_3,
  output [6:0] Ctrl_Down_3
);

  wire dma_controller_1_dma_ack_1, dma_controller_1_dma_ack_2, dma_controller_1_dma_ack_3, Is_ECAM,
       nor_1_out, or_1_out, or_2_out, root_port_module_1_bus_req, root_port_module_1_internal_ecam,
       root_port_module_1_this_port_mmio, root_port_module_1_write_req, root_port_module_2_bus_req,
       root_port_module_2_internal_ecam, root_port_module_2_this_port_mmio, root_port_module_2_write_req,
       root_port_module_3_bus_req, root_port_module_3_internal_ecam, root_port_module_3_this_port_mmio,
       root_port_module_3_write_req;
  wire [4:0] ecam_mapper_1_disp;
  wire [5:0] ecam_mapper_1_bus_dir;
  wire [11:0] ecam_mapper_1_reg_sel;
  wire [31:0] root_port_module_1_addr_to_ram, root_port_module_2_addr_to_ram, root_port_module_3_addr_to_ram;
  wire [63:0] Data_To_CPU, root_port_module_1_data_out, root_port_module_2_data_out,
       root_port_module_3_data_out;

  and and_1 (Is_RAM, ~or_2_out, ~Is_ECAM, nor_1_out);  // AND_Gate
  Multiplexer #(.width(64)) multiplexer_1 (.in0({64{1'b1}}), .in1(Data_To_CPU), .out(Data_Out), .sel(or_1_out));
  or or_1 (or_1_out, ~nor_1_out, or_2_out);  // OR_Gate
  nor nor_1 (nor_1_out, root_port_module_1_this_port_mmio, root_port_module_2_this_port_mmio, root_port_module_3_this_port_mmio);
  and and_2 (RAM_Read, ~RAM_Write, DMA_ACK);  // AND_Gate
  or or_2 (or_2_out, root_port_module_1_internal_ecam, root_port_module_2_internal_ecam, root_port_module_3_internal_ecam);
  or or_3 (RAM_Write, root_port_module_1_write_req, root_port_module_2_write_req, root_port_module_3_write_req);
  ECAM_Mapper ecam_mapper_1 (
    .Addr(Addr), .Is_ECAM(Is_ECAM), .Reg_sel(ecam_mapper_1_reg_sel), .Disp(ecam_mapper_1_disp),
    .Bus_Dir(ecam_mapper_1_bus_dir));  // open: Func
  DMA_Controller dma_controller_1 (
    .Clk(Clk), .RST(RST), .RAM_ACK(DMA_ACK), .Bus_REQ_1(root_port_module_1_bus_req),
    .Bus_REQ_2(root_port_module_2_bus_req), .Bus_REQ_3(root_port_module_3_bus_req), .RAM_REQ(Bus_REQ),
    .DMA_ACK_1(dma_controller_1_dma_ack_1), .DMA_ACK_2(dma_controller_1_dma_ack_2),
    .DMA_ACK_3(dma_controller_1_dma_ack_3));
  assign Addr_To_CPU = root_port_module_3_addr_to_ram | root_port_module_2_addr_to_ram | root_port_module_1_addr_to_ram;  // OR_Gate or_4, 32 bits wide
  assign Data_To_CPU = root_port_module_3_data_out | root_port_module_2_data_out | root_port_module_1_data_out;  // OR_Gate or_5, 64 bits wide
  Root_Port_Module root_port_module_1 (
    .DMA_ACK(dma_controller_1_dma_ack_1), .Data_In(Data_In), .Reg_Sel(ecam_mapper_1_reg_sel),
    .En_Write(Write), .En_Read(Read), .RST(RST), .Clk(Clk), .D_Pre_Config(5'b00001), .D(ecam_mapper_1_disp),
    .B(ecam_mapper_1_bus_dir), .Addr_CPU(Addr), .Is_ECAM(Is_ECAM), .Data_To_Up(Data_To_Up_1),
    .Addr_To_Up(Addr_To_Up_1), .Ctrl_Up(Ctrl_Up_1), .Write_REQ(root_port_module_1_write_req),
    .Bus_REQ(root_port_module_1_bus_req), .This_Port_MMIO(root_port_module_1_this_port_mmio),
    .Addr_To_RAM(root_port_module_1_addr_to_ram), .Internal_ECAM(root_port_module_1_internal_ecam),
    .Data_Out(root_port_module_1_data_out), .Data_To_Down(Data_To_Down_1), .Addr_To_Down(Addr_To_Down_1),
    .Ctrl_Down(Ctrl_Down_1));
  Root_Port_Module root_port_module_2 (
    .DMA_ACK(dma_controller_1_dma_ack_2), .Data_In(Data_In), .Reg_Sel(ecam_mapper_1_reg_sel),
    .En_Write(Write), .En_Read(Read), .RST(RST), .Clk(Clk), .D_Pre_Config(5'b00010), .D(ecam_mapper_1_disp),
    .B(ecam_mapper_1_bus_dir), .Addr_CPU(Addr), .Is_ECAM(Is_ECAM), .Data_To_Up(Data_To_Up_2),
    .Addr_To_Up(Addr_To_Up_2), .Ctrl_Up(Ctrl_Up_2), .Write_REQ(root_port_module_2_write_req),
    .Bus_REQ(root_port_module_2_bus_req), .This_Port_MMIO(root_port_module_2_this_port_mmio),
    .Addr_To_RAM(root_port_module_2_addr_to_ram), .Internal_ECAM(root_port_module_2_internal_ecam),
    .Data_Out(root_port_module_2_data_out), .Data_To_Down(Data_To_Down_2), .Addr_To_Down(Addr_To_Down_2),
    .Ctrl_Down(Ctrl_Down_2));
  Root_Port_Module root_port_module_3 (
    .DMA_ACK(dma_controller_1_dma_ack_3), .Data_In(Data_In), .Reg_Sel(ecam_mapper_1_reg_sel),
    .En_Write(Write), .En_Read(Read), .RST(RST), .Clk(Clk), .D_Pre_Config(5'b00011), .D(ecam_mapper_1_disp),
    .B(ecam_mapper_1_bus_dir), .Addr_CPU(Addr), .Is_ECAM(Is_ECAM), .Data_To_Up(Data_To_Up_3),
    .Addr_To_Up(Addr_To_Up_3), .Ctrl_Up(Ctrl_Up_3), .Write_REQ(root_port_module_3_write_req),
    .Bus_REQ(root_port_module_3_bus_req), .This_Port_MMIO(root_port_module_3_this_port_mmio),
    .Addr_To_RAM(root_port_module_3_addr_to_ram), .Internal_ECAM(root_port_module_3_internal_ecam),
    .Data_Out(root_port_module_3_data_out), .Data_To_Down(Data_To_Down_3), .Addr_To_Down(Addr_To_Down_3),
    .Ctrl_Down(Ctrl_Down_3));
endmodule

module DMA_Controller (
  input  Clk,
  input  RST,
  input  RAM_ACK,
  input  Bus_REQ_1,
  input  Bus_REQ_2,
  input  Bus_REQ_3,
  output DMA_ACK_1,
  output DMA_ACK_2,
  output DMA_ACK_3,
  output RAM_REQ
);

  wire decoder_1_out0, decoder_1_out1, decoder_1_out2, nor_1_out;
  wire [1:0] counter_1_q;

  Counter #(.max('h2), .width(2)) counter_1 (
    .count(nor_1_out), .Q(counter_1_q), .clk(Clk), .clr(RST));  // open: load, D, carry, up
  Decoder #(.select(2)) decoder_1 (
    .out0(decoder_1_out0), .out1(decoder_1_out1), .out2(decoder_1_out2), .sel(counter_1_q), .en(RAM_ACK));  // open: out3
  nor nor_1 (nor_1_out, DMA_ACK_1, DMA_ACK_2, DMA_ACK_3);
  and and_1 (DMA_ACK_1, decoder_1_out0, Bus_REQ_1);
  and and_2 (DMA_ACK_2, decoder_1_out1, Bus_REQ_2);
  and and_3 (DMA_ACK_3, decoder_1_out2, Bus_REQ_3);
  or or_1 (RAM_REQ, Bus_REQ_1, Bus_REQ_2, Bus_REQ_3);
endmodule

module Root_Port_Module (
  input  [11:0] Reg_Sel,
  input  En_Write,
  input  En_Read,
  input  RST,
  input  Clk,
  input  [63:0] Data_To_Up,
  input  [31:0] Addr_To_Up,
  input  [4:0] D_Pre_Config,
  input  [4:0] D,
  input  [5:0] B,
  input  [31:0] Addr_CPU,
  input  [1:0] Ctrl_Up,
  input  Is_ECAM,
  input  DMA_ACK,
  input  [63:0] Data_In,
  output [63:0] Data_Out,
  output Internal_ECAM,
  output [63:0] Data_To_Down,
  output [31:0] Addr_To_Down,
  output [6:0] Ctrl_Down,
  output Write_REQ,
  output Bus_REQ,
  output [31:0] Addr_To_RAM,
  output This_Port_MMIO
);

  wire and_1_out, and_2_out, and_3_out, and_4_out, and_5_out, and_7_out, and_8_out,
       downstream_1_downstream_ecam, or_2_out, or_3_out, This_MMIO, tlp_1_bus_req, tlp_1_en_write,
       upstream_1_dma_ack;
  wire [1:0] Sel_Read, Sel_Write;
  wire [2:0] and_10_out, and_12_out;
  wire [15:0] port_ecam_1_comand;
  wire [31:0] downstream_1_addr_out, port_ecam_1_base_limit, port_ecam_1_data_out, port_ecam_1_pss0_out,
       tlp_1_addr_to_up;
  wire [63:0] bit_extender_1_out, demultiplexer_1_out1, demultiplexer_1_out2, demultiplexer_1_out3,
       downstream_1_data_out, downstream_1_response_out, tlp_1_data_to_up, upstream_1_data_to_cpu,
       upstream_1_data_to_perif;

  and and_1 (and_1_out, DMA_ACK, ~Write_REQ);  // AND_Gate
  or or_1 (This_Port_MMIO, This_MMIO, and_3_out);
  Multiplexer #(.enable("true"), .select(2), .width(64)) multiplexer_1 (
    .in0({64{1'b0}}), .in1(bit_extender_1_out), .in2(downstream_1_response_out),
    .in3(upstream_1_data_to_cpu), .out(Data_Out), .sel(Sel_Read), .en(or_2_out));
  or or_2 (or_2_out, En_Read, and_2_out);
  and and_2 (and_2_out, Write_REQ, DMA_ACK);
  or or_3 (or_3_out, and_1_out, En_Write);
  Demultiplexer #(.enable("true"), .select(2), .width(64)) demultiplexer_1 (
    .out1(demultiplexer_1_out1), .out2(demultiplexer_1_out2), .out3(demultiplexer_1_out3), .in(Data_In),
    .sel(Sel_Write), .en(or_3_out));  // open: out0
  and and_3 (and_3_out, DMA_ACK, Write_REQ);
  Upstream upstream_1 (
    .Comand(port_ecam_1_comand), .DMA_REQ(tlp_1_bus_req), .DMA_ACK_From_CPU(DMA_ACK),
    .Addr_Perif(tlp_1_addr_to_up), .Data_From_Perif(tlp_1_data_to_up), .En_Write(tlp_1_en_write),
    .Data_From_CPU(demultiplexer_1_out3), .Data_To_Perif(upstream_1_data_to_perif), .Bus_REQ(Bus_REQ),
    .DMA_ACK(upstream_1_dma_ack), .Addr_To_CPU(Addr_To_RAM), .Data_To_CPU(upstream_1_data_to_cpu),
    .En_Write_Out(Write_REQ));
  assign bit_extender_1_out = {{32{1'b0}}, port_ecam_1_data_out};  // Bit_Extender bit_extender_1
  Port_ECAM port_ecam_1 (
    .Data_In(demultiplexer_1_out1), .Read(En_Read), .Clk(Clk), .Addr(Reg_Sel), .Status(port_ecam_1_comand),
    .Vendor_Device(32'h7a320001), .Is_ECAM(Internal_ECAM), .Class_Code(24'h60400), .Header_Type(8'h1),
    .Capabilities_Pointer({12{1'b1}}), .RST(RST), .Data_Out(port_ecam_1_data_out),
    .Comand(port_ecam_1_comand), .PSS0_Out(port_ecam_1_pss0_out), .Base_Limit(port_ecam_1_base_limit));
  Downstream downstream_1 (
    .Base_Limit(port_ecam_1_base_limit), .Addr_CPU(Addr_CPU), .Data_In(demultiplexer_1_out2), .B(B),
    .PSS0(port_ecam_1_pss0_out), .D(D), .Comand(port_ecam_1_comand), .Device_ID(D_Pre_Config),
    .Is_ECAM(Is_ECAM), .Response(tlp_1_data_to_up), .Response_Out(downstream_1_response_out),
    .Internal_ECAM(Internal_ECAM), .Addr_Out(downstream_1_addr_out), .Data_Out(downstream_1_data_out),
    .Downstream_ECAM(downstream_1_downstream_ecam), .This_Port_MMIO(This_MMIO));
  and and_4 (and_4_out, Internal_ECAM, En_Read);
  and and_5 (and_5_out, ~Internal_ECAM, This_MMIO, En_Read);  // AND_Gate
  and and_6 (and_10_out[2], Write_REQ, DMA_ACK);
  and and_7 (and_7_out, Internal_ECAM, ~En_Read, En_Write);  // AND_Gate
  and and_8 (and_8_out, ~Internal_ECAM, This_MMIO, En_Write);  // AND_Gate
  and and_9 (and_12_out[2], ~Write_REQ, DMA_ACK);  // AND_Gate
  Pull_Resistor #(.pull(1)) pull_resistor_1 (.node(Data_To_Up));
  TLP tlp_1 (
    .ECAM(downstream_1_downstream_ecam), .MMIO(This_MMIO), .En_Write_CPU(En_Write), .En_Read_CPU(En_Read),
    .DMA_ACK(upstream_1_dma_ack), .Clk(Clk), .RST(RST), .Data_From_CPU(downstream_1_data_out),
    .Data_From_DMA(upstream_1_data_to_perif), .Addr_From_CPU(downstream_1_addr_out),
    .Addr_To_Upstream(Addr_To_Up), .Data_To_Upstream(Data_To_Up), .Ctrl_Upstream(Ctrl_Up),
    .Bus_REQ(tlp_1_bus_req), .En_Write(tlp_1_en_write), .Addr_To_Up(tlp_1_addr_to_up),
    .Data_To_Up(tlp_1_data_to_up), .Addr_To_Downstream(Addr_To_Down), .Data_To_Downstream(Data_To_Down),
    .Ctrl_Downstream(Ctrl_Down));
  and and_10 (and_10_out[0], and_4_out, ~and_10_out[2]);  // AND_Gate
  and and_11 (and_10_out[1], and_5_out, ~and_10_out[2]);  // AND_Gate
  PLA #(.in_width(3), .\table ("001 01 # This\n010 10 # Down\n1xx 11 # DMA")) pla_1 (.in(and_10_out), .out(Sel_Read));
  and and_12 (and_12_out[0], and_7_out, ~and_12_out[2]);  // AND_Gate
  and and_13 (and_12_out[1], and_8_out, ~and_12_out[2]);  // AND_Gate
  PLA #(.in_width(3), .\table ("001 01 # This\n010 10 # Down\n1xx 11 # DMA")) pla_2 (.in(and_12_out), .out(Sel_Write));

  // Other names for the same wires on the sheet: Read_CPU = En_Read; This_ECAM = Internal_ECAM; Write_CPU = En_Write

  // Notes on the sheet:
  //   This_ECAM
  //   Down ECAM/MMIO
  //   DMA
endmodule

module Downstream (
  input  [15:0] Comand,
  input  [31:0] Base_Limit,
  input  [31:0] Addr_CPU,
  input  [63:0] Data_In,
  input  [63:0] Response,
  input  [5:0] B,
  input  [31:0] PSS0,
  input  [4:0] D,
  input  [4:0] Device_ID,
  input  Is_ECAM,
  output This_Port_MMIO,
  output [31:0] Addr_Out,
  output [63:0] Data_Out,
  output [63:0] Response_Out,
  output Downstream_ECAM,
  output Internal_ECAM
);

  wire and_1_out, and_2_out, and_3_out, comparator_1_eq, comparator_1_lt, comparator_2_eq, comparator_2_gt,
       comparator_3_eq, comparator_3_lt, comparator_4_eq, comparator_4_gt, comparator_5_eq, comparator_6_eq,
       ECAM_Downstream, or_1_out, or_2_out, or_3_out, or_4_out;
  wire [7:0] bit_extender_1_out;

  assign bit_extender_1_out = {{2{1'b0}}, B};  // Bit_Extender bit_extender_1
  Comparator #(.mode("unsigned"), .width(32)) comparator_1 (
    .a({Base_Limit[15:0], {16{1'b0}}}), .b(Addr_CPU), .eq(comparator_1_eq), .lt(comparator_1_lt));  // open: gt
  Comparator #(.mode("unsigned"), .width(32)) comparator_2 (
    .a({Base_Limit[31:16], {16{1'b1}}}), .b(Addr_CPU), .gt(comparator_2_gt), .eq(comparator_2_eq));  // open: lt
  or or_1 (or_1_out, comparator_1_eq, comparator_1_lt);
  or or_2 (or_2_out, comparator_2_gt, comparator_2_eq);
  Comparator #(.mode("unsigned")) comparator_3 (
    .a(PSS0[15:8]), .b(bit_extender_1_out), .eq(comparator_3_eq), .lt(comparator_3_lt));  // open: gt
  Comparator #(.mode("unsigned")) comparator_4 (
    .a(PSS0[23:16]), .b(bit_extender_1_out), .gt(comparator_4_gt), .eq(comparator_4_eq));  // open: lt
  Comparator #(.mode("unsigned")) comparator_5 (
    .a(PSS0[7:0]), .b(bit_extender_1_out), .eq(comparator_5_eq));  // open: gt, lt
  Comparator #(.mode("unsigned"), .width(5)) comparator_6 (.a(D), .b(Device_ID), .eq(comparator_6_eq));  // open: gt, lt
  and and_1 (and_1_out, Comand[0], and_2_out);
  and and_2 (and_2_out, or_1_out, or_2_out);
  or or_3 (or_3_out, comparator_4_gt, comparator_4_eq);
  and and_3 (and_3_out, ~Internal_ECAM, comparator_3_eq, ~comparator_5_eq, Is_ECAM);  // AND_Gate
  and and_4 (Internal_ECAM, comparator_5_eq, Is_ECAM, comparator_6_eq);
  or or_4 (or_4_out, and_3_out, and_1_out, ECAM_Downstream);
  Multiplexer #(.width(32)) multiplexer_1 (.in0({32{1'b0}}), .in1(Addr_CPU), .out(Addr_Out), .sel(This_Port_MMIO));
  Multiplexer #(.width(64)) multiplexer_2 (.in0({64{1'b0}}), .in1(Data_In), .out(Data_Out), .sel(This_Port_MMIO));
  Multiplexer #(.width(64)) multiplexer_3 (.in0({64{1'b1}}), .in1(Response), .out(Response_Out), .sel(This_Port_MMIO));
  and and_5 (ECAM_Downstream, comparator_3_lt, Is_ECAM, or_3_out, ~Internal_ECAM);  // AND_Gate
  and and_6 (This_Port_MMIO, ~Internal_ECAM, or_4_out);  // AND_Gate
  or or_5 (Downstream_ECAM, and_3_out, ECAM_Downstream);

  // Notes on the sheet:
  //   MMIO Normal
  //   Secondary
  //   Subordinate
  //   Primary
  //   ECAM
endmodule

module Upstream (
  input  [15:0] Comand,
  input  DMA_REQ,
  input  DMA_ACK_From_CPU,
  input  [31:0] Addr_Perif,
  input  [63:0] Data_From_Perif,
  input  En_Write,
  input  [63:0] Data_From_CPU,
  output Bus_REQ,
  output DMA_ACK,
  output [31:0] Addr_To_CPU,
  output [63:0] Data_To_CPU,
  output En_Write_Out,
  output [63:0] Data_To_Perif
);

  and and_1 (Bus_REQ, Comand[1], DMA_REQ);
  Multiplexer #(.width(32)) multiplexer_1 (.in0({32{1'b0}}), .in1(Addr_Perif), .out(Addr_To_CPU), .sel(DMA_ACK));
  Multiplexer #(.enable("true"), .width(64)) multiplexer_2 (
    .in0({64{1'b0}}), .in1(Data_From_Perif), .out(Data_To_CPU), .sel(DMA_ACK), .en(En_Write));
  Multiplexer #(.width(64)) multiplexer_3 (.in0({64{1'b0}}), .in1(Data_From_CPU), .out(Data_To_Perif), .sel(DMA_ACK));
  and and_2 (DMA_ACK, Bus_REQ, DMA_ACK_From_CPU);
  and and_3 (En_Write_Out, DMA_ACK, En_Write);
endmodule

module TLP (
  input  [31:0] Addr_To_Upstream,
  input  [63:0] Data_To_Upstream,
  input  [63:0] Data_From_CPU,
  input  [63:0] Data_From_DMA,
  input  [31:0] Addr_From_CPU,
  input  ECAM,
  input  MMIO,
  input  En_Write_CPU,
  input  En_Read_CPU,
  input  DMA_ACK,
  input  Clk,
  input  RST,
  input  [1:0] Ctrl_Upstream,
  output [31:0] Addr_To_Up,
  output [63:0] Data_To_Up,
  output [63:0] Data_To_Downstream,
  output [31:0] Addr_To_Downstream,
  output [6:0] Ctrl_Downstream,
  output Bus_REQ,
  output En_Write
);

  wire DMA_Read, DMA_Write, or_1_out, or_2_out, or_3_out;
  wire [1:0] pla_1_out;

  PLA #(.\table ("x1 10 # DMA_R\n10 01 # CPU_W")) pla_1 (.in({Ctrl_Downstream[2], DMA_Read}), .out(pla_1_out));
  Multiplexer #(.width(32)) multiplexer_1 (
    .in0({32{1'b0}}), .in1(Addr_To_Upstream), .out(Addr_To_Up), .sel(Ctrl_Downstream[4]));
  Multiplexer #(.width(64)) multiplexer_2 (.in0({64{1'b0}}), .in1(Data_To_Upstream), .out(Data_To_Up), .sel(or_1_out));
  or or_1 (or_1_out, En_Read_CPU, DMA_Write);
  or or_2 (or_2_out, ECAM, Ctrl_Downstream[1]);
  and and_1 (Ctrl_Downstream[1], ~ECAM, MMIO);  // AND_Gate
  and and_2 (Ctrl_Downstream[2], En_Write_CPU, ~En_Read_CPU);  // AND_Gate
  and and_3 (Ctrl_Downstream[4], DMA_ACK, Ctrl_Upstream[0]);
  Multiplexer #(.select(2), .width(64)) multiplexer_3 (
    .in0({64{1'b0}}), .in1(Data_From_CPU), .in2(Data_From_DMA), .out(Data_To_Downstream), .sel(pla_1_out));  // open: in3
  Multiplexer #(.enable("true"), .width(32)) multiplexer_4 (
    .in0({32{1'b0}}), .in1(Addr_From_CPU), .out(Addr_To_Downstream), .sel(or_2_out), .en(or_3_out));
  or or_3 (or_3_out, Ctrl_Downstream[2], En_Read_CPU);
  and and_4 (DMA_Write, Ctrl_Downstream[4], Ctrl_Upstream[1]);
  and and_5 (DMA_Read, Ctrl_Downstream[4], ~Ctrl_Upstream[1]);  // AND_Gate

  assign Bus_REQ = Ctrl_Upstream[0];
  assign {Ctrl_Downstream[6:5], Ctrl_Downstream[3], Ctrl_Downstream[0]} = {RST, Clk, En_Read_CPU, ECAM};
  assign En_Write = Ctrl_Upstream[1];

  // Other names for the same wires on the sheet: CPU_Write = Ctrl_Downstream[2]; CPU_Read = En_Read_CPU;
  //   DMA = Ctrl_Downstream[4]

  // Notes on the sheet:
  //   DMA
  //   Ctrl
endmodule
