// Logisim project mother.circ as structural Verilog: 2 circuits, main circuit main
module main (
);

  wire button_1_out, clock_1_out, die_1_clk_out, die_1_hlt, die_1_read_en, die_1_rst_out, die_1_write_en,
       keyboard_1_avail, keyboard_main_1_clk, keyboard_main_1_cls, keyboard_main_1_read, memory_1_ram_ready,
       on_off_sys_1_clk_out, on_off_sys_1_rst_out, tty_main_1_clear, tty_main_1_clk, tty_main_1_en_write;
  wire [1:0] keyboard_main_1_ctrl_up, tty_main_1_ctrl_up;
  wire [6:0] die_1_ctrl_down_1, die_1_ctrl_down_2, keyboard_1_data, tty_main_1_data;
  wire [7:0] die_1_write_flags;
  wire [19:0] die_1_rom_addr;
  wire [31:0] die_1_addr, die_1_addr_to_perif_1, die_1_addr_to_perif_2, die_1_data_out,
       keyboard_main_1_addr_to_ram, keyboard_main_1_data_out, tty_main_1_addr_to_ram, tty_main_1_data_out;
  wire [63:0] die_1_data_to_perif_1, die_1_data_to_perif_2, memory_1_out_9, rom_bios_1_data_out;

  LED led_1 (.in(die_1_hlt));
  Clock #(.highDuration(275), .lowDuration(275)) clock_1 (.out(clock_1_out));
  Button button_1 (.out(button_1_out));
  On_Off_Sys on_off_sys_1 (
    .RST(button_1_out), .Clk(clock_1_out), .RST_Out(on_off_sys_1_rst_out), .Clk_Out(on_off_sys_1_clk_out));
  ROM_BIOS rom_bios_1 (.Addr(die_1_rom_addr), .Data_Out(rom_bios_1_data_out));
  // Probe on die_1_data_out
  // Probe on memory_1_out_9
  // Probe on die_1_addr
  Die die_1 (
    .Addr_From_Perif_1(tty_main_1_addr_to_ram), .Data_From_Perif_1(tty_main_1_data_out),
    .Ctrl_Up_1(tty_main_1_ctrl_up), .Addr_From_Perif_2(keyboard_main_1_addr_to_ram),
    .Data_From_Perif_2(keyboard_main_1_data_out), .Ctrl_Up_2(keyboard_main_1_ctrl_up),
    .Data_From_Perif_3({32{1'b1}}), .ROM_Data_In(rom_bios_1_data_out), .RAM_Ready(memory_1_ram_ready),
    .Clk(on_off_sys_1_clk_out), .RST(on_off_sys_1_rst_out), .Data_In(memory_1_out_9),
    .RST_Out(die_1_rst_out), .Data_To_Perif_1(die_1_data_to_perif_1),
    .Addr_To_Perif_1(die_1_addr_to_perif_1), .Ctrl_Down_1(die_1_ctrl_down_1),
    .Data_To_Perif_2(die_1_data_to_perif_2), .Addr_To_Perif_2(die_1_addr_to_perif_2),
    .Ctrl_Down_2(die_1_ctrl_down_2), .ROM_Addr(die_1_rom_addr), .Clk_Out(die_1_clk_out),
    .Read_En(die_1_read_en), .Write_En(die_1_write_en), .HLT(die_1_hlt), .Write_Flags(die_1_write_flags),
    .Addr(die_1_addr), .Data_Out(die_1_data_out));  // open: Addr_From_Perif_3, Ctrl_Up_3, Data_To_Perif_3, Addr_To_Perif_3, Ctrl_Down_3
  // Probe on rom_bios_1_data_out
  // Probe on die_1_rom_addr
  Memory memory_1 (
    .Write_En(die_1_write_en), .RST(die_1_rst_out), .Read_En(die_1_read_en), .Write_Flags(die_1_write_flags),
    .Clk(die_1_clk_out), .Data_In(die_1_data_out), .Addr(die_1_addr), .RAM_Ready(memory_1_ram_ready),
    .out_9(memory_1_out_9));
  TTY #(.cols(40), .rows(10)) tty_1 (
    .data(tty_main_1_data), .clk(tty_main_1_clk), .we(tty_main_1_en_write), .clr(tty_main_1_clear));
  TTY_Main tty_main_1 (
    .Ctrl_Down(die_1_ctrl_down_1), .Data_In(die_1_data_to_perif_1), .Addr_In(die_1_addr_to_perif_1),
    .Clk(tty_main_1_clk), .En_Write(tty_main_1_en_write), .Clear(tty_main_1_clear), .Data(tty_main_1_data),
    .Data_Out(tty_main_1_data_out), .Ctrl_Up(tty_main_1_ctrl_up), .Addr_To_RAM(tty_main_1_addr_to_ram));
  Keyboard_Main keyboard_main_1 (
    .Data_Available(keyboard_1_avail), .Data_Keyboard(keyboard_1_data), .Ctrl_Down(die_1_ctrl_down_2),
    .Data_In(die_1_data_to_perif_2), .Addr_In(die_1_addr_to_perif_2), .Clk(keyboard_main_1_clk),
    .Cls(keyboard_main_1_cls), .Read(keyboard_main_1_read), .Data_Out(keyboard_main_1_data_out),
    .Ctrl_Up(keyboard_main_1_ctrl_up), .Addr_To_RAM(keyboard_main_1_addr_to_ram));
  Keyboard keyboard_1 (
    .clk(keyboard_main_1_clk), .re(keyboard_main_1_read), .clr(keyboard_main_1_cls),
    .avail(keyboard_1_avail), .data(keyboard_1_data));
endmodule

module On_Off_Sys (
  input  RST,
  input  Clk,
  output RST_Out,
  output Clk_Out
);

  wire and_1_out, and_2_out, and_3_out, and_4_out, and_5_out, and_6_out, and_7_out, and_8_out, and_9_out,
       and_10_out, and_11_out, and_12_out, and_13_out, or_1_out, or_2_out, or_3_out, or_4_out, Q0, Q1, Q2;

  and and_1 (and_1_out, ~Q1, RST);  // AND_Gate
  and and_2 (and_2_out, ~Q1, Q0);  // AND_Gate
  and and_3 (and_3_out, Q0, RST);
  and and_4 (and_4_out, ~Q0, Q2);  // AND_Gate
  and and_5 (and_5_out, ~Q2, Q0);  // AND_Gate
  and and_6 (and_6_out, Q1, ~Q0);  // AND_Gate
  and and_7 (and_7_out, Q1, RST);
  and and_8 (and_8_out, Q2, ~Q0);  // AND_Gate
  and and_9 (and_9_out, Q2, RST);
  and and_10 (and_10_out, Q1, ~Q0, RST);  // AND_Gate
  or or_1 (or_1_out, and_1_out, and_2_out, and_3_out, and_4_out);
  or or_2 (or_2_out, and_5_out, and_6_out, and_7_out);
  or or_3 (or_3_out, and_8_out, and_9_out, and_10_out);
  D_Flip_Flop d_ff_1 (.D(or_1_out), .clk(Clk), .Q(Q0));  // open: Qn, preset, reset
  D_Flip_Flop d_ff_2 (.D(or_2_out), .clk(Clk), .Q(Q1));  // open: Qn, preset, reset
  D_Flip_Flop d_ff_3 (.D(or_3_out), .clk(Clk), .Q(Q2));  // open: Qn, preset, reset
  and and_11 (and_11_out, Q2, Q1, ~Q0);  // AND_Gate
  and and_12 (and_12_out, ~Q2, ~Q1, Q0);  // AND_Gate
  or or_4 (or_4_out, Q0, Q1);
  or or_5 (RST_Out, and_11_out, and_12_out);
  and and_13 (and_13_out, ~Q2, or_4_out);  // AND_Gate
  and and_14 (Clk_Out, and_13_out, Clk);
endmodule
